// Logisim project nick.circ as structural Verilog: 2 circuits, main circuit nickname
module nickname (
  input  clear,
  input  [6:0] key,
  input  enter,
  input  not_empty,
  input  get_data,
  output clear_2,
  output [7:0] key_2,
  output ignore,
  output ready,
  output get_data_2
);

  D_Flip_Flop d_ff_1 (.Q(ignore), .preset(enter), .reset(clear));  // open: clk, D, Qn, en
  and and_1 (ready, ignore, not_empty, get_data);

  assign clear_2 = clear;
  assign get_data_2 = get_data;
  assign key_2 = {1'b0, key};
endmodule

module example (
  input  get,
  output [7:0] key,
  output ready
);

  wire clear_out, enter_out, keyboard_1_avail, nickname_1_clear_2, nickname_1_get_data_2, nickname_1_ignore;
  wire [6:0] keyboard_1_data;

  Button enter (.out(enter_out));
  Button clear (.out(clear_out));
  Keyboard #(.trigger("falling")) keyboard_1 (
    .clk(nickname_1_get_data_2), .re(nickname_1_ignore), .clr(nickname_1_clear_2), .avail(keyboard_1_avail),
    .data(keyboard_1_data));
  nickname nickname_1 (
    .clear(clear_out), .clear_2(nickname_1_clear_2), .key(keyboard_1_data), .key_2(key),
    .not_empty(keyboard_1_avail), .enter(enter_out), .get_data(get), .get_data_2(nickname_1_get_data_2),
    .ready(ready), .ignore(nickname_1_ignore));
endmodule
