// Logisim project proj.circ as structural Verilog: 21 circuits, main circuit interface
module \interface  (
);

  wire clr_out, ent_out, keyboard_2_avail, main_1_kboard_clk, main_1_out_229, main_1_out_230, main_1_out_262;
  wire [3:0] main_1_out_30, main_1_out_31, main_1_out_32, main_1_out_33, main_1_out_34, main_1_out_35,
       main_1_out_36, main_1_out_37;
  wire [4:0] main_1_out_167, main_1_out_168, main_1_out_169, main_1_out_170, main_1_out_171, main_1_out_172,
       main_1_out_173, main_1_out_174, main_1_out_175, main_1_out_176, main_1_out_177, main_1_out_178,
       main_1_out_179, main_1_out_180, main_1_out_181, main_1_out_182, main_1_out_183, main_1_out_184,
       main_1_out_185, main_1_out_186, main_1_out_187, main_1_out_188, main_1_out_189, main_1_out_190,
       main_1_out_191, main_1_out_192, main_1_out_193, main_1_out_194, main_1_out_195, main_1_out_196,
       main_1_out_197, main_1_out_198, main_1_out_199, main_1_out_200, main_1_out_201, main_1_out_202,
       main_1_out_203, main_1_out_204, main_1_out_205, main_1_out_206, main_1_out_207, main_1_out_208,
       main_1_out_209, main_1_out_210, main_1_out_211, main_1_out_212, main_1_out_213, main_1_out_214,
       main_1_out_215, main_1_out_216, main_1_out_217, main_1_out_218, main_1_out_219, main_1_out_220,
       main_1_out_221, main_1_out_222, main_1_out_223, main_1_out_224, main_1_out_225, main_1_out_226,
       main_1_out_227, main_1_out_228, main_1_out_231, main_1_out_232, main_1_out_233, main_1_out_234,
       main_1_out_235, main_1_out_236, main_1_out_237, main_1_out_238, main_1_out_239, main_1_out_240,
       main_1_out_241, main_1_out_242, main_1_out_243, main_1_out_244, main_1_out_245, main_1_out_246,
       main_1_out_247, main_1_out_248, main_1_out_249, main_1_out_250, main_1_out_251, main_1_out_252,
       main_1_out_253, main_1_out_254, main_1_out_255, main_1_out_256, main_1_out_257, main_1_out_258,
       main_1_out_259, main_1_out_260, main_1_out_261, main_1_out_263, main_1_out_264, main_1_out_265,
       main_1_out_266, main_1_out_267, main_1_out_268, main_1_out_269, main_1_out_270, main_1_out_271,
       main_1_out_272, main_1_out_273, main_1_out_274, main_1_out_275, main_1_out_276, main_1_out_277,
       main_1_out_278, main_1_out_279, main_1_out_280, main_1_out_281, main_1_out_282, main_1_out_283,
       main_1_out_284, main_1_out_285, main_1_out_286, main_1_out_287, main_1_out_288, main_1_out_289,
       main_1_out_290, main_1_out_291, main_1_out_292, main_1_out_293, main_1_out_294, main_1_out_295,
       main_1_out_296, main_1_out_297, main_1_out_298, main_1_out_299, main_1_out_300, main_1_out_301,
       main_1_out_302, main_1_out_303, main_1_out_304, main_1_out_305, main_1_out_306, main_1_out_307,
       main_1_out_308, main_1_out_309, main_1_out_310, main_1_out_311, main_1_out_312, main_1_out_313,
       main_1_out_314, main_1_out_315, main_1_out_316, main_1_out_317, main_1_out_318, main_1_out_319,
       main_1_out_320, main_1_out_321, main_1_out_322, main_1_out_323, main_1_out_324;
  wire [5:0] main_1_out_6, main_1_out_7, main_1_out_8, main_1_out_9, main_1_out_10, main_1_out_11,
       main_1_out_12, main_1_out_13, main_1_out_14, main_1_out_15, main_1_out_16, main_1_out_17,
       main_1_out_18, main_1_out_19, main_1_out_20, main_1_out_21, main_1_out_22, main_1_out_23,
       main_1_out_24, main_1_out_25, main_1_out_26, main_1_out_27, main_1_out_28, main_1_out_29;
  wire [6:0] keyboard_1_data, keyboard_2_data;
  wire [31:0] main_1_out_38, main_1_out_39, main_1_out_40, main_1_out_41, main_1_out_42, main_1_out_43,
       main_1_out_44, main_1_out_45, main_1_out_46, main_1_out_47, main_1_out_48, main_1_out_49,
       main_1_out_50, main_1_out_51, main_1_out_52, main_1_out_53, main_1_out_54, main_1_out_55,
       main_1_out_56, main_1_out_57, main_1_out_58, main_1_out_59, main_1_out_60, main_1_out_61,
       main_1_out_62, main_1_out_63, main_1_out_64, main_1_out_65, main_1_out_66, main_1_out_67,
       main_1_out_68, main_1_out_69, main_1_out_70, main_1_out_71, main_1_out_72, main_1_out_73,
       main_1_out_74, main_1_out_75, main_1_out_76, main_1_out_77, main_1_out_78, main_1_out_79,
       main_1_out_80, main_1_out_81, main_1_out_82, main_1_out_83, main_1_out_84, main_1_out_85,
       main_1_out_86, main_1_out_87, main_1_out_88, main_1_out_89, main_1_out_90, main_1_out_91,
       main_1_out_92, main_1_out_93, main_1_out_94, main_1_out_95, main_1_out_96, main_1_out_97,
       main_1_out_98, main_1_out_99, main_1_out_100, main_1_out_101, main_1_out_102, main_1_out_103,
       main_1_out_104, main_1_out_105, main_1_out_106, main_1_out_107, main_1_out_108, main_1_out_109,
       main_1_out_110, main_1_out_111, main_1_out_112, main_1_out_113, main_1_out_114, main_1_out_115,
       main_1_out_116, main_1_out_117, main_1_out_118, main_1_out_119, main_1_out_120, main_1_out_121,
       main_1_out_122, main_1_out_123, main_1_out_124, main_1_out_125, main_1_out_126, main_1_out_127,
       main_1_out_128, main_1_out_129, main_1_out_130, main_1_out_131, main_1_out_132, main_1_out_133,
       main_1_out_134, main_1_out_135, main_1_out_136, main_1_out_137, main_1_out_138, main_1_out_139,
       main_1_out_140, main_1_out_141, main_1_out_142, main_1_out_143, main_1_out_144, main_1_out_145,
       main_1_out_146, main_1_out_147, main_1_out_148, main_1_out_149, main_1_out_150, main_1_out_151,
       main_1_out_152, main_1_out_153, main_1_out_154, main_1_out_155, main_1_out_156, main_1_out_157,
       main_1_out_158, main_1_out_159, main_1_out_160, main_1_out_161, main_1_out_162, main_1_out_163,
       main_1_out_164, main_1_out_165;

  Keyboard #(.buflen(1)) keyboard_1 (.clk(main_1_kboard_clk), .data(keyboard_1_data));  // open: re, clr, avail
  Keyboard keyboard_2 (
    .clk(main_1_out_262), .re(main_1_out_229), .clr(main_1_out_230), .avail(keyboard_2_avail),
    .data(keyboard_2_data));
  DotMatrix #(.matrixcols(32), .matrixrows(32)) dotmatrix_1 (
    .col0(main_1_out_38), .col1(main_1_out_39), .col2(main_1_out_40), .col3(main_1_out_41),
    .col4(main_1_out_42), .col5(main_1_out_43), .col6(main_1_out_44), .col7(main_1_out_45),
    .col8(main_1_out_46), .col9(main_1_out_47), .col10(main_1_out_48), .col11(main_1_out_49),
    .col12(main_1_out_50), .col13(main_1_out_51), .col14(main_1_out_52), .col15(main_1_out_53),
    .col16(main_1_out_54), .col17(main_1_out_55), .col18(main_1_out_56), .col19(main_1_out_57),
    .col20(main_1_out_58), .col21(main_1_out_59), .col22(main_1_out_60), .col23(main_1_out_61),
    .col24(main_1_out_62), .col25(main_1_out_63), .col26(main_1_out_64), .col27(main_1_out_65),
    .col28(main_1_out_66), .col29(main_1_out_67), .col30(main_1_out_68), .col31(main_1_out_69));
  Button ent (.out(ent_out));
  Button clr (.out(clr_out));
  DotMatrix #(.matrixcols(16), .matrixrows(5)) dotmatrix_2 (
    .col0(main_1_out_167), .col1(main_1_out_168), .col2(main_1_out_169), .col3(main_1_out_170),
    .col4(main_1_out_171), .col5(main_1_out_172), .col6(main_1_out_173), .col7(main_1_out_174),
    .col8(main_1_out_175), .col9(main_1_out_176), .col10(main_1_out_177), .col11(main_1_out_178),
    .col12(main_1_out_179), .col13(main_1_out_180), .col14(main_1_out_181), .col15(main_1_out_182));
  DotMatrix #(.matrixcols(16), .matrixrows(5)) dotmatrix_3 (
    .col0(main_1_out_198), .col1(main_1_out_199), .col2(main_1_out_200), .col3(main_1_out_201),
    .col4(main_1_out_202), .col5(main_1_out_203), .col6(main_1_out_204), .col7(main_1_out_205),
    .col8(main_1_out_206), .col9(main_1_out_207), .col10(main_1_out_208), .col11(main_1_out_209),
    .col12(main_1_out_210), .col13(main_1_out_211), .col14(main_1_out_212), .col15(main_1_out_213));
  DotMatrix #(.matrixcols(16), .matrixrows(5)) dotmatrix_4 (
    .col0(main_1_out_231), .col1(main_1_out_232), .col2(main_1_out_233), .col3(main_1_out_234),
    .col4(main_1_out_235), .col5(main_1_out_236), .col6(main_1_out_237), .col7(main_1_out_238),
    .col8(main_1_out_239), .col9(main_1_out_240), .col10(main_1_out_241), .col11(main_1_out_242),
    .col12(main_1_out_243), .col13(main_1_out_244), .col14(main_1_out_245), .col15(main_1_out_246));
  DotMatrix #(.matrixcols(16), .matrixrows(5)) dotmatrix_5 (
    .col0(main_1_out_263), .col1(main_1_out_264), .col2(main_1_out_265), .col3(main_1_out_266),
    .col4(main_1_out_267), .col5(main_1_out_268), .col6(main_1_out_269), .col7(main_1_out_270),
    .col8(main_1_out_271), .col9(main_1_out_272), .col10(main_1_out_273), .col11(main_1_out_274),
    .col12(main_1_out_275), .col13(main_1_out_276), .col14(main_1_out_277), .col15(main_1_out_278));
  DotMatrix #(.matrixcols(16), .matrixrows(5)) dotmatrix_6 (
    .col0(main_1_out_294), .col1(main_1_out_295), .col2(main_1_out_296), .col3(main_1_out_297),
    .col4(main_1_out_298), .col5(main_1_out_299), .col6(main_1_out_300), .col7(main_1_out_301),
    .col8(main_1_out_302), .col9(main_1_out_303), .col10(main_1_out_304), .col11(main_1_out_305),
    .col12(main_1_out_306), .col13(main_1_out_307), .col14(main_1_out_308), .col15(main_1_out_309));
  main main_1 (
    .out_30(main_1_out_30), .out_34(main_1_out_34), .out_35(main_1_out_35), .out_36(main_1_out_36),
    .out_37(main_1_out_37), .key(keyboard_1_data), .kboard_clk(main_1_kboard_clk), .out_31(main_1_out_31),
    .out_32(main_1_out_32), .out_33(main_1_out_33), .out_38(main_1_out_38), .out_39(main_1_out_39),
    .out_40(main_1_out_40), .out_41(main_1_out_41), .out_42(main_1_out_42), .out_43(main_1_out_43),
    .out_44(main_1_out_44), .out_45(main_1_out_45), .out_46(main_1_out_46), .out_47(main_1_out_47),
    .out_48(main_1_out_48), .out_49(main_1_out_49), .out_50(main_1_out_50), .out_51(main_1_out_51),
    .out_52(main_1_out_52), .out_53(main_1_out_53), .out_54(main_1_out_54), .out_55(main_1_out_55),
    .out_56(main_1_out_56), .out_57(main_1_out_57), .out_58(main_1_out_58), .out_59(main_1_out_59),
    .out_60(main_1_out_60), .out_61(main_1_out_61), .out_62(main_1_out_62), .out_63(main_1_out_63),
    .out_64(main_1_out_64), .out_65(main_1_out_65), .out_66(main_1_out_66), .out_67(main_1_out_67),
    .out_68(main_1_out_68), .out_69(main_1_out_69), .out_70(main_1_out_70), .out_71(main_1_out_71),
    .out_72(main_1_out_72), .out_73(main_1_out_73), .out_74(main_1_out_74), .out_75(main_1_out_75),
    .out_76(main_1_out_76), .out_77(main_1_out_77), .out_78(main_1_out_78), .out_79(main_1_out_79),
    .out_80(main_1_out_80), .out_81(main_1_out_81), .out_82(main_1_out_82), .out_83(main_1_out_83),
    .out_84(main_1_out_84), .out_85(main_1_out_85), .out_86(main_1_out_86), .out_87(main_1_out_87),
    .out_88(main_1_out_88), .out_89(main_1_out_89), .out_90(main_1_out_90), .out_91(main_1_out_91),
    .out_98(main_1_out_98), .out_99(main_1_out_99), .out_100(main_1_out_100), .out_101(main_1_out_101),
    .out_102(main_1_out_102), .out_103(main_1_out_103), .out_104(main_1_out_104), .out_105(main_1_out_105),
    .out_106(main_1_out_106), .out_107(main_1_out_107), .out_108(main_1_out_108), .out_109(main_1_out_109),
    .out_110(main_1_out_110), .out_111(main_1_out_111), .out_112(main_1_out_112), .out_113(main_1_out_113),
    .out_114(main_1_out_114), .out_115(main_1_out_115), .out_116(main_1_out_116), .out_117(main_1_out_117),
    .out_118(main_1_out_118), .out_119(main_1_out_119), .out_120(main_1_out_120), .out_121(main_1_out_121),
    .out_122(main_1_out_122), .out_123(main_1_out_123), .out_124(main_1_out_124), .out_125(main_1_out_125),
    .out_126(main_1_out_126), .out_127(main_1_out_127), .out_128(main_1_out_128), .out_129(main_1_out_129),
    .out_130(main_1_out_130), .out_131(main_1_out_131), .out_132(main_1_out_132), .out_133(main_1_out_133),
    .out_134(main_1_out_134), .out_135(main_1_out_135), .out_136(main_1_out_136), .out_137(main_1_out_137),
    .out_138(main_1_out_138), .out_139(main_1_out_139), .out_140(main_1_out_140), .out_141(main_1_out_141),
    .out_142(main_1_out_142), .out_143(main_1_out_143), .out_144(main_1_out_144), .out_145(main_1_out_145),
    .out_146(main_1_out_146), .out_147(main_1_out_147), .out_148(main_1_out_148), .out_149(main_1_out_149),
    .out_150(main_1_out_150), .out_151(main_1_out_151), .out_152(main_1_out_152), .out_153(main_1_out_153),
    .out_154(main_1_out_154), .out_155(main_1_out_155), .out_156(main_1_out_156), .out_157(main_1_out_157),
    .out_158(main_1_out_158), .out_159(main_1_out_159), .out_160(main_1_out_160), .out_161(main_1_out_161),
    .out_162(main_1_out_162), .out_163(main_1_out_163), .out_164(main_1_out_164), .out_165(main_1_out_165),
    .out_6(main_1_out_6), .out_7(main_1_out_7), .out_8(main_1_out_8), .out_9(main_1_out_9),
    .out_10(main_1_out_10), .out_11(main_1_out_11), .out_12(main_1_out_12), .out_13(main_1_out_13),
    .out_14(main_1_out_14), .out_15(main_1_out_15), .out_16(main_1_out_16), .out_17(main_1_out_17),
    .out_18(main_1_out_18), .out_19(main_1_out_19), .out_20(main_1_out_20), .out_21(main_1_out_21),
    .out_22(main_1_out_22), .out_23(main_1_out_23), .out_24(main_1_out_24), .out_25(main_1_out_25),
    .out_26(main_1_out_26), .out_27(main_1_out_27), .out_28(main_1_out_28), .out_29(main_1_out_29),
    .out_92(main_1_out_92), .out_93(main_1_out_93), .out_94(main_1_out_94), .out_95(main_1_out_95),
    .out_96(main_1_out_96), .out_97(main_1_out_97), .enter(ent_out), .clear(clr_out),
    .out_262(main_1_out_262), .out_229(main_1_out_229), .out_230(main_1_out_230), .in_5(keyboard_2_avail),
    .in_4(keyboard_2_data), .out_167(main_1_out_167), .out_168(main_1_out_168), .out_169(main_1_out_169),
    .out_170(main_1_out_170), .out_171(main_1_out_171), .out_172(main_1_out_172), .out_173(main_1_out_173),
    .out_174(main_1_out_174), .out_175(main_1_out_175), .out_176(main_1_out_176), .out_177(main_1_out_177),
    .out_178(main_1_out_178), .out_179(main_1_out_179), .out_180(main_1_out_180), .out_181(main_1_out_181),
    .out_182(main_1_out_182), .out_183(main_1_out_183), .out_184(main_1_out_184), .out_185(main_1_out_185),
    .out_186(main_1_out_186), .out_187(main_1_out_187), .out_188(main_1_out_188), .out_189(main_1_out_189),
    .out_190(main_1_out_190), .out_191(main_1_out_191), .out_192(main_1_out_192), .out_193(main_1_out_193),
    .out_194(main_1_out_194), .out_195(main_1_out_195), .out_196(main_1_out_196), .out_197(main_1_out_197),
    .out_198(main_1_out_198), .out_199(main_1_out_199), .out_200(main_1_out_200), .out_201(main_1_out_201),
    .out_202(main_1_out_202), .out_203(main_1_out_203), .out_204(main_1_out_204), .out_205(main_1_out_205),
    .out_206(main_1_out_206), .out_207(main_1_out_207), .out_208(main_1_out_208), .out_209(main_1_out_209),
    .out_210(main_1_out_210), .out_211(main_1_out_211), .out_212(main_1_out_212), .out_213(main_1_out_213),
    .out_214(main_1_out_214), .out_215(main_1_out_215), .out_216(main_1_out_216), .out_217(main_1_out_217),
    .out_218(main_1_out_218), .out_219(main_1_out_219), .out_220(main_1_out_220), .out_221(main_1_out_221),
    .out_222(main_1_out_222), .out_223(main_1_out_223), .out_224(main_1_out_224), .out_225(main_1_out_225),
    .out_226(main_1_out_226), .out_227(main_1_out_227), .out_228(main_1_out_228), .out_231(main_1_out_231),
    .out_232(main_1_out_232), .out_233(main_1_out_233), .out_234(main_1_out_234), .out_235(main_1_out_235),
    .out_236(main_1_out_236), .out_237(main_1_out_237), .out_238(main_1_out_238), .out_239(main_1_out_239),
    .out_240(main_1_out_240), .out_241(main_1_out_241), .out_242(main_1_out_242), .out_243(main_1_out_243),
    .out_244(main_1_out_244), .out_245(main_1_out_245), .out_246(main_1_out_246), .out_247(main_1_out_247),
    .out_248(main_1_out_248), .out_249(main_1_out_249), .out_250(main_1_out_250), .out_251(main_1_out_251),
    .out_252(main_1_out_252), .out_253(main_1_out_253), .out_254(main_1_out_254), .out_255(main_1_out_255),
    .out_256(main_1_out_256), .out_257(main_1_out_257), .out_258(main_1_out_258), .out_259(main_1_out_259),
    .out_260(main_1_out_260), .out_261(main_1_out_261), .out_263(main_1_out_263), .out_264(main_1_out_264),
    .out_265(main_1_out_265), .out_266(main_1_out_266), .out_267(main_1_out_267), .out_268(main_1_out_268),
    .out_269(main_1_out_269), .out_270(main_1_out_270), .out_271(main_1_out_271), .out_272(main_1_out_272),
    .out_273(main_1_out_273), .out_274(main_1_out_274), .out_275(main_1_out_275), .out_276(main_1_out_276),
    .out_277(main_1_out_277), .out_278(main_1_out_278), .out_279(main_1_out_279), .out_280(main_1_out_280),
    .out_281(main_1_out_281), .out_282(main_1_out_282), .out_283(main_1_out_283), .out_284(main_1_out_284),
    .out_285(main_1_out_285), .out_286(main_1_out_286), .out_287(main_1_out_287), .out_288(main_1_out_288),
    .out_289(main_1_out_289), .out_290(main_1_out_290), .out_291(main_1_out_291), .out_292(main_1_out_292),
    .out_293(main_1_out_293), .out_294(main_1_out_294), .out_295(main_1_out_295), .out_296(main_1_out_296),
    .out_297(main_1_out_297), .out_298(main_1_out_298), .out_299(main_1_out_299), .out_300(main_1_out_300),
    .out_301(main_1_out_301), .out_302(main_1_out_302), .out_303(main_1_out_303), .out_304(main_1_out_304),
    .out_305(main_1_out_305), .out_306(main_1_out_306), .out_307(main_1_out_307), .out_308(main_1_out_308),
    .out_309(main_1_out_309), .out_310(main_1_out_310), .out_311(main_1_out_311), .out_312(main_1_out_312),
    .out_313(main_1_out_313), .out_314(main_1_out_314), .out_315(main_1_out_315), .out_316(main_1_out_316),
    .out_317(main_1_out_317), .out_318(main_1_out_318), .out_319(main_1_out_319), .out_320(main_1_out_320),
    .out_321(main_1_out_321), .out_322(main_1_out_322), .out_323(main_1_out_323), .out_324(main_1_out_324));
  DotMatrix #(.matrixcols(15), .matrixrows(5)) dotmatrix_7 (
    .col0(main_1_out_183), .col1(main_1_out_184), .col2(main_1_out_185), .col3(main_1_out_186),
    .col4(main_1_out_187), .col5(main_1_out_188), .col6(main_1_out_189), .col7(main_1_out_190),
    .col8(main_1_out_191), .col9(main_1_out_192), .col10(main_1_out_193), .col11(main_1_out_194),
    .col12(main_1_out_195), .col13(main_1_out_196), .col14(main_1_out_197));
  DotMatrix #(.matrixcols(15), .matrixrows(5)) dotmatrix_8 (
    .col0(main_1_out_214), .col1(main_1_out_215), .col2(main_1_out_216), .col3(main_1_out_217),
    .col4(main_1_out_218), .col5(main_1_out_219), .col6(main_1_out_220), .col7(main_1_out_221),
    .col8(main_1_out_222), .col9(main_1_out_223), .col10(main_1_out_224), .col11(main_1_out_225),
    .col12(main_1_out_226), .col13(main_1_out_227), .col14(main_1_out_228));
  DotMatrix #(.matrixcols(15), .matrixrows(5)) dotmatrix_9 (
    .col0(main_1_out_247), .col1(main_1_out_248), .col2(main_1_out_249), .col3(main_1_out_250),
    .col4(main_1_out_251), .col5(main_1_out_252), .col6(main_1_out_253), .col7(main_1_out_254),
    .col8(main_1_out_255), .col9(main_1_out_256), .col10(main_1_out_257), .col11(main_1_out_258),
    .col12(main_1_out_259), .col13(main_1_out_260), .col14(main_1_out_261));
  DotMatrix #(.matrixcols(15), .matrixrows(5)) dotmatrix_10 (
    .col0(main_1_out_279), .col1(main_1_out_280), .col2(main_1_out_281), .col3(main_1_out_282),
    .col4(main_1_out_283), .col5(main_1_out_284), .col6(main_1_out_285), .col7(main_1_out_286),
    .col8(main_1_out_287), .col9(main_1_out_288), .col10(main_1_out_289), .col11(main_1_out_290),
    .col12(main_1_out_291), .col13(main_1_out_292), .col14(main_1_out_293));
  DotMatrix #(.matrixcols(15), .matrixrows(5)) dotmatrix_11 (
    .col0(main_1_out_310), .col1(main_1_out_311), .col2(main_1_out_312), .col3(main_1_out_313),
    .col4(main_1_out_314), .col5(main_1_out_315), .col6(main_1_out_316), .col7(main_1_out_317),
    .col8(main_1_out_318), .col9(main_1_out_319), .col10(main_1_out_320), .col11(main_1_out_321),
    .col12(main_1_out_322), .col13(main_1_out_323), .col14(main_1_out_324));
  Hex_Digit_Display hex_digit_display_1 (.value(main_1_out_31));  // open: dp
  Hex_Digit_Display hex_digit_display_2 (.value(main_1_out_30));  // open: dp
  Hex_Digit_Display hex_digit_display_3 (.value(main_1_out_32));  // open: dp
  Hex_Digit_Display hex_digit_display_4 (.value(main_1_out_33));  // open: dp
  DotMatrix #(.matrixcols(32), .matrixrows(32)) dotmatrix_12 (
    .col0(main_1_out_70), .col1(main_1_out_71), .col2(main_1_out_72), .col3(main_1_out_73),
    .col4(main_1_out_74), .col5(main_1_out_75), .col6(main_1_out_76), .col7(main_1_out_77),
    .col8(main_1_out_78), .col9(main_1_out_79), .col10(main_1_out_80), .col11(main_1_out_81),
    .col12(main_1_out_82), .col13(main_1_out_83), .col14(main_1_out_84), .col15(main_1_out_85),
    .col16(main_1_out_86), .col17(main_1_out_87), .col18(main_1_out_88), .col19(main_1_out_89),
    .col20(main_1_out_90), .col21(main_1_out_91), .col22(main_1_out_92), .col23(main_1_out_93),
    .col24(main_1_out_94), .col25(main_1_out_95), .col26(main_1_out_96), .col27(main_1_out_97),
    .col28(main_1_out_98), .col29(main_1_out_99), .col30(main_1_out_100), .col31(main_1_out_101));
  DotMatrix #(.matrixcols(24), .matrixrows(6)) dotmatrix_13 (
    .col0(main_1_out_6), .col1(main_1_out_7), .col2(main_1_out_8), .col3(main_1_out_9), .col4(main_1_out_10),
    .col5(main_1_out_11), .col6(main_1_out_12), .col7(main_1_out_13), .col8(main_1_out_14),
    .col9(main_1_out_15), .col10(main_1_out_16), .col11(main_1_out_17), .col12(main_1_out_18),
    .col13(main_1_out_19), .col14(main_1_out_20), .col15(main_1_out_21), .col16(main_1_out_22),
    .col17(main_1_out_23), .col18(main_1_out_24), .col19(main_1_out_25), .col20(main_1_out_26),
    .col21(main_1_out_27), .col22(main_1_out_28), .col23(main_1_out_29));
  DotMatrix #(.matrixcols(32), .matrixrows(32)) dotmatrix_14 (
    .col0(main_1_out_102), .col1(main_1_out_103), .col2(main_1_out_104), .col3(main_1_out_105),
    .col4(main_1_out_106), .col5(main_1_out_107), .col6(main_1_out_108), .col7(main_1_out_109),
    .col8(main_1_out_110), .col9(main_1_out_111), .col10(main_1_out_112), .col11(main_1_out_113),
    .col12(main_1_out_114), .col13(main_1_out_115), .col14(main_1_out_116), .col15(main_1_out_117),
    .col16(main_1_out_118), .col17(main_1_out_119), .col18(main_1_out_120), .col19(main_1_out_121),
    .col20(main_1_out_122), .col21(main_1_out_123), .col22(main_1_out_124), .col23(main_1_out_125),
    .col24(main_1_out_126), .col25(main_1_out_127), .col26(main_1_out_128), .col27(main_1_out_129),
    .col28(main_1_out_130), .col29(main_1_out_131), .col30(main_1_out_132), .col31(main_1_out_133));
  DotMatrix #(.matrixcols(32), .matrixrows(32)) dotmatrix_15 (
    .col0(main_1_out_134), .col1(main_1_out_135), .col2(main_1_out_136), .col3(main_1_out_137),
    .col4(main_1_out_138), .col5(main_1_out_139), .col6(main_1_out_140), .col7(main_1_out_141),
    .col8(main_1_out_142), .col9(main_1_out_143), .col10(main_1_out_144), .col11(main_1_out_145),
    .col12(main_1_out_146), .col13(main_1_out_147), .col14(main_1_out_148), .col15(main_1_out_149),
    .col16(main_1_out_150), .col17(main_1_out_151), .col18(main_1_out_152), .col19(main_1_out_153),
    .col20(main_1_out_154), .col21(main_1_out_155), .col22(main_1_out_156), .col23(main_1_out_157),
    .col24(main_1_out_158), .col25(main_1_out_159), .col26(main_1_out_160), .col27(main_1_out_161),
    .col28(main_1_out_162), .col29(main_1_out_163), .col30(main_1_out_164), .col31(main_1_out_165));
  Hex_Digit_Display hex_digit_display_5 (.value(main_1_out_34));  // open: dp
  Hex_Digit_Display hex_digit_display_6 (.value(main_1_out_35));  // open: dp
  Hex_Digit_Display hex_digit_display_7 (.value(main_1_out_36));  // open: dp
  Hex_Digit_Display hex_digit_display_8 (.value(main_1_out_37));  // open: dp

  // Notes on the sheet:
  //   R - restart
  //   P - pause
  //   W / Space - jump
  //   S - crouch
  //   KEYBOARD
endmodule

module main (
  input  [6:0] key,
  input  enter,
  input  clear,
  input  [6:0] in_4,
  input  in_5,
  output [5:0] out_6,
  output [5:0] out_7,
  output [5:0] out_8,
  output [5:0] out_9,
  output [5:0] out_10,
  output [5:0] out_11,
  output [5:0] out_12,
  output [5:0] out_13,
  output [5:0] out_14,
  output [5:0] out_15,
  output [5:0] out_16,
  output [5:0] out_17,
  output [5:0] out_18,
  output [5:0] out_19,
  output [5:0] out_20,
  output [5:0] out_21,
  output [5:0] out_22,
  output [5:0] out_23,
  output [5:0] out_24,
  output [5:0] out_25,
  output [5:0] out_26,
  output [5:0] out_27,
  output [5:0] out_28,
  output [5:0] out_29,
  output [3:0] out_30,
  output [3:0] out_31,
  output [3:0] out_32,
  output [3:0] out_33,
  output [3:0] out_34,
  output [3:0] out_35,
  output [3:0] out_36,
  output [3:0] out_37,
  output [31:0] out_38,
  output [31:0] out_39,
  output [31:0] out_40,
  output [31:0] out_41,
  output [31:0] out_42,
  output [31:0] out_43,
  output [31:0] out_44,
  output [31:0] out_45,
  output [31:0] out_46,
  output [31:0] out_47,
  output [31:0] out_48,
  output [31:0] out_49,
  output [31:0] out_50,
  output [31:0] out_51,
  output [31:0] out_52,
  output [31:0] out_53,
  output [31:0] out_54,
  output [31:0] out_55,
  output [31:0] out_56,
  output [31:0] out_57,
  output [31:0] out_58,
  output [31:0] out_59,
  output [31:0] out_60,
  output [31:0] out_61,
  output [31:0] out_62,
  output [31:0] out_63,
  output [31:0] out_64,
  output [31:0] out_65,
  output [31:0] out_66,
  output [31:0] out_67,
  output [31:0] out_68,
  output [31:0] out_69,
  output [31:0] out_70,
  output [31:0] out_71,
  output [31:0] out_72,
  output [31:0] out_73,
  output [31:0] out_74,
  output [31:0] out_75,
  output [31:0] out_76,
  output [31:0] out_77,
  output [31:0] out_78,
  output [31:0] out_79,
  output [31:0] out_80,
  output [31:0] out_81,
  output [31:0] out_82,
  output [31:0] out_83,
  output [31:0] out_84,
  output [31:0] out_85,
  output [31:0] out_86,
  output [31:0] out_87,
  output [31:0] out_88,
  output [31:0] out_89,
  output [31:0] out_90,
  output [31:0] out_91,
  output [31:0] out_92,
  output [31:0] out_93,
  output [31:0] out_94,
  output [31:0] out_95,
  output [31:0] out_96,
  output [31:0] out_97,
  output [31:0] out_98,
  output [31:0] out_99,
  output [31:0] out_100,
  output [31:0] out_101,
  output [31:0] out_102,
  output [31:0] out_103,
  output [31:0] out_104,
  output [31:0] out_105,
  output [31:0] out_106,
  output [31:0] out_107,
  output [31:0] out_108,
  output [31:0] out_109,
  output [31:0] out_110,
  output [31:0] out_111,
  output [31:0] out_112,
  output [31:0] out_113,
  output [31:0] out_114,
  output [31:0] out_115,
  output [31:0] out_116,
  output [31:0] out_117,
  output [31:0] out_118,
  output [31:0] out_119,
  output [31:0] out_120,
  output [31:0] out_121,
  output [31:0] out_122,
  output [31:0] out_123,
  output [31:0] out_124,
  output [31:0] out_125,
  output [31:0] out_126,
  output [31:0] out_127,
  output [31:0] out_128,
  output [31:0] out_129,
  output [31:0] out_130,
  output [31:0] out_131,
  output [31:0] out_132,
  output [31:0] out_133,
  output [31:0] out_134,
  output [31:0] out_135,
  output [31:0] out_136,
  output [31:0] out_137,
  output [31:0] out_138,
  output [31:0] out_139,
  output [31:0] out_140,
  output [31:0] out_141,
  output [31:0] out_142,
  output [31:0] out_143,
  output [31:0] out_144,
  output [31:0] out_145,
  output [31:0] out_146,
  output [31:0] out_147,
  output [31:0] out_148,
  output [31:0] out_149,
  output [31:0] out_150,
  output [31:0] out_151,
  output [31:0] out_152,
  output [31:0] out_153,
  output [31:0] out_154,
  output [31:0] out_155,
  output [31:0] out_156,
  output [31:0] out_157,
  output [31:0] out_158,
  output [31:0] out_159,
  output [31:0] out_160,
  output [31:0] out_161,
  output [31:0] out_162,
  output [31:0] out_163,
  output [31:0] out_164,
  output [31:0] out_165,
  output kboard_clk,
  output [4:0] out_167,
  output [4:0] out_168,
  output [4:0] out_169,
  output [4:0] out_170,
  output [4:0] out_171,
  output [4:0] out_172,
  output [4:0] out_173,
  output [4:0] out_174,
  output [4:0] out_175,
  output [4:0] out_176,
  output [4:0] out_177,
  output [4:0] out_178,
  output [4:0] out_179,
  output [4:0] out_180,
  output [4:0] out_181,
  output [4:0] out_182,
  output [4:0] out_183,
  output [4:0] out_184,
  output [4:0] out_185,
  output [4:0] out_186,
  output [4:0] out_187,
  output [4:0] out_188,
  output [4:0] out_189,
  output [4:0] out_190,
  output [4:0] out_191,
  output [4:0] out_192,
  output [4:0] out_193,
  output [4:0] out_194,
  output [4:0] out_195,
  output [4:0] out_196,
  output [4:0] out_197,
  output [4:0] out_198,
  output [4:0] out_199,
  output [4:0] out_200,
  output [4:0] out_201,
  output [4:0] out_202,
  output [4:0] out_203,
  output [4:0] out_204,
  output [4:0] out_205,
  output [4:0] out_206,
  output [4:0] out_207,
  output [4:0] out_208,
  output [4:0] out_209,
  output [4:0] out_210,
  output [4:0] out_211,
  output [4:0] out_212,
  output [4:0] out_213,
  output [4:0] out_214,
  output [4:0] out_215,
  output [4:0] out_216,
  output [4:0] out_217,
  output [4:0] out_218,
  output [4:0] out_219,
  output [4:0] out_220,
  output [4:0] out_221,
  output [4:0] out_222,
  output [4:0] out_223,
  output [4:0] out_224,
  output [4:0] out_225,
  output [4:0] out_226,
  output [4:0] out_227,
  output [4:0] out_228,
  output out_229,
  output out_230,
  output [4:0] out_231,
  output [4:0] out_232,
  output [4:0] out_233,
  output [4:0] out_234,
  output [4:0] out_235,
  output [4:0] out_236,
  output [4:0] out_237,
  output [4:0] out_238,
  output [4:0] out_239,
  output [4:0] out_240,
  output [4:0] out_241,
  output [4:0] out_242,
  output [4:0] out_243,
  output [4:0] out_244,
  output [4:0] out_245,
  output [4:0] out_246,
  output [4:0] out_247,
  output [4:0] out_248,
  output [4:0] out_249,
  output [4:0] out_250,
  output [4:0] out_251,
  output [4:0] out_252,
  output [4:0] out_253,
  output [4:0] out_254,
  output [4:0] out_255,
  output [4:0] out_256,
  output [4:0] out_257,
  output [4:0] out_258,
  output [4:0] out_259,
  output [4:0] out_260,
  output [4:0] out_261,
  output out_262,
  output [4:0] out_263,
  output [4:0] out_264,
  output [4:0] out_265,
  output [4:0] out_266,
  output [4:0] out_267,
  output [4:0] out_268,
  output [4:0] out_269,
  output [4:0] out_270,
  output [4:0] out_271,
  output [4:0] out_272,
  output [4:0] out_273,
  output [4:0] out_274,
  output [4:0] out_275,
  output [4:0] out_276,
  output [4:0] out_277,
  output [4:0] out_278,
  output [4:0] out_279,
  output [4:0] out_280,
  output [4:0] out_281,
  output [4:0] out_282,
  output [4:0] out_283,
  output [4:0] out_284,
  output [4:0] out_285,
  output [4:0] out_286,
  output [4:0] out_287,
  output [4:0] out_288,
  output [4:0] out_289,
  output [4:0] out_290,
  output [4:0] out_291,
  output [4:0] out_292,
  output [4:0] out_293,
  output [4:0] out_294,
  output [4:0] out_295,
  output [4:0] out_296,
  output [4:0] out_297,
  output [4:0] out_298,
  output [4:0] out_299,
  output [4:0] out_300,
  output [4:0] out_301,
  output [4:0] out_302,
  output [4:0] out_303,
  output [4:0] out_304,
  output [4:0] out_305,
  output [4:0] out_306,
  output [4:0] out_307,
  output [4:0] out_308,
  output [4:0] out_309,
  output [4:0] out_310,
  output [4:0] out_311,
  output [4:0] out_312,
  output [4:0] out_313,
  output [4:0] out_314,
  output [4:0] out_315,
  output [4:0] out_316,
  output [4:0] out_317,
  output [4:0] out_318,
  output [4:0] out_319,
  output [4:0] out_320,
  output [4:0] out_321,
  output [4:0] out_322,
  output [4:0] out_323,
  output [4:0] out_324
);

  wire and_3_out, and_4_out, and_5_out, and_6_out, birds_1_birds_clk, clk, clk_cdm, clkp, clock_1_out,
       clock_2_out, clock_3_out, clr, clrp, col, counter_1_carry, day_sw, dino_jump_1_is_crouch,
       dino_jump_1_is_jump, jump_clk, keyboard_handler_1_crouch, keyboard_handler_1_jump,
       keyboard_handler_1_pause, keyboard_handler_1_reset, not_1_out, not_2_out, not_3_out, not_4_out,
       not_5_out, or_1_out, or_4_out, random_spawn_1_spawn_bird, random_spawn_1_spawn_cactus, ready,
       sen_kboard, sen_num, shiftreg_3_clear, shiftreg_4_clear, shiftreg_5_clear, shiftreg_6_clear,
       shiftreg_7_clear, shiftreg_8_clear, shiftreg_9_clear, shiftreg_10_clear, shiftreg_11_clear,
       shiftreg_12_clear, speeddino_1_clk, stop, t_ff_1_q, t_ff_1_qn;
  wire [3:0] hund, speed, thous;
  wire [4:0] dino_jump_1_y;
  wire [7:0] char, number_sen_1_num_out, sym;
  wire [15:0] num_out;
  wire [31:0] birds_1_down, birds_1_up, dino_1_out_18, dino_1_out_19, dino_1_out_20, dino_1_out_21,
       dino_1_out_22, dino_1_out_23, dino_1_out_24, dino_1_out_25, dino_1_out_26, dino_1_out_27,
       dino_1_out_28, gameover_1_out_66, gameover_1_out_67, gameover_1_out_68, gameover_1_out_69,
       gameover_1_out_70, gameover_1_out_71, gameover_1_out_72, gameover_1_out_73, gameover_1_out_74,
       gameover_1_out_75, gameover_1_out_76, gameover_1_out_77, gameover_1_out_78, gameover_1_out_79,
       gameover_1_out_80, gameover_1_out_81, gameover_1_out_82, gameover_1_out_83, gameover_1_out_84,
       gameover_1_out_85, gameover_1_out_86, gameover_1_out_87, gameover_1_out_88, gameover_1_out_89,
       gameover_1_out_90, gameover_1_out_91, gameover_1_out_92, gameover_1_out_93, gameover_1_out_94,
       gameover_1_out_95, gameover_1_out_96, gameover_1_out_97, gameover_1_out_98, gameover_1_out_99,
       gameover_1_out_100, gameover_1_out_101, gameover_1_out_102, gameover_1_out_103, gameover_1_out_104,
       gameover_1_out_105, gameover_1_out_106, gameover_1_out_107, gameover_1_out_108, gameover_1_out_109,
       gameover_1_out_110, gameover_1_out_111, gameover_1_out_112, gameover_1_out_113, gameover_1_out_114,
       gameover_1_out_115, gameover_1_out_116, gameover_1_out_117, gameover_1_out_118, gameover_1_out_119,
       gameover_1_out_120, gameover_1_out_121, gameover_1_out_122, gameover_1_out_123, gameover_1_out_124,
       gameover_1_out_125, gameover_1_out_126, gameover_1_out_127, gameover_1_out_128, gameover_1_out_129,
       obstacles_1_out, pause_1_out_66, pause_1_out_67, pause_1_out_68, pause_1_out_69, pause_1_out_70,
       pause_1_out_71, pause_1_out_72, pause_1_out_73, pause_1_out_74, pause_1_out_75, pause_1_out_76,
       pause_1_out_77, pause_1_out_78, pause_1_out_79, pause_1_out_80, pause_1_out_81, pause_1_out_82,
       pause_1_out_83, pause_1_out_84, pause_1_out_85, pause_1_out_86, pause_1_out_87, pause_1_out_88,
       pause_1_out_89, pause_1_out_90, pause_1_out_91, pause_1_out_92, pause_1_out_93, pause_1_out_94,
       pause_1_out_95, pause_1_out_96, pause_1_out_97, pause_1_out_98, pause_1_out_99, pause_1_out_100,
       pause_1_out_101, pause_1_out_102, pause_1_out_103, pause_1_out_104, pause_1_out_105, pause_1_out_106,
       pause_1_out_107, pause_1_out_108, pause_1_out_109, pause_1_out_110, pause_1_out_111, pause_1_out_112,
       pause_1_out_113, pause_1_out_114, pause_1_out_115, pause_1_out_116, pause_1_out_117, pause_1_out_118,
       pause_1_out_119, pause_1_out_120, pause_1_out_121, pause_1_out_122, pause_1_out_123, pause_1_out_124,
       pause_1_out_125, pause_1_out_126, pause_1_out_127, pause_1_out_128, pause_1_out_129,
       shiftreg_1_out_38, shiftreg_1_out_39, shiftreg_1_out_40, shiftreg_1_out_41, shiftreg_1_out_42,
       shiftreg_1_out_43, shiftreg_1_out_44, shiftreg_1_out_45, shiftreg_1_out_46, shiftreg_1_out_47,
       shiftreg_1_out_48, shiftreg_1_out_49, shiftreg_1_out_50, shiftreg_1_out_51, shiftreg_1_out_52,
       shiftreg_1_out_53, shiftreg_1_out_54, shiftreg_1_out_55, shiftreg_1_out_56, shiftreg_1_out_57,
       shiftreg_1_out_58, shiftreg_1_out_59, shiftreg_1_out_60, shiftreg_1_out_61, shiftreg_1_out_62,
       shiftreg_1_out_63, shiftreg_1_out_64, shiftreg_1_out_65, shiftreg_1_out_66, shiftreg_1_out_67,
       shiftreg_1_out_68, shiftreg_1_out_69, shiftreg_2_out_38, shiftreg_2_out_39, shiftreg_2_out_40,
       shiftreg_2_out_41, shiftreg_2_out_42, shiftreg_2_out_43, shiftreg_2_out_44, shiftreg_2_out_45,
       shiftreg_2_out_46, shiftreg_2_out_47, shiftreg_2_out_48, shiftreg_2_out_49, shiftreg_2_out_50,
       shiftreg_2_out_51, shiftreg_2_out_52, shiftreg_2_out_53, shiftreg_2_out_54, shiftreg_2_out_55,
       shiftreg_2_out_56, shiftreg_2_out_57, shiftreg_2_out_58, shiftreg_2_out_59, shiftreg_2_out_60,
       shiftreg_2_out_61, shiftreg_2_out_62, shiftreg_2_out_63, shiftreg_2_out_64, shiftreg_2_out_65,
       shiftreg_2_out_66, shiftreg_2_out_67, shiftreg_2_out_68, shiftreg_2_out_69, shiftreg_3_out_38,
       shiftreg_3_out_39, shiftreg_3_out_40, shiftreg_3_out_41, shiftreg_3_out_42, shiftreg_3_out_43,
       shiftreg_3_out_44, shiftreg_3_out_45, shiftreg_3_out_46, shiftreg_3_out_47, shiftreg_3_out_48,
       shiftreg_3_out_49, shiftreg_3_out_50, shiftreg_3_out_51, shiftreg_3_out_52, shiftreg_3_out_53,
       shiftreg_3_out_54, shiftreg_3_out_55, shiftreg_3_out_56, shiftreg_3_out_57, shiftreg_3_out_58,
       shiftreg_3_out_59, shiftreg_3_out_60, shiftreg_3_out_61, shiftreg_3_out_62, shiftreg_3_out_63,
       shiftreg_3_out_64, shiftreg_3_out_65, shiftreg_3_out_66, shiftreg_3_out_67, shiftreg_3_out_68,
       shiftreg_3_out_69, shiftreg_4_out_38, shiftreg_4_out_39, shiftreg_4_out_40, shiftreg_4_out_41,
       shiftreg_4_out_42, shiftreg_4_out_43, shiftreg_4_out_44, shiftreg_4_out_45, shiftreg_4_out_46,
       shiftreg_4_out_47, shiftreg_4_out_48, shiftreg_4_out_49, shiftreg_4_out_50, shiftreg_4_out_51,
       shiftreg_4_out_52, shiftreg_4_out_53, shiftreg_4_out_54, shiftreg_4_out_55, shiftreg_4_out_56,
       shiftreg_4_out_57, shiftreg_4_out_58, shiftreg_4_out_59, shiftreg_4_out_60, shiftreg_4_out_61,
       shiftreg_4_out_62, shiftreg_4_out_63, shiftreg_4_out_64, shiftreg_4_out_65, shiftreg_4_out_66,
       shiftreg_4_out_67, shiftreg_4_out_68, shiftreg_4_out_69, shiftreg_4_shift_out, shiftreg_5_out_38,
       shiftreg_5_out_39, shiftreg_5_out_40, shiftreg_5_out_41, shiftreg_5_out_42, shiftreg_5_out_43,
       shiftreg_5_out_44, shiftreg_5_out_45, shiftreg_5_out_46, shiftreg_5_out_47, shiftreg_5_out_48,
       shiftreg_5_out_49, shiftreg_5_out_50, shiftreg_5_out_51, shiftreg_5_out_52, shiftreg_5_out_53,
       shiftreg_5_out_54, shiftreg_5_out_55, shiftreg_5_out_56, shiftreg_5_out_57, shiftreg_5_out_58,
       shiftreg_5_out_59, shiftreg_5_out_60, shiftreg_5_out_61, shiftreg_5_out_62, shiftreg_5_out_63,
       shiftreg_5_out_64, shiftreg_5_out_65, shiftreg_5_out_66, shiftreg_5_out_67, shiftreg_5_out_68,
       shiftreg_5_out_69, shiftreg_5_shift_out, shiftreg_6_out_38, shiftreg_6_out_39, shiftreg_6_out_40,
       shiftreg_6_out_41, shiftreg_6_out_42, shiftreg_6_out_43, shiftreg_6_out_44, shiftreg_6_out_45,
       shiftreg_6_out_46, shiftreg_6_out_47, shiftreg_6_out_48, shiftreg_6_out_49, shiftreg_6_out_50,
       shiftreg_6_out_51, shiftreg_6_out_52, shiftreg_6_out_53, shiftreg_6_out_54, shiftreg_6_out_55,
       shiftreg_6_out_56, shiftreg_6_out_57, shiftreg_6_out_58, shiftreg_6_out_59, shiftreg_6_out_60,
       shiftreg_6_out_61, shiftreg_6_out_62, shiftreg_6_out_63, shiftreg_6_out_64, shiftreg_6_out_65,
       shiftreg_6_out_66, shiftreg_6_out_67, shiftreg_6_out_68, shiftreg_6_out_69, shiftreg_6_shift_out,
       shiftreg_7_out_38, shiftreg_7_out_39, shiftreg_7_out_40, shiftreg_7_out_41, shiftreg_7_out_42,
       shiftreg_7_out_43, shiftreg_7_out_44, shiftreg_7_out_45, shiftreg_7_out_46, shiftreg_7_out_47,
       shiftreg_7_out_48, shiftreg_7_out_49, shiftreg_7_out_50, shiftreg_7_out_51, shiftreg_7_out_52,
       shiftreg_7_out_53, shiftreg_7_out_54, shiftreg_7_out_55, shiftreg_7_out_56, shiftreg_7_out_57,
       shiftreg_7_out_58, shiftreg_7_out_59, shiftreg_7_out_60, shiftreg_7_out_61, shiftreg_7_out_62,
       shiftreg_7_out_63, shiftreg_7_out_64, shiftreg_7_out_65, shiftreg_7_out_66, shiftreg_7_out_67,
       shiftreg_7_out_68, shiftreg_7_out_69, shiftreg_7_shift_out, shiftreg_8_out_38, shiftreg_8_out_39,
       shiftreg_8_out_40, shiftreg_8_out_41, shiftreg_8_out_42, shiftreg_8_out_43, shiftreg_8_out_44,
       shiftreg_8_out_45, shiftreg_8_out_46, shiftreg_8_out_47, shiftreg_8_out_48, shiftreg_8_out_49,
       shiftreg_8_out_50, shiftreg_8_out_51, shiftreg_8_out_52, shiftreg_8_out_53, shiftreg_8_out_54,
       shiftreg_8_out_55, shiftreg_8_out_56, shiftreg_8_out_57, shiftreg_8_out_58, shiftreg_8_out_59,
       shiftreg_8_out_60, shiftreg_8_out_61, shiftreg_8_out_62, shiftreg_8_out_63, shiftreg_8_out_64,
       shiftreg_8_out_65, shiftreg_8_out_66, shiftreg_8_out_67, shiftreg_8_out_68, shiftreg_8_out_69,
       shiftreg_8_shift_out, shiftreg_9_out_38, shiftreg_9_out_39, shiftreg_9_out_40, shiftreg_9_out_41,
       shiftreg_9_out_42, shiftreg_9_out_43, shiftreg_9_out_44, shiftreg_9_out_45, shiftreg_9_out_46,
       shiftreg_9_out_47, shiftreg_9_out_48, shiftreg_9_out_49, shiftreg_9_out_50, shiftreg_9_out_51,
       shiftreg_9_out_52, shiftreg_9_out_53, shiftreg_9_out_54, shiftreg_9_out_55, shiftreg_9_out_56,
       shiftreg_9_out_57, shiftreg_9_out_58, shiftreg_9_out_59, shiftreg_9_out_60, shiftreg_9_out_61,
       shiftreg_9_out_62, shiftreg_9_out_63, shiftreg_9_out_64, shiftreg_9_out_65, shiftreg_9_out_66,
       shiftreg_9_out_67, shiftreg_9_out_68, shiftreg_9_out_69, shiftreg_9_shift_out, shiftreg_10_out_38,
       shiftreg_10_out_39, shiftreg_10_out_40, shiftreg_10_out_41, shiftreg_10_out_42, shiftreg_10_out_43,
       shiftreg_10_out_44, shiftreg_10_out_45, shiftreg_10_out_46, shiftreg_10_out_47, shiftreg_10_out_48,
       shiftreg_10_out_49, shiftreg_10_out_50, shiftreg_10_out_51, shiftreg_10_out_52, shiftreg_10_out_53,
       shiftreg_10_out_54, shiftreg_10_out_55, shiftreg_10_out_56, shiftreg_10_out_57, shiftreg_10_out_58,
       shiftreg_10_out_59, shiftreg_10_out_60, shiftreg_10_out_61, shiftreg_10_out_62, shiftreg_10_out_63,
       shiftreg_10_out_64, shiftreg_10_out_65, shiftreg_10_out_66, shiftreg_10_out_67, shiftreg_10_out_68,
       shiftreg_10_out_69, shiftreg_10_shift_out, shiftreg_11_out_38, shiftreg_11_out_39, shiftreg_11_out_40,
       shiftreg_11_out_41, shiftreg_11_out_42, shiftreg_11_out_43, shiftreg_11_out_44, shiftreg_11_out_45,
       shiftreg_11_out_46, shiftreg_11_out_47, shiftreg_11_out_48, shiftreg_11_out_49, shiftreg_11_out_50,
       shiftreg_11_out_51, shiftreg_11_out_52, shiftreg_11_out_53, shiftreg_11_out_54, shiftreg_11_out_55,
       shiftreg_11_out_56, shiftreg_11_out_57, shiftreg_11_out_58, shiftreg_11_out_59, shiftreg_11_out_60,
       shiftreg_11_out_61, shiftreg_11_out_62, shiftreg_11_out_63, shiftreg_11_out_64, shiftreg_11_out_65,
       shiftreg_11_out_66, shiftreg_11_out_67, shiftreg_11_out_68, shiftreg_11_out_69, shiftreg_11_shift_out,
       shiftreg_12_out_38, shiftreg_12_out_39, shiftreg_12_out_40, shiftreg_12_out_41, shiftreg_12_out_42,
       shiftreg_12_out_43, shiftreg_12_out_44, shiftreg_12_out_45, shiftreg_12_out_46, shiftreg_12_out_47,
       shiftreg_12_out_48, shiftreg_12_out_49, shiftreg_12_out_50, shiftreg_12_out_51, shiftreg_12_out_52,
       shiftreg_12_out_53, shiftreg_12_out_54, shiftreg_12_out_55, shiftreg_12_out_56, shiftreg_12_out_57,
       shiftreg_12_out_58, shiftreg_12_out_59, shiftreg_12_out_60, shiftreg_12_out_61, shiftreg_12_out_62,
       shiftreg_12_out_63, shiftreg_12_out_64, shiftreg_12_out_65, shiftreg_12_out_66, shiftreg_12_out_67,
       shiftreg_12_out_68, shiftreg_12_out_69, shiftreg_12_shift_out;

  Pull_Resistor pull_resistor_1 (.node(jump_clk));
  speeddino speeddino_1 (.speed(speed), .clk(speeddino_1_clk));
  assign jump_clk = not_1_out ? speeddino_1_clk : 1'bz;  // Controlled_Buffer controlled_buffer_1
  not not_1 (not_1_out, stop);
  speed speed_1 (.speed(speed), .clk(clk_cdm));
  Pull_Resistor pull_resistor_2 (.node(clk));
  assign clk = not_2_out ? clk_cdm : 1'bz;  // Controlled_Buffer controlled_buffer_2
  not not_2 (not_2_out, stop);
  and and_1 (kboard_clk, clk_cdm, sen_num);
  not not_3 (not_3_out, stop);
  and and_2 (clrp, not_3_out, stop);
  or or_1 (or_1_out, clrp, clear);
  or or_2 (clr, sen_kboard, keyboard_handler_1_reset);
  keyboard_handler keyboard_handler_1 (
    .key(key), .crouch(keyboard_handler_1_crouch), .jump(keyboard_handler_1_jump),
    .pause(keyboard_handler_1_pause), .reset(keyboard_handler_1_reset), .is_jump(dino_jump_1_is_jump),
    .sen_kboard(sen_kboard));
  or or_3 (stop, keyboard_handler_1_pause, col);
  dino_jump dino_jump_1 (
    .clr(clr), .jump(keyboard_handler_1_jump), .crouch(keyboard_handler_1_crouch), .Y(dino_jump_1_y),
    .is_jump(dino_jump_1_is_jump), .is_crouch(dino_jump_1_is_crouch), .clk(jump_clk));
  nickname nickname_1 (
    .clear(or_1_out), .clear_2(out_230), .key(in_4), .key_2(char), .not_empty(in_5), .enter(enter),
    .get_data(sen_kboard), .get_data_2(out_262), .ready(ready), .ignore(out_229));
  invertor invertor_1 (
    .out_131(out_38), .out_132(out_39), .out_133(out_40), .out_134(out_41), .out_135(out_42),
    .out_136(out_43), .out_137(out_44), .out_138(out_45), .out_139(out_46), .out_140(out_47),
    .out_141(out_48), .out_142(out_49), .out_143(out_50), .out_144(out_51), .out_145(out_52),
    .out_146(out_53), .out_147(out_54), .out_148(out_55), .out_149(out_56), .out_150(out_57),
    .out_151(out_58), .out_152(out_59), .out_153(out_60), .out_154(out_61), .out_155(out_62),
    .out_156(out_63), .out_157(out_64), .out_158(out_65), .out_159(out_66), .out_160(out_67),
    .out_161(out_68), .out_162(out_69), .out_163(out_70), .out_164(out_71), .out_165(out_72),
    .out_166(out_73), .out_167(out_74), .out_168(out_75), .out_169(out_76), .out_170(out_77),
    .out_171(out_78), .out_172(out_79), .out_173(out_80), .out_174(out_81), .out_175(out_82),
    .out_176(out_83), .out_177(out_84), .out_178(out_85), .out_179(out_86), .out_180(out_87),
    .out_181(out_88), .out_182(out_89), .out_183(out_90), .out_184(out_91), .out_185(out_92),
    .out_186(out_93), .out_187(out_94), .out_188(out_95), .out_189(out_96), .out_190(out_97),
    .out_191(out_98), .out_192(out_99), .out_193(out_100), .out_194(out_101), .out_195(out_102),
    .out_196(out_103), .out_197(out_104), .out_198(out_105), .out_199(out_106), .out_200(out_107),
    .out_201(out_108), .out_202(out_109), .out_203(out_110), .out_204(out_111), .out_205(out_112),
    .out_206(out_113), .out_207(out_114), .out_208(out_115), .out_209(out_116), .out_210(out_117),
    .out_211(out_118), .out_212(out_119), .out_213(out_120), .out_214(out_121), .out_215(out_122),
    .out_216(out_123), .out_217(out_124), .out_218(out_125), .out_219(out_126), .out_220(out_127),
    .out_221(out_128), .out_222(out_129), .out_223(out_130), .out_224(out_131), .out_225(out_132),
    .out_226(out_133), .out_227(out_134), .out_228(out_135), .out_229(out_136), .out_230(out_137),
    .out_231(out_138), .out_232(out_139), .out_233(out_140), .out_234(out_141), .out_235(out_142),
    .out_236(out_143), .out_237(out_144), .out_238(out_145), .out_239(out_146), .out_240(out_147),
    .out_241(out_148), .out_242(out_149), .out_243(out_150), .out_244(out_151), .out_245(out_152),
    .out_246(out_153), .out_247(out_154), .out_248(out_155), .out_249(out_156), .out_250(out_157),
    .out_251(out_158), .out_252(out_159), .out_253(out_160), .out_254(out_161), .out_255(out_162),
    .out_256(out_163), .out_257(out_164), .out_258(out_165), .in_3(dino_1_out_18), .in_4(dino_1_out_19),
    .in_5(dino_1_out_20), .in_6(dino_1_out_21), .in_7(dino_1_out_22), .in_8(dino_1_out_23),
    .in_9(dino_1_out_24), .in_10(dino_1_out_25), .in_11(dino_1_out_26), .in_12(dino_1_out_27),
    .in_13(dino_1_out_28), .in_14(shiftreg_1_out_58), .in_15(shiftreg_1_out_57), .in_16(shiftreg_1_out_56),
    .in_17(shiftreg_1_out_55), .in_18(shiftreg_1_out_54), .in_19(shiftreg_1_out_53),
    .in_20(shiftreg_1_out_52), .in_21(shiftreg_1_out_51), .in_22(shiftreg_1_out_50),
    .in_23(shiftreg_1_out_49), .in_24(shiftreg_1_out_48), .in_25(shiftreg_1_out_47),
    .in_26(shiftreg_1_out_46), .in_27(shiftreg_1_out_45), .in_28(shiftreg_1_out_44),
    .in_29(shiftreg_1_out_43), .in_30(shiftreg_1_out_42), .in_31(shiftreg_1_out_41),
    .in_32(shiftreg_1_out_40), .in_33(shiftreg_1_out_39), .in_34(shiftreg_1_out_38),
    .in_35(gameover_1_out_66), .in_36(gameover_1_out_67), .in_37(gameover_1_out_68),
    .in_38(gameover_1_out_69), .in_39(gameover_1_out_70), .in_40(gameover_1_out_71),
    .in_41(gameover_1_out_72), .in_42(gameover_1_out_73), .in_43(gameover_1_out_74),
    .in_44(gameover_1_out_75), .in_45(gameover_1_out_76), .in_46(gameover_1_out_77),
    .in_47(gameover_1_out_78), .in_48(gameover_1_out_79), .in_49(gameover_1_out_80),
    .in_50(gameover_1_out_81), .in_51(gameover_1_out_82), .in_52(gameover_1_out_83),
    .in_53(gameover_1_out_84), .in_54(gameover_1_out_85), .in_55(gameover_1_out_86),
    .in_56(gameover_1_out_87), .in_57(gameover_1_out_88), .in_58(gameover_1_out_89),
    .in_59(gameover_1_out_90), .in_60(gameover_1_out_91), .in_61(gameover_1_out_92),
    .in_62(gameover_1_out_93), .in_63(gameover_1_out_94), .in_64(gameover_1_out_95),
    .in_65(gameover_1_out_96), .in_66(gameover_1_out_97), .in_67(gameover_1_out_98),
    .in_68(gameover_1_out_99), .in_69(gameover_1_out_100), .in_70(gameover_1_out_101),
    .in_71(gameover_1_out_102), .in_72(gameover_1_out_103), .in_73(gameover_1_out_104),
    .in_74(gameover_1_out_105), .in_75(gameover_1_out_106), .in_76(gameover_1_out_107),
    .in_77(gameover_1_out_108), .in_78(gameover_1_out_109), .in_79(gameover_1_out_110),
    .in_80(gameover_1_out_111), .in_81(gameover_1_out_112), .in_82(gameover_1_out_113),
    .in_83(gameover_1_out_114), .in_84(gameover_1_out_115), .in_85(gameover_1_out_116),
    .in_86(gameover_1_out_117), .in_87(gameover_1_out_118), .in_88(gameover_1_out_119),
    .in_89(gameover_1_out_120), .in_90(gameover_1_out_121), .in_91(gameover_1_out_122),
    .in_92(gameover_1_out_123), .in_93(gameover_1_out_124), .in_94(gameover_1_out_125),
    .in_95(gameover_1_out_126), .in_96(gameover_1_out_127), .in_97(gameover_1_out_128),
    .in_98(gameover_1_out_129), .in_99(shiftreg_10_out_69), .in_100(shiftreg_10_out_68),
    .in_101(shiftreg_10_out_67), .in_102(shiftreg_10_out_66), .in_103(shiftreg_10_out_65),
    .in_104(shiftreg_10_out_64), .in_105(shiftreg_10_out_63), .in_106(shiftreg_10_out_62),
    .in_107(shiftreg_10_out_61), .in_108(shiftreg_10_out_60), .in_109(shiftreg_10_out_59),
    .in_110(shiftreg_10_out_58), .in_111(shiftreg_10_out_57), .in_112(shiftreg_10_out_56),
    .in_113(shiftreg_10_out_55), .in_114(shiftreg_10_out_54), .in_115(shiftreg_10_out_53),
    .in_116(shiftreg_10_out_52), .in_117(shiftreg_10_out_51), .in_118(shiftreg_10_out_50),
    .in_119(shiftreg_10_out_49), .in_120(shiftreg_10_out_48), .in_121(shiftreg_10_out_47),
    .in_122(shiftreg_10_out_46), .in_123(shiftreg_10_out_45), .in_124(shiftreg_10_out_44),
    .in_125(shiftreg_10_out_43), .in_126(shiftreg_10_out_42), .in_127(shiftreg_10_out_41),
    .in_128(shiftreg_10_out_40), .in_129(shiftreg_10_out_39), .in_130(shiftreg_10_out_38), .switch(day_sw),
    .clr(clr));
  dino dino_1 (
    .clk(clk), .is_crouch(dino_jump_1_is_crouch), .Y(dino_jump_1_y), .is_jump(dino_jump_1_is_jump),
    .out_18(dino_1_out_18), .out_19(dino_1_out_19), .out_20(dino_1_out_20), .out_21(dino_1_out_21),
    .out_22(dino_1_out_22), .out_23(dino_1_out_23), .out_24(dino_1_out_24), .out_25(dino_1_out_25),
    .out_26(dino_1_out_26), .out_27(dino_1_out_27), .out_28(dino_1_out_28), .in_15(shiftreg_1_out_59),
    .in_14(shiftreg_1_out_60), .in_13(shiftreg_1_out_61), .in_12(shiftreg_1_out_62),
    .in_11(shiftreg_1_out_63), .in_10(shiftreg_1_out_64), .in_9(shiftreg_1_out_65), .in_7(shiftreg_1_out_66),
    .in_4(shiftreg_1_out_67), .in_3(shiftreg_1_out_68), .in_2(shiftreg_1_out_69), .collision(col), .clr(clr),
    .cls(col));
  Counter #(.max('h2)) counter_1 (.carry(counter_1_carry), .clk(clk));  // open: load, D, count, Q, clr
  number_sen number_sen_1 (.sen(sen_num), .reset(clr), .num_in(num_out), .num_out(number_sen_1_num_out));
  and and_3 (and_3_out, sen_num, col);
  or or_4 (or_4_out, and_3_out, and_4_out);
  and and_4 (and_4_out, ready, sen_kboard);
  gameover gameover_1 (
    .is_gameover(and_5_out), .out_66(gameover_1_out_66), .out_67(gameover_1_out_67),
    .out_68(gameover_1_out_68), .out_69(gameover_1_out_69), .out_70(gameover_1_out_70),
    .out_71(gameover_1_out_71), .out_72(gameover_1_out_72), .out_73(gameover_1_out_73),
    .out_74(gameover_1_out_74), .out_75(gameover_1_out_75), .out_76(gameover_1_out_76),
    .out_77(gameover_1_out_77), .out_78(gameover_1_out_78), .out_79(gameover_1_out_79),
    .out_80(gameover_1_out_80), .out_81(gameover_1_out_81), .out_82(gameover_1_out_82),
    .out_83(gameover_1_out_83), .out_84(gameover_1_out_84), .out_85(gameover_1_out_85),
    .out_86(gameover_1_out_86), .out_87(gameover_1_out_87), .out_88(gameover_1_out_88),
    .out_89(gameover_1_out_89), .out_90(gameover_1_out_90), .out_91(gameover_1_out_91),
    .out_92(gameover_1_out_92), .out_93(gameover_1_out_93), .out_94(gameover_1_out_94),
    .out_95(gameover_1_out_95), .out_96(gameover_1_out_96), .out_97(gameover_1_out_97),
    .out_98(gameover_1_out_98), .out_99(gameover_1_out_99), .out_100(gameover_1_out_100),
    .out_101(gameover_1_out_101), .out_102(gameover_1_out_102), .out_103(gameover_1_out_103),
    .out_104(gameover_1_out_104), .out_105(gameover_1_out_105), .out_106(gameover_1_out_106),
    .out_107(gameover_1_out_107), .out_108(gameover_1_out_108), .out_109(gameover_1_out_109),
    .out_110(gameover_1_out_110), .out_111(gameover_1_out_111), .out_112(gameover_1_out_112),
    .out_113(gameover_1_out_113), .out_114(gameover_1_out_114), .out_115(gameover_1_out_115),
    .out_116(gameover_1_out_116), .out_117(gameover_1_out_117), .out_118(gameover_1_out_118),
    .out_119(gameover_1_out_119), .out_120(gameover_1_out_120), .out_121(gameover_1_out_121),
    .out_122(gameover_1_out_122), .out_123(gameover_1_out_123), .out_124(gameover_1_out_124),
    .out_125(gameover_1_out_125), .out_126(gameover_1_out_126), .out_127(gameover_1_out_127),
    .out_128(gameover_1_out_128), .out_129(gameover_1_out_129), .in_2(pause_1_out_66), .in_3(pause_1_out_67),
    .in_4(pause_1_out_68), .in_5(pause_1_out_69), .in_6(pause_1_out_70), .in_7(pause_1_out_71),
    .in_8(pause_1_out_72), .in_9(pause_1_out_73), .in_10(pause_1_out_74), .in_11(pause_1_out_75),
    .in_12(pause_1_out_76), .in_13(pause_1_out_77), .in_14(pause_1_out_78), .in_15(pause_1_out_79),
    .in_16(pause_1_out_80), .in_17(pause_1_out_81), .in_18(pause_1_out_82), .in_19(pause_1_out_83),
    .in_20(pause_1_out_84), .in_21(pause_1_out_85), .in_22(pause_1_out_86), .in_23(pause_1_out_87),
    .in_24(pause_1_out_88), .in_25(pause_1_out_89), .in_26(pause_1_out_90), .in_27(pause_1_out_91),
    .in_28(pause_1_out_92), .in_29(pause_1_out_93), .in_30(pause_1_out_94), .in_31(pause_1_out_95),
    .in_32(pause_1_out_96), .in_33(pause_1_out_97), .in_34(pause_1_out_98), .in_35(pause_1_out_99),
    .in_36(pause_1_out_100), .in_37(pause_1_out_101), .in_38(pause_1_out_102), .in_39(pause_1_out_103),
    .in_40(pause_1_out_104), .in_41(pause_1_out_105), .in_42(pause_1_out_106), .in_43(pause_1_out_107),
    .in_44(pause_1_out_108), .in_45(pause_1_out_109), .in_46(pause_1_out_110), .in_47(pause_1_out_111),
    .in_48(pause_1_out_112), .in_49(pause_1_out_113), .in_50(pause_1_out_114), .in_51(pause_1_out_115),
    .in_52(pause_1_out_116), .in_53(pause_1_out_117), .in_54(pause_1_out_118), .in_55(pause_1_out_119),
    .in_56(pause_1_out_120), .in_57(pause_1_out_121), .in_58(pause_1_out_122), .in_59(pause_1_out_123),
    .in_60(pause_1_out_124), .in_61(pause_1_out_125), .in_62(pause_1_out_126), .in_63(pause_1_out_127),
    .in_64(pause_1_out_128), .in_65(pause_1_out_129));
  pause pause_1 (
    .is_pause(and_6_out), .out_66(pause_1_out_66), .out_67(pause_1_out_67), .out_68(pause_1_out_68),
    .out_69(pause_1_out_69), .out_70(pause_1_out_70), .out_71(pause_1_out_71), .out_72(pause_1_out_72),
    .out_73(pause_1_out_73), .out_74(pause_1_out_74), .out_75(pause_1_out_75), .out_76(pause_1_out_76),
    .out_77(pause_1_out_77), .out_78(pause_1_out_78), .out_79(pause_1_out_79), .out_80(pause_1_out_80),
    .out_81(pause_1_out_81), .out_82(pause_1_out_82), .out_83(pause_1_out_83), .out_84(pause_1_out_84),
    .out_85(pause_1_out_85), .out_86(pause_1_out_86), .out_87(pause_1_out_87), .out_88(pause_1_out_88),
    .out_89(pause_1_out_89), .out_90(pause_1_out_90), .out_91(pause_1_out_91), .out_92(pause_1_out_92),
    .out_93(pause_1_out_93), .out_94(pause_1_out_94), .out_95(pause_1_out_95), .out_96(pause_1_out_96),
    .out_97(pause_1_out_97), .out_98(pause_1_out_98), .out_99(pause_1_out_99), .out_100(pause_1_out_100),
    .out_101(pause_1_out_101), .out_102(pause_1_out_102), .out_103(pause_1_out_103),
    .out_104(pause_1_out_104), .out_105(pause_1_out_105), .out_106(pause_1_out_106),
    .out_107(pause_1_out_107), .out_108(pause_1_out_108), .out_109(pause_1_out_109),
    .out_110(pause_1_out_110), .out_111(pause_1_out_111), .out_112(pause_1_out_112),
    .out_113(pause_1_out_113), .out_114(pause_1_out_114), .out_115(pause_1_out_115),
    .out_116(pause_1_out_116), .out_117(pause_1_out_117), .out_118(pause_1_out_118),
    .out_119(pause_1_out_119), .out_120(pause_1_out_120), .out_121(pause_1_out_121),
    .out_122(pause_1_out_122), .out_123(pause_1_out_123), .out_124(pause_1_out_124),
    .out_125(pause_1_out_125), .out_126(pause_1_out_126), .out_127(pause_1_out_127),
    .out_128(pause_1_out_128), .out_129(pause_1_out_129), .in_2(shiftreg_4_out_69), .in_3(shiftreg_4_out_68),
    .in_4(shiftreg_4_out_67), .in_5(shiftreg_4_out_66), .in_6(shiftreg_4_out_65), .in_7(shiftreg_4_out_64),
    .in_8(shiftreg_4_out_63), .in_9(shiftreg_4_out_62), .in_10(shiftreg_4_out_61), .in_11(shiftreg_4_out_60),
    .in_12(shiftreg_4_out_59), .in_13(shiftreg_4_out_58), .in_14(shiftreg_4_out_57),
    .in_15(shiftreg_4_out_56), .in_16(shiftreg_4_out_55), .in_17(shiftreg_4_out_54),
    .in_18(shiftreg_4_out_53), .in_19(shiftreg_4_out_52), .in_20(shiftreg_4_out_51),
    .in_21(shiftreg_4_out_50), .in_22(shiftreg_4_out_49), .in_23(shiftreg_4_out_48),
    .in_24(shiftreg_4_out_47), .in_25(shiftreg_4_out_46), .in_26(shiftreg_4_out_45),
    .in_27(shiftreg_4_out_44), .in_28(shiftreg_4_out_43), .in_29(shiftreg_4_out_42),
    .in_30(shiftreg_4_out_41), .in_31(shiftreg_4_out_40), .in_32(shiftreg_4_out_39),
    .in_33(shiftreg_4_out_38), .in_34(shiftreg_7_out_69), .in_35(shiftreg_7_out_68),
    .in_36(shiftreg_7_out_67), .in_37(shiftreg_7_out_66), .in_38(shiftreg_7_out_65),
    .in_39(shiftreg_7_out_64), .in_40(shiftreg_7_out_63), .in_41(shiftreg_7_out_62),
    .in_42(shiftreg_7_out_61), .in_43(shiftreg_7_out_60), .in_44(shiftreg_7_out_59),
    .in_45(shiftreg_7_out_58), .in_46(shiftreg_7_out_57), .in_47(shiftreg_7_out_56),
    .in_48(shiftreg_7_out_55), .in_49(shiftreg_7_out_54), .in_50(shiftreg_7_out_53),
    .in_51(shiftreg_7_out_52), .in_52(shiftreg_7_out_51), .in_53(shiftreg_7_out_50),
    .in_54(shiftreg_7_out_49), .in_55(shiftreg_7_out_48), .in_56(shiftreg_7_out_47),
    .in_57(shiftreg_7_out_46), .in_58(shiftreg_7_out_45), .in_59(shiftreg_7_out_44),
    .in_60(shiftreg_7_out_43), .in_61(shiftreg_7_out_42), .in_62(shiftreg_7_out_41),
    .in_63(shiftreg_7_out_40), .in_64(shiftreg_7_out_39), .in_65(shiftreg_7_out_38));
  shiftreg shiftreg_1 (
    .clk(clk), .shift_in(shiftreg_4_shift_out), .in_4(shiftreg_2_out_38), .out_38(shiftreg_1_out_38),
    .out_39(shiftreg_1_out_39), .in_13(shiftreg_2_out_47), .out_40(shiftreg_1_out_40),
    .in_6(shiftreg_2_out_40), .out_41(shiftreg_1_out_41), .in_7(shiftreg_2_out_41),
    .out_42(shiftreg_1_out_42), .in_8(shiftreg_2_out_42), .out_43(shiftreg_1_out_43),
    .out_44(shiftreg_1_out_44), .out_45(shiftreg_1_out_45), .out_46(shiftreg_1_out_46),
    .in_9(shiftreg_2_out_43), .in_10(shiftreg_2_out_44), .in_11(shiftreg_2_out_45),
    .in_12(shiftreg_2_out_46), .in_5(shiftreg_2_out_39), .out_47(shiftreg_1_out_47),
    .out_48(shiftreg_1_out_48), .out_49(shiftreg_1_out_49), .out_50(shiftreg_1_out_50),
    .out_51(shiftreg_1_out_51), .out_52(shiftreg_1_out_52), .out_53(shiftreg_1_out_53),
    .out_54(shiftreg_1_out_54), .in_14(shiftreg_2_out_48), .in_15(shiftreg_2_out_49),
    .in_16(shiftreg_2_out_50), .in_17(shiftreg_2_out_51), .in_18(shiftreg_2_out_52),
    .in_19(shiftreg_2_out_53), .in_20(shiftreg_2_out_54), .out_55(shiftreg_1_out_55),
    .out_56(shiftreg_1_out_56), .out_57(shiftreg_1_out_57), .out_58(shiftreg_1_out_58),
    .out_59(shiftreg_1_out_59), .in_21(shiftreg_2_out_55), .in_22(shiftreg_2_out_56),
    .in_23(shiftreg_2_out_57), .in_24(shiftreg_2_out_58), .in_25(shiftreg_2_out_59),
    .out_60(shiftreg_1_out_60), .out_61(shiftreg_1_out_61), .in_26(shiftreg_2_out_60),
    .in_27(shiftreg_2_out_61), .out_62(shiftreg_1_out_62), .out_63(shiftreg_1_out_63),
    .in_28(shiftreg_2_out_62), .in_29(shiftreg_2_out_63), .out_64(shiftreg_1_out_64),
    .out_65(shiftreg_1_out_65), .out_66(shiftreg_1_out_66), .in_30(shiftreg_2_out_64),
    .in_31(shiftreg_2_out_65), .in_32(shiftreg_2_out_66), .out_67(shiftreg_1_out_67),
    .out_68(shiftreg_1_out_68), .out_69(shiftreg_1_out_69), .in_33(shiftreg_2_out_67),
    .in_34(shiftreg_2_out_68), .in_35(shiftreg_2_out_69), .clr(clr), .prev_clear(shiftreg_4_clear));  // open: shift_out, clear, hide
  shiftreg shiftreg_2 (
    .clk(birds_1_birds_clk), .shift_in(shiftreg_5_shift_out), .in_4(shiftreg_3_out_38),
    .out_38(shiftreg_2_out_38), .out_39(shiftreg_2_out_39), .in_13(shiftreg_3_out_47),
    .out_40(shiftreg_2_out_40), .in_6(shiftreg_3_out_40), .out_41(shiftreg_2_out_41),
    .in_7(shiftreg_3_out_41), .out_42(shiftreg_2_out_42), .in_8(shiftreg_3_out_42),
    .out_43(shiftreg_2_out_43), .out_44(shiftreg_2_out_44), .out_45(shiftreg_2_out_45),
    .out_46(shiftreg_2_out_46), .in_9(shiftreg_3_out_43), .in_10(shiftreg_3_out_44),
    .in_11(shiftreg_3_out_45), .in_12(shiftreg_3_out_46), .in_5(shiftreg_3_out_39),
    .out_47(shiftreg_2_out_47), .out_48(shiftreg_2_out_48), .out_49(shiftreg_2_out_49),
    .out_50(shiftreg_2_out_50), .out_51(shiftreg_2_out_51), .out_52(shiftreg_2_out_52),
    .out_53(shiftreg_2_out_53), .out_54(shiftreg_2_out_54), .in_14(shiftreg_3_out_48),
    .in_15(shiftreg_3_out_49), .in_16(shiftreg_3_out_50), .in_17(shiftreg_3_out_51),
    .in_18(shiftreg_3_out_52), .in_19(shiftreg_3_out_53), .in_20(shiftreg_3_out_54),
    .out_55(shiftreg_2_out_55), .out_56(shiftreg_2_out_56), .out_57(shiftreg_2_out_57),
    .out_58(shiftreg_2_out_58), .out_59(shiftreg_2_out_59), .in_21(shiftreg_3_out_55),
    .in_22(shiftreg_3_out_56), .in_23(shiftreg_3_out_57), .in_24(shiftreg_3_out_58),
    .in_25(shiftreg_3_out_59), .out_60(shiftreg_2_out_60), .out_61(shiftreg_2_out_61),
    .in_26(shiftreg_3_out_60), .in_27(shiftreg_3_out_61), .out_62(shiftreg_2_out_62),
    .out_63(shiftreg_2_out_63), .in_28(shiftreg_3_out_62), .in_29(shiftreg_3_out_63),
    .out_64(shiftreg_2_out_64), .out_65(shiftreg_2_out_65), .out_66(shiftreg_2_out_66),
    .in_30(shiftreg_3_out_64), .in_31(shiftreg_3_out_65), .in_32(shiftreg_3_out_66),
    .out_67(shiftreg_2_out_67), .out_68(shiftreg_2_out_68), .out_69(shiftreg_2_out_69),
    .in_33(shiftreg_3_out_67), .in_34(shiftreg_3_out_68), .in_35(shiftreg_3_out_69), .clr(clr),
    .prev_clear(shiftreg_5_clear), .hide(t_ff_1_qn));  // open: shift_out, clear
  shiftreg shiftreg_3 (
    .clk(birds_1_birds_clk), .shift_in(shiftreg_6_shift_out), .out_38(shiftreg_3_out_38),
    .out_39(shiftreg_3_out_39), .out_40(shiftreg_3_out_40), .out_41(shiftreg_3_out_41),
    .out_42(shiftreg_3_out_42), .out_43(shiftreg_3_out_43), .out_44(shiftreg_3_out_44),
    .out_45(shiftreg_3_out_45), .out_46(shiftreg_3_out_46), .out_47(shiftreg_3_out_47),
    .out_48(shiftreg_3_out_48), .out_49(shiftreg_3_out_49), .out_50(shiftreg_3_out_50),
    .out_51(shiftreg_3_out_51), .out_52(shiftreg_3_out_52), .out_53(shiftreg_3_out_53),
    .out_54(shiftreg_3_out_54), .out_55(shiftreg_3_out_55), .out_56(shiftreg_3_out_56),
    .out_57(shiftreg_3_out_57), .out_58(shiftreg_3_out_58), .out_59(shiftreg_3_out_59),
    .out_60(shiftreg_3_out_60), .out_61(shiftreg_3_out_61), .out_62(shiftreg_3_out_62),
    .out_63(shiftreg_3_out_63), .out_64(shiftreg_3_out_64), .out_65(shiftreg_3_out_65),
    .out_66(shiftreg_3_out_66), .out_67(shiftreg_3_out_67), .out_68(shiftreg_3_out_68),
    .out_69(shiftreg_3_out_69), .clr(clr), .prev_clear(shiftreg_6_clear), .clear(shiftreg_3_clear),
    .hide(t_ff_1_q));  // open: shift_out, in_4, in_13, in_6, in_7, in_8, in_9, in_10, in_11, in_12, in_5, in_14, in_15, in_16, in_17, in_18, in_19, in_20, in_21, in_22, in_23, in_24, in_25, in_26, in_27, in_28, in_29, in_30, in_31, in_32, in_33, in_34, in_35
  counter counter_2 (
    .stop(stop), .reset(clr), ._3(out_31), ._2(out_32), ._1(out_33), .thous(thous), .clock(counter_1_carry),
    .hund(hund), .out_10(num_out), ._4(out_30));
  cdm8_main main_1 (
    .char(char), .num(number_sen_1_num_out), .ready(or_4_out), .out_5(sym), .clock_2(clkp),
    .sen_num(sen_num), .sen_kboard(sen_kboard), .clock(clk_cdm));
  level_new level_new_1 (
    .clock(clk), .hund(hund), .thous(thous), .reset(clr), .out_5(out_6), .out_6(out_7), .out_7(out_27),
    .out_8(out_28), .out_9(out_29), .out_10(out_8), .out_11(out_9), .out_12(out_10), .out_13(out_11),
    .out_14(out_12), .out_15(out_13), .out_16(out_14), .out_17(out_15), .speed(speed), .out_19(out_16),
    .out_20(out_17), .out_21(out_18), .out_22(out_19), .out_23(out_20), .out_24(out_21), .out_25(out_22),
    .out_26(out_23), .out_27(out_24), .out_28(out_25), .out_29(out_26));
  shiftreg shiftreg_4 (
    .clk(clk), .shift_in(shiftreg_7_shift_out), .shift_out(shiftreg_4_shift_out), .in_4(shiftreg_5_out_38),
    .out_38(shiftreg_4_out_38), .out_39(shiftreg_4_out_39), .in_13(shiftreg_5_out_47),
    .out_40(shiftreg_4_out_40), .in_6(shiftreg_5_out_40), .out_41(shiftreg_4_out_41),
    .in_7(shiftreg_5_out_41), .out_42(shiftreg_4_out_42), .in_8(shiftreg_5_out_42),
    .out_43(shiftreg_4_out_43), .out_44(shiftreg_4_out_44), .out_45(shiftreg_4_out_45),
    .out_46(shiftreg_4_out_46), .in_9(shiftreg_5_out_43), .in_10(shiftreg_5_out_44),
    .in_11(shiftreg_5_out_45), .in_12(shiftreg_5_out_46), .in_5(shiftreg_5_out_39),
    .out_47(shiftreg_4_out_47), .out_48(shiftreg_4_out_48), .out_49(shiftreg_4_out_49),
    .out_50(shiftreg_4_out_50), .out_51(shiftreg_4_out_51), .out_52(shiftreg_4_out_52),
    .out_53(shiftreg_4_out_53), .out_54(shiftreg_4_out_54), .in_14(shiftreg_5_out_48),
    .in_15(shiftreg_5_out_49), .in_16(shiftreg_5_out_50), .in_17(shiftreg_5_out_51),
    .in_18(shiftreg_5_out_52), .in_19(shiftreg_5_out_53), .in_20(shiftreg_5_out_54),
    .out_55(shiftreg_4_out_55), .out_56(shiftreg_4_out_56), .out_57(shiftreg_4_out_57),
    .out_58(shiftreg_4_out_58), .out_59(shiftreg_4_out_59), .in_21(shiftreg_5_out_55),
    .in_22(shiftreg_5_out_56), .in_23(shiftreg_5_out_57), .in_24(shiftreg_5_out_58),
    .in_25(shiftreg_5_out_59), .out_60(shiftreg_4_out_60), .out_61(shiftreg_4_out_61),
    .in_26(shiftreg_5_out_60), .in_27(shiftreg_5_out_61), .out_62(shiftreg_4_out_62),
    .out_63(shiftreg_4_out_63), .in_28(shiftreg_5_out_62), .in_29(shiftreg_5_out_63),
    .out_64(shiftreg_4_out_64), .out_65(shiftreg_4_out_65), .out_66(shiftreg_4_out_66),
    .in_30(shiftreg_5_out_64), .in_31(shiftreg_5_out_65), .in_32(shiftreg_5_out_66),
    .out_67(shiftreg_4_out_67), .out_68(shiftreg_4_out_68), .out_69(shiftreg_4_out_69),
    .in_33(shiftreg_5_out_67), .in_34(shiftreg_5_out_68), .in_35(shiftreg_5_out_69), .clr(clr),
    .prev_clear(shiftreg_7_clear), .clear(shiftreg_4_clear));  // open: hide
  shiftreg shiftreg_5 (
    .clk(birds_1_birds_clk), .shift_in(shiftreg_8_shift_out), .shift_out(shiftreg_5_shift_out),
    .in_4(shiftreg_6_out_38), .out_38(shiftreg_5_out_38), .out_39(shiftreg_5_out_39),
    .in_13(shiftreg_6_out_47), .out_40(shiftreg_5_out_40), .in_6(shiftreg_6_out_40),
    .out_41(shiftreg_5_out_41), .in_7(shiftreg_6_out_41), .out_42(shiftreg_5_out_42),
    .in_8(shiftreg_6_out_42), .out_43(shiftreg_5_out_43), .out_44(shiftreg_5_out_44),
    .out_45(shiftreg_5_out_45), .out_46(shiftreg_5_out_46), .in_9(shiftreg_6_out_43),
    .in_10(shiftreg_6_out_44), .in_11(shiftreg_6_out_45), .in_12(shiftreg_6_out_46),
    .in_5(shiftreg_6_out_39), .out_47(shiftreg_5_out_47), .out_48(shiftreg_5_out_48),
    .out_49(shiftreg_5_out_49), .out_50(shiftreg_5_out_50), .out_51(shiftreg_5_out_51),
    .out_52(shiftreg_5_out_52), .out_53(shiftreg_5_out_53), .out_54(shiftreg_5_out_54),
    .in_14(shiftreg_6_out_48), .in_15(shiftreg_6_out_49), .in_16(shiftreg_6_out_50),
    .in_17(shiftreg_6_out_51), .in_18(shiftreg_6_out_52), .in_19(shiftreg_6_out_53),
    .in_20(shiftreg_6_out_54), .out_55(shiftreg_5_out_55), .out_56(shiftreg_5_out_56),
    .out_57(shiftreg_5_out_57), .out_58(shiftreg_5_out_58), .out_59(shiftreg_5_out_59),
    .in_21(shiftreg_6_out_55), .in_22(shiftreg_6_out_56), .in_23(shiftreg_6_out_57),
    .in_24(shiftreg_6_out_58), .in_25(shiftreg_6_out_59), .out_60(shiftreg_5_out_60),
    .out_61(shiftreg_5_out_61), .in_26(shiftreg_6_out_60), .in_27(shiftreg_6_out_61),
    .out_62(shiftreg_5_out_62), .out_63(shiftreg_5_out_63), .in_28(shiftreg_6_out_62),
    .in_29(shiftreg_6_out_63), .out_64(shiftreg_5_out_64), .out_65(shiftreg_5_out_65),
    .out_66(shiftreg_5_out_66), .in_30(shiftreg_6_out_64), .in_31(shiftreg_6_out_65),
    .in_32(shiftreg_6_out_66), .out_67(shiftreg_5_out_67), .out_68(shiftreg_5_out_68),
    .out_69(shiftreg_5_out_69), .in_33(shiftreg_6_out_67), .in_34(shiftreg_6_out_68),
    .in_35(shiftreg_6_out_69), .clr(clr), .prev_clear(shiftreg_8_clear), .clear(shiftreg_5_clear),
    .hide(t_ff_1_qn));
  shiftreg shiftreg_6 (
    .clk(birds_1_birds_clk), .shift_in(shiftreg_9_shift_out), .shift_out(shiftreg_6_shift_out),
    .out_38(shiftreg_6_out_38), .out_39(shiftreg_6_out_39), .out_40(shiftreg_6_out_40),
    .out_41(shiftreg_6_out_41), .out_42(shiftreg_6_out_42), .out_43(shiftreg_6_out_43),
    .out_44(shiftreg_6_out_44), .out_45(shiftreg_6_out_45), .out_46(shiftreg_6_out_46),
    .out_47(shiftreg_6_out_47), .out_48(shiftreg_6_out_48), .out_49(shiftreg_6_out_49),
    .out_50(shiftreg_6_out_50), .out_51(shiftreg_6_out_51), .out_52(shiftreg_6_out_52),
    .out_53(shiftreg_6_out_53), .out_54(shiftreg_6_out_54), .out_55(shiftreg_6_out_55),
    .out_56(shiftreg_6_out_56), .out_57(shiftreg_6_out_57), .out_58(shiftreg_6_out_58),
    .out_59(shiftreg_6_out_59), .out_60(shiftreg_6_out_60), .out_61(shiftreg_6_out_61),
    .out_62(shiftreg_6_out_62), .out_63(shiftreg_6_out_63), .out_64(shiftreg_6_out_64),
    .out_65(shiftreg_6_out_65), .out_66(shiftreg_6_out_66), .out_67(shiftreg_6_out_67),
    .out_68(shiftreg_6_out_68), .out_69(shiftreg_6_out_69), .clr(clr), .prev_clear(shiftreg_9_clear),
    .clear(shiftreg_6_clear), .hide(t_ff_1_q));  // open: in_4, in_13, in_6, in_7, in_8, in_9, in_10, in_11, in_12, in_5, in_14, in_15, in_16, in_17, in_18, in_19, in_20, in_21, in_22, in_23, in_24, in_25, in_26, in_27, in_28, in_29, in_30, in_31, in_32, in_33, in_34, in_35
  magic_printer magic_printer_1 (
    .in_1(sym), .clock(clkp), .reset(clrp), .out_4(out_294), .out_5(out_295), .out_6(out_296),
    .out_7(out_297), .out_8(out_298), .out_9(out_299), .out_10(out_300), .out_11(out_301), .out_12(out_302),
    .out_13(out_303), .out_14(out_304), .out_15(out_305), .out_16(out_306), .out_17(out_307),
    .out_18(out_308), .out_19(out_309), .out_21(out_319), .out_22(out_320), .out_23(out_321),
    .out_24(out_322), .out_25(out_323), .out_27(out_317), .out_35(out_263), .out_36(out_264),
    .out_37(out_265), .out_38(out_266), .out_39(out_267), .out_40(out_268), .out_41(out_269),
    .out_42(out_270), .out_43(out_271), .out_44(out_272), .out_45(out_273), .out_46(out_274),
    .out_47(out_275), .out_48(out_276), .out_49(out_277), .out_50(out_278), .out_66(out_231),
    .out_67(out_232), .out_68(out_233), .out_69(out_234), .out_70(out_235), .out_71(out_236),
    .out_72(out_237), .out_73(out_238), .out_74(out_239), .out_75(out_240), .out_76(out_241),
    .out_77(out_242), .out_78(out_243), .out_79(out_244), .out_80(out_245), .out_81(out_246),
    .out_97(out_198), .out_98(out_199), .out_99(out_200), .out_100(out_201), .out_101(out_202),
    .out_102(out_203), .out_103(out_204), .out_104(out_205), .out_105(out_206), .out_106(out_207),
    .out_107(out_208), .out_108(out_209), .out_109(out_210), .out_110(out_211), .out_111(out_212),
    .out_112(out_213), .out_128(out_167), .out_129(out_168), .out_130(out_169), .out_131(out_170),
    .out_132(out_171), .out_133(out_172), .out_134(out_173), .out_135(out_174), .out_136(out_175),
    .out_137(out_176), .out_138(out_177), .out_139(out_178), .out_140(out_179), .out_141(out_180),
    .out_142(out_181), .out_143(out_182), .out_20(out_318), .out_26(out_324), .out_28(out_310),
    .out_29(out_311), .out_30(out_312), .out_31(out_313), .out_32(out_314), .out_33(out_315),
    .out_34(out_316), .out_51(out_287), .out_52(out_288), .out_53(out_289), .out_54(out_290),
    .out_55(out_291), .out_56(out_292), .out_57(out_293), .out_58(out_286), .out_59(out_279),
    .out_60(out_280), .out_61(out_281), .out_62(out_282), .out_63(out_283), .out_64(out_284),
    .out_65(out_285), .out_82(out_255), .out_83(out_256), .out_84(out_257), .out_85(out_258),
    .out_86(out_259), .out_87(out_260), .out_88(out_261), .out_89(out_254), .out_90(out_247),
    .out_91(out_248), .out_92(out_249), .out_93(out_250), .out_94(out_251), .out_95(out_252),
    .out_96(out_253), .out_113(out_222), .out_114(out_223), .out_115(out_224), .out_116(out_225),
    .out_117(out_226), .out_118(out_227), .out_119(out_228), .out_120(out_221), .out_121(out_214),
    .out_122(out_215), .out_123(out_216), .out_124(out_217), .out_125(out_218), .out_126(out_219),
    .out_127(out_220), .out_144(out_191), .out_145(out_192), .out_146(out_193), .out_147(out_194),
    .out_148(out_195), .out_149(out_196), .out_150(out_197), .out_151(out_190), .out_152(out_183),
    .out_153(out_184), .out_154(out_185), .out_155(out_186), .out_156(out_187), .out_157(out_188),
    .out_158(out_189));
  // Probe on speed
  timer timer_1 (
    .clock(clock_1_out), .stop(stop), .out_4(out_34), .out_5(out_35), .out_7(out_36), .out_8(out_37),
    .reset(clr));  // open: out_6
  Clock #(.lowDuration(511)) clock_1 (.out(clock_1_out));
  Counter #(.max('h1e)) counter_3 (
    .count(not_4_out), .carry(day_sw), .clk(clock_2_out), .clr(clr));  // open: load, D, Q
  not not_4 (not_4_out, stop);
  Clock #(.lowDuration(511)) clock_2 (.out(clock_2_out));
  shiftreg shiftreg_7 (
    .clk(clk), .shift_in(shiftreg_10_shift_out), .shift_out(shiftreg_7_shift_out), .in_4(shiftreg_8_out_38),
    .out_38(shiftreg_7_out_38), .out_39(shiftreg_7_out_39), .in_13(shiftreg_8_out_47),
    .out_40(shiftreg_7_out_40), .in_6(shiftreg_8_out_40), .out_41(shiftreg_7_out_41),
    .in_7(shiftreg_8_out_41), .out_42(shiftreg_7_out_42), .in_8(shiftreg_8_out_42),
    .out_43(shiftreg_7_out_43), .out_44(shiftreg_7_out_44), .out_45(shiftreg_7_out_45),
    .out_46(shiftreg_7_out_46), .in_9(shiftreg_8_out_43), .in_10(shiftreg_8_out_44),
    .in_11(shiftreg_8_out_45), .in_12(shiftreg_8_out_46), .in_5(shiftreg_8_out_39),
    .out_47(shiftreg_7_out_47), .out_48(shiftreg_7_out_48), .out_49(shiftreg_7_out_49),
    .out_50(shiftreg_7_out_50), .out_51(shiftreg_7_out_51), .out_52(shiftreg_7_out_52),
    .out_53(shiftreg_7_out_53), .out_54(shiftreg_7_out_54), .in_14(shiftreg_8_out_48),
    .in_15(shiftreg_8_out_49), .in_16(shiftreg_8_out_50), .in_17(shiftreg_8_out_51),
    .in_18(shiftreg_8_out_52), .in_19(shiftreg_8_out_53), .in_20(shiftreg_8_out_54),
    .out_55(shiftreg_7_out_55), .out_56(shiftreg_7_out_56), .out_57(shiftreg_7_out_57),
    .out_58(shiftreg_7_out_58), .out_59(shiftreg_7_out_59), .in_21(shiftreg_8_out_55),
    .in_22(shiftreg_8_out_56), .in_23(shiftreg_8_out_57), .in_24(shiftreg_8_out_58),
    .in_25(shiftreg_8_out_59), .out_60(shiftreg_7_out_60), .out_61(shiftreg_7_out_61),
    .in_26(shiftreg_8_out_60), .in_27(shiftreg_8_out_61), .out_62(shiftreg_7_out_62),
    .out_63(shiftreg_7_out_63), .in_28(shiftreg_8_out_62), .in_29(shiftreg_8_out_63),
    .out_64(shiftreg_7_out_64), .out_65(shiftreg_7_out_65), .out_66(shiftreg_7_out_66),
    .in_30(shiftreg_8_out_64), .in_31(shiftreg_8_out_65), .in_32(shiftreg_8_out_66),
    .out_67(shiftreg_7_out_67), .out_68(shiftreg_7_out_68), .out_69(shiftreg_7_out_69),
    .in_33(shiftreg_8_out_67), .in_34(shiftreg_8_out_68), .in_35(shiftreg_8_out_69), .clr(clr),
    .prev_clear(shiftreg_10_clear), .clear(shiftreg_7_clear));  // open: hide
  shiftreg shiftreg_8 (
    .clk(birds_1_birds_clk), .shift_in(shiftreg_11_shift_out), .shift_out(shiftreg_8_shift_out),
    .in_4(shiftreg_9_out_38), .out_38(shiftreg_8_out_38), .out_39(shiftreg_8_out_39),
    .in_13(shiftreg_9_out_47), .out_40(shiftreg_8_out_40), .in_6(shiftreg_9_out_40),
    .out_41(shiftreg_8_out_41), .in_7(shiftreg_9_out_41), .out_42(shiftreg_8_out_42),
    .in_8(shiftreg_9_out_42), .out_43(shiftreg_8_out_43), .out_44(shiftreg_8_out_44),
    .out_45(shiftreg_8_out_45), .out_46(shiftreg_8_out_46), .in_9(shiftreg_9_out_43),
    .in_10(shiftreg_9_out_44), .in_11(shiftreg_9_out_45), .in_12(shiftreg_9_out_46),
    .in_5(shiftreg_9_out_39), .out_47(shiftreg_8_out_47), .out_48(shiftreg_8_out_48),
    .out_49(shiftreg_8_out_49), .out_50(shiftreg_8_out_50), .out_51(shiftreg_8_out_51),
    .out_52(shiftreg_8_out_52), .out_53(shiftreg_8_out_53), .out_54(shiftreg_8_out_54),
    .in_14(shiftreg_9_out_48), .in_15(shiftreg_9_out_49), .in_16(shiftreg_9_out_50),
    .in_17(shiftreg_9_out_51), .in_18(shiftreg_9_out_52), .in_19(shiftreg_9_out_53),
    .in_20(shiftreg_9_out_54), .out_55(shiftreg_8_out_55), .out_56(shiftreg_8_out_56),
    .out_57(shiftreg_8_out_57), .out_58(shiftreg_8_out_58), .out_59(shiftreg_8_out_59),
    .in_21(shiftreg_9_out_55), .in_22(shiftreg_9_out_56), .in_23(shiftreg_9_out_57),
    .in_24(shiftreg_9_out_58), .in_25(shiftreg_9_out_59), .out_60(shiftreg_8_out_60),
    .out_61(shiftreg_8_out_61), .in_26(shiftreg_9_out_60), .in_27(shiftreg_9_out_61),
    .out_62(shiftreg_8_out_62), .out_63(shiftreg_8_out_63), .in_28(shiftreg_9_out_62),
    .in_29(shiftreg_9_out_63), .out_64(shiftreg_8_out_64), .out_65(shiftreg_8_out_65),
    .out_66(shiftreg_8_out_66), .in_30(shiftreg_9_out_64), .in_31(shiftreg_9_out_65),
    .in_32(shiftreg_9_out_66), .out_67(shiftreg_8_out_67), .out_68(shiftreg_8_out_68),
    .out_69(shiftreg_8_out_69), .in_33(shiftreg_9_out_67), .in_34(shiftreg_9_out_68),
    .in_35(shiftreg_9_out_69), .clr(clr), .prev_clear(shiftreg_11_clear), .clear(shiftreg_8_clear),
    .hide(t_ff_1_qn));
  shiftreg shiftreg_9 (
    .clk(birds_1_birds_clk), .shift_in(shiftreg_12_shift_out), .shift_out(shiftreg_9_shift_out),
    .out_38(shiftreg_9_out_38), .out_39(shiftreg_9_out_39), .out_40(shiftreg_9_out_40),
    .out_41(shiftreg_9_out_41), .out_42(shiftreg_9_out_42), .out_43(shiftreg_9_out_43),
    .out_44(shiftreg_9_out_44), .out_45(shiftreg_9_out_45), .out_46(shiftreg_9_out_46),
    .out_47(shiftreg_9_out_47), .out_48(shiftreg_9_out_48), .out_49(shiftreg_9_out_49),
    .out_50(shiftreg_9_out_50), .out_51(shiftreg_9_out_51), .out_52(shiftreg_9_out_52),
    .out_53(shiftreg_9_out_53), .out_54(shiftreg_9_out_54), .out_55(shiftreg_9_out_55),
    .out_56(shiftreg_9_out_56), .out_57(shiftreg_9_out_57), .out_58(shiftreg_9_out_58),
    .out_59(shiftreg_9_out_59), .out_60(shiftreg_9_out_60), .out_61(shiftreg_9_out_61),
    .out_62(shiftreg_9_out_62), .out_63(shiftreg_9_out_63), .out_64(shiftreg_9_out_64),
    .out_65(shiftreg_9_out_65), .out_66(shiftreg_9_out_66), .out_67(shiftreg_9_out_67),
    .out_68(shiftreg_9_out_68), .out_69(shiftreg_9_out_69), .clr(clr), .prev_clear(shiftreg_12_clear),
    .clear(shiftreg_9_clear), .hide(t_ff_1_q));  // open: in_4, in_13, in_6, in_7, in_8, in_9, in_10, in_11, in_12, in_5, in_14, in_15, in_16, in_17, in_18, in_19, in_20, in_21, in_22, in_23, in_24, in_25, in_26, in_27, in_28, in_29, in_30, in_31, in_32, in_33, in_34, in_35
  Clock #(.lowDuration(240)) clock_3 (.out(clock_3_out));
  and and_5 (and_5_out, stop, col);
  and and_6 (and_6_out, stop, ~col);  // AND_Gate
  shiftreg shiftreg_10 (
    .clk(clk), .shift_in(obstacles_1_out), .shift_out(shiftreg_10_shift_out), .in_4(shiftreg_11_out_38),
    .out_38(shiftreg_10_out_38), .out_39(shiftreg_10_out_39), .in_13(shiftreg_11_out_47),
    .out_40(shiftreg_10_out_40), .in_6(shiftreg_11_out_40), .out_41(shiftreg_10_out_41),
    .in_7(shiftreg_11_out_41), .out_42(shiftreg_10_out_42), .in_8(shiftreg_11_out_42),
    .out_43(shiftreg_10_out_43), .out_44(shiftreg_10_out_44), .out_45(shiftreg_10_out_45),
    .out_46(shiftreg_10_out_46), .in_9(shiftreg_11_out_43), .in_10(shiftreg_11_out_44),
    .in_11(shiftreg_11_out_45), .in_12(shiftreg_11_out_46), .in_5(shiftreg_11_out_39),
    .out_47(shiftreg_10_out_47), .out_48(shiftreg_10_out_48), .out_49(shiftreg_10_out_49),
    .out_50(shiftreg_10_out_50), .out_51(shiftreg_10_out_51), .out_52(shiftreg_10_out_52),
    .out_53(shiftreg_10_out_53), .out_54(shiftreg_10_out_54), .in_14(shiftreg_11_out_48),
    .in_15(shiftreg_11_out_49), .in_16(shiftreg_11_out_50), .in_17(shiftreg_11_out_51),
    .in_18(shiftreg_11_out_52), .in_19(shiftreg_11_out_53), .in_20(shiftreg_11_out_54),
    .out_55(shiftreg_10_out_55), .out_56(shiftreg_10_out_56), .out_57(shiftreg_10_out_57),
    .out_58(shiftreg_10_out_58), .out_59(shiftreg_10_out_59), .in_21(shiftreg_11_out_55),
    .in_22(shiftreg_11_out_56), .in_23(shiftreg_11_out_57), .in_24(shiftreg_11_out_58),
    .in_25(shiftreg_11_out_59), .out_60(shiftreg_10_out_60), .out_61(shiftreg_10_out_61),
    .in_26(shiftreg_11_out_60), .in_27(shiftreg_11_out_61), .out_62(shiftreg_10_out_62),
    .out_63(shiftreg_10_out_63), .in_28(shiftreg_11_out_62), .in_29(shiftreg_11_out_63),
    .out_64(shiftreg_10_out_64), .out_65(shiftreg_10_out_65), .out_66(shiftreg_10_out_66),
    .in_30(shiftreg_11_out_64), .in_31(shiftreg_11_out_65), .in_32(shiftreg_11_out_66),
    .out_67(shiftreg_10_out_67), .out_68(shiftreg_10_out_68), .out_69(shiftreg_10_out_69),
    .in_33(shiftreg_11_out_67), .in_34(shiftreg_11_out_68), .in_35(shiftreg_11_out_69), .clr(clr),
    .clear(shiftreg_10_clear));  // open: prev_clear, hide
  shiftreg shiftreg_11 (
    .clk(birds_1_birds_clk), .shift_in(birds_1_up), .shift_out(shiftreg_11_shift_out),
    .in_4(shiftreg_12_out_38), .out_38(shiftreg_11_out_38), .out_39(shiftreg_11_out_39),
    .in_13(shiftreg_12_out_47), .out_40(shiftreg_11_out_40), .in_6(shiftreg_12_out_40),
    .out_41(shiftreg_11_out_41), .in_7(shiftreg_12_out_41), .out_42(shiftreg_11_out_42),
    .in_8(shiftreg_12_out_42), .out_43(shiftreg_11_out_43), .out_44(shiftreg_11_out_44),
    .out_45(shiftreg_11_out_45), .out_46(shiftreg_11_out_46), .in_9(shiftreg_12_out_43),
    .in_10(shiftreg_12_out_44), .in_11(shiftreg_12_out_45), .in_12(shiftreg_12_out_46),
    .in_5(shiftreg_12_out_39), .out_47(shiftreg_11_out_47), .out_48(shiftreg_11_out_48),
    .out_49(shiftreg_11_out_49), .out_50(shiftreg_11_out_50), .out_51(shiftreg_11_out_51),
    .out_52(shiftreg_11_out_52), .out_53(shiftreg_11_out_53), .out_54(shiftreg_11_out_54),
    .in_14(shiftreg_12_out_48), .in_15(shiftreg_12_out_49), .in_16(shiftreg_12_out_50),
    .in_17(shiftreg_12_out_51), .in_18(shiftreg_12_out_52), .in_19(shiftreg_12_out_53),
    .in_20(shiftreg_12_out_54), .out_55(shiftreg_11_out_55), .out_56(shiftreg_11_out_56),
    .out_57(shiftreg_11_out_57), .out_58(shiftreg_11_out_58), .out_59(shiftreg_11_out_59),
    .in_21(shiftreg_12_out_55), .in_22(shiftreg_12_out_56), .in_23(shiftreg_12_out_57),
    .in_24(shiftreg_12_out_58), .in_25(shiftreg_12_out_59), .out_60(shiftreg_11_out_60),
    .out_61(shiftreg_11_out_61), .in_26(shiftreg_12_out_60), .in_27(shiftreg_12_out_61),
    .out_62(shiftreg_11_out_62), .out_63(shiftreg_11_out_63), .in_28(shiftreg_12_out_62),
    .in_29(shiftreg_12_out_63), .out_64(shiftreg_11_out_64), .out_65(shiftreg_11_out_65),
    .out_66(shiftreg_11_out_66), .in_30(shiftreg_12_out_64), .in_31(shiftreg_12_out_65),
    .in_32(shiftreg_12_out_66), .out_67(shiftreg_11_out_67), .out_68(shiftreg_11_out_68),
    .out_69(shiftreg_11_out_69), .in_33(shiftreg_12_out_67), .in_34(shiftreg_12_out_68),
    .in_35(shiftreg_12_out_69), .clr(clr), .clear(shiftreg_11_clear), .hide(t_ff_1_qn));  // open: prev_clear
  shiftreg shiftreg_12 (
    .clk(birds_1_birds_clk), .shift_in(birds_1_down), .shift_out(shiftreg_12_shift_out),
    .out_38(shiftreg_12_out_38), .out_39(shiftreg_12_out_39), .out_40(shiftreg_12_out_40),
    .out_41(shiftreg_12_out_41), .out_42(shiftreg_12_out_42), .out_43(shiftreg_12_out_43),
    .out_44(shiftreg_12_out_44), .out_45(shiftreg_12_out_45), .out_46(shiftreg_12_out_46),
    .out_47(shiftreg_12_out_47), .out_48(shiftreg_12_out_48), .out_49(shiftreg_12_out_49),
    .out_50(shiftreg_12_out_50), .out_51(shiftreg_12_out_51), .out_52(shiftreg_12_out_52),
    .out_53(shiftreg_12_out_53), .out_54(shiftreg_12_out_54), .out_55(shiftreg_12_out_55),
    .out_56(shiftreg_12_out_56), .out_57(shiftreg_12_out_57), .out_58(shiftreg_12_out_58),
    .out_59(shiftreg_12_out_59), .out_60(shiftreg_12_out_60), .out_61(shiftreg_12_out_61),
    .out_62(shiftreg_12_out_62), .out_63(shiftreg_12_out_63), .out_64(shiftreg_12_out_64),
    .out_65(shiftreg_12_out_65), .out_66(shiftreg_12_out_66), .out_67(shiftreg_12_out_67),
    .out_68(shiftreg_12_out_68), .out_69(shiftreg_12_out_69), .clr(clr), .clear(shiftreg_12_clear),
    .hide(t_ff_1_q));  // open: in_4, in_13, in_6, in_7, in_8, in_9, in_10, in_11, in_12, in_5, in_14, in_15, in_16, in_17, in_18, in_19, in_20, in_21, in_22, in_23, in_24, in_25, in_26, in_27, in_28, in_29, in_30, in_31, in_32, in_33, in_34, in_35, prev_clear
  T_Flip_Flop t_ff_1 (
    .clk(clock_3_out), .T(1'b1), .Q(t_ff_1_q), .Qn(t_ff_1_qn), .en(not_5_out));  // open: preset, reset
  not not_5 (not_5_out, stop);
  obstacles obstacles_1 (.clk(clk), .gen_obst(random_spawn_1_spawn_cactus), .out(obstacles_1_out));
  birds birds_1 (
    .birds_clk(birds_1_birds_clk), .up(birds_1_up), .down(birds_1_down),
    .gen_obst(random_spawn_1_spawn_bird), .pause(stop), .speed(speed));
  random_spawn random_spawn_1 (
    .clk(clk), .spawn_bird(random_spawn_1_spawn_bird), .spawn_cactus(random_spawn_1_spawn_cactus),
    .allow(shiftreg_3_clear), .level(speed));

  // Other names for the same wires on the sheet: kboard = clk_cdm

  // Notes on the sheet:
  //   LEVELS
  //   CACTUSES LINE
  //   BIRDS LINE
endmodule
module shiftreg (
  input  clk,
  input  clr,
  input  hide,
  input  [31:0] in_4,
  input  [31:0] in_5,
  input  [31:0] in_6,
  input  [31:0] in_7,
  input  [31:0] in_8,
  input  [31:0] in_9,
  input  [31:0] in_10,
  input  [31:0] in_11,
  input  [31:0] in_12,
  input  [31:0] in_13,
  input  [31:0] in_14,
  input  [31:0] in_15,
  input  [31:0] in_16,
  input  [31:0] in_17,
  input  [31:0] in_18,
  input  [31:0] in_19,
  input  [31:0] in_20,
  input  [31:0] in_21,
  input  [31:0] in_22,
  input  [31:0] in_23,
  input  [31:0] in_24,
  input  [31:0] in_25,
  input  [31:0] in_26,
  input  [31:0] in_27,
  input  [31:0] in_28,
  input  [31:0] in_29,
  input  [31:0] in_30,
  input  [31:0] in_31,
  input  [31:0] in_32,
  input  [31:0] in_33,
  input  [31:0] in_34,
  input  [31:0] in_35,
  input  [31:0] shift_in,
  input  prev_clear,
  output [31:0] out_38,
  output [31:0] out_39,
  output [31:0] out_40,
  output [31:0] out_41,
  output [31:0] out_42,
  output [31:0] out_43,
  output [31:0] out_44,
  output [31:0] out_45,
  output [31:0] out_46,
  output [31:0] out_47,
  output [31:0] out_48,
  output [31:0] out_49,
  output [31:0] out_50,
  output [31:0] out_51,
  output [31:0] out_52,
  output [31:0] out_53,
  output [31:0] out_54,
  output [31:0] out_55,
  output [31:0] out_56,
  output [31:0] out_57,
  output [31:0] out_58,
  output [31:0] out_59,
  output [31:0] out_60,
  output [31:0] out_61,
  output [31:0] out_62,
  output [31:0] out_63,
  output [31:0] out_64,
  output [31:0] out_65,
  output [31:0] out_66,
  output [31:0] out_67,
  output [31:0] out_68,
  output [31:0] out_69,
  output [31:0] shift_out,
  output clear
);

  wire nor_1_out, show;
  wire [31:0] or_1_out, or_2_out, or_3_out, or_4_out, or_5_out, or_6_out, or_7_out, or_8_out, or_9_out,
       or_10_out, or_11_out, or_12_out, or_13_out, or_14_out, or_15_out, or_16_out, or_17_out, or_18_out,
       or_19_out, or_20_out, or_21_out, or_22_out, or_23_out, or_24_out, or_25_out, or_26_out, or_27_out,
       or_28_out, or_29_out, or_30_out, or_31_out, or_32_out, or_33_out, or_34_out, or_35_out, or_36_out,
       or_37_out, or_38_out, or_39_out, or_40_out, or_41_out, or_42_out, or_43_out, or_44_out, or_45_out,
       or_46_out, or_47_out, or_48_out, or_49_out, or_50_out, or_51_out, or_52_out, or_53_out, or_54_out,
       or_55_out, or_56_out, or_57_out, or_58_out, or_59_out, or_60_out, or_61_out, or_62_out, or_63_out,
       or_64_out, or_65_out, or_66_out, or_67_out, or_68_out, or_69_out, or_70_out, or_71_out, or_72_out,
       or_73_out, or_74_out, or_75_out, or_76_out, or_77_out, or_78_out, or_79_out, or_80_out, or_81_out,
       or_82_out, or_83_out, or_84_out, or_85_out, or_86_out, or_87_out, or_88_out, or_89_out, or_90_out,
       or_91_out, or_92_out, or_93_out, or_94_out, or_95_out, pull_resistor_3_node, pull_resistor_5_node,
       pull_resistor_7_node, pull_resistor_9_node, pull_resistor_11_node, pull_resistor_13_node,
       pull_resistor_15_node, pull_resistor_17_node, pull_resistor_19_node, pull_resistor_21_node,
       pull_resistor_23_node, pull_resistor_25_node, pull_resistor_27_node, pull_resistor_29_node,
       pull_resistor_31_node, pull_resistor_33_node, pull_resistor_35_node, pull_resistor_37_node,
       pull_resistor_39_node, pull_resistor_41_node, pull_resistor_43_node, pull_resistor_45_node,
       pull_resistor_47_node, pull_resistor_49_node, pull_resistor_51_node, pull_resistor_53_node,
       pull_resistor_55_node, pull_resistor_57_node, pull_resistor_59_node, pull_resistor_61_node,
       pull_resistor_63_node, pull_resistor_65_node, register_1_q, register_2_q, register_3_q, register_4_q,
       register_5_q, register_6_q, register_7_q, register_8_q, register_9_q, register_10_q, register_11_q,
       register_12_q, register_13_q, register_14_q, register_15_q, register_16_q, register_17_q,
       register_18_q, register_19_q, register_20_q, register_21_q, register_22_q, register_23_q,
       register_24_q, register_25_q, register_26_q, register_27_q, register_28_q, register_29_q,
       register_30_q, register_31_q;

  Pull_Resistor pull_resistor_1 (.node(hide));
  not not_1 (show, hide);
  Pull_Resistor pull_resistor_2 (.node(in_4));
  Pull_Resistor pull_resistor_3 (.node(pull_resistor_3_node));
  assign pull_resistor_3_node = show ? register_1_q : 32'bz;  // Controlled_Buffer controlled_buffer_1
  Register #(.width(32)) register_1 (.D(shift_in), .en(1'b1), .Q(register_1_q), .clk(clk), .clr(clr));
  assign or_1_out = register_1_q | in_4;  // OR_Gate or_1, 32 bits wide
  assign or_2_out = in_4 | pull_resistor_3_node;  // OR_Gate or_2, 32 bits wide
  Multiplexer #(.width(32), .enable("false")) multiplexer_1 (
    .in0(register_1_q), .in1(or_2_out), .out(out_38), .sel(1'b1));
  Register #(.width(32)) register_2 (.D(register_1_q), .en(1'b1), .Q(register_2_q), .clk(clk), .clr(clr));
  Pull_Resistor pull_resistor_4 (.node(in_5));
  Pull_Resistor pull_resistor_5 (.node(pull_resistor_5_node));
  assign pull_resistor_5_node = show ? register_2_q : 32'bz;  // Controlled_Buffer controlled_buffer_2
  assign or_3_out = register_2_q | in_5;  // OR_Gate or_3, 32 bits wide
  assign or_4_out = or_3_out | or_1_out;  // OR_Gate or_4, 32 bits wide
  Multiplexer #(.width(32), .enable("false")) multiplexer_2 (
    .in0(register_2_q), .in1(or_5_out), .out(out_39), .sel(1'b1));
  assign or_5_out = in_5 | pull_resistor_5_node;  // OR_Gate or_5, 32 bits wide
  Register #(.width(32)) register_3 (.D(register_2_q), .en(1'b1), .Q(register_3_q), .clk(clk), .clr(clr));
  assign or_6_out = register_3_q | in_6;  // OR_Gate or_6, 32 bits wide
  assign or_7_out = in_6 | pull_resistor_7_node;  // OR_Gate or_7, 32 bits wide
  Pull_Resistor pull_resistor_6 (.node(in_6));
  Pull_Resistor pull_resistor_7 (.node(pull_resistor_7_node));
  assign pull_resistor_7_node = show ? register_3_q : 32'bz;  // Controlled_Buffer controlled_buffer_3
  assign or_8_out = or_6_out | or_4_out;  // OR_Gate or_8, 32 bits wide
  Multiplexer #(.width(32), .enable("false")) multiplexer_3 (
    .in0(register_3_q), .in1(or_7_out), .out(out_40), .sel(1'b1));
  Pull_Resistor pull_resistor_8 (.node(in_7));
  Pull_Resistor pull_resistor_9 (.node(pull_resistor_9_node));
  assign pull_resistor_9_node = show ? register_4_q : 32'bz;  // Controlled_Buffer controlled_buffer_4
  Register #(.width(32)) register_4 (.D(register_3_q), .en(1'b1), .Q(register_4_q), .clk(clk), .clr(clr));
  assign or_9_out = register_4_q | in_7;  // OR_Gate or_9, 32 bits wide
  Multiplexer #(.width(32), .enable("false")) multiplexer_4 (
    .in0(register_4_q), .in1(or_10_out), .out(out_41), .sel(1'b1));
  assign or_10_out = in_7 | pull_resistor_9_node;  // OR_Gate or_10, 32 bits wide
  assign or_11_out = or_9_out | or_8_out;  // OR_Gate or_11, 32 bits wide
  Register #(.width(32)) register_5 (.D(register_4_q), .en(1'b1), .Q(register_5_q), .clk(clk), .clr(clr));
  assign or_12_out = in_8 | pull_resistor_11_node;  // OR_Gate or_12, 32 bits wide
  Pull_Resistor pull_resistor_10 (.node(in_8));
  Pull_Resistor pull_resistor_11 (.node(pull_resistor_11_node));
  assign pull_resistor_11_node = show ? register_5_q : 32'bz;  // Controlled_Buffer controlled_buffer_5
  assign or_13_out = register_5_q | in_8;  // OR_Gate or_13, 32 bits wide
  assign or_14_out = or_13_out | or_11_out;  // OR_Gate or_14, 32 bits wide
  Multiplexer #(.width(32), .enable("false")) multiplexer_5 (
    .in0(register_5_q), .in1(or_12_out), .out(out_42), .sel(1'b1));
  Pull_Resistor pull_resistor_12 (.node(in_9));
  Register #(.width(32)) register_6 (.D(register_5_q), .en(1'b1), .Q(register_6_q), .clk(clk), .clr(clr));
  assign or_15_out = register_6_q | in_9;  // OR_Gate or_15, 32 bits wide
  assign or_16_out = in_9 | pull_resistor_13_node;  // OR_Gate or_16, 32 bits wide
  Pull_Resistor pull_resistor_13 (.node(pull_resistor_13_node));
  assign pull_resistor_13_node = show ? register_6_q : 32'bz;  // Controlled_Buffer controlled_buffer_6
  assign or_17_out = or_15_out | or_14_out;  // OR_Gate or_17, 32 bits wide
  Multiplexer #(.width(32), .enable("false")) multiplexer_6 (
    .in0(register_6_q), .in1(or_16_out), .out(out_43), .sel(1'b1));
  Register #(.width(32)) register_7 (.D(register_6_q), .en(1'b1), .Q(register_7_q), .clk(clk), .clr(clr));
  Pull_Resistor pull_resistor_14 (.node(in_10));
  Pull_Resistor pull_resistor_15 (.node(pull_resistor_15_node));
  assign pull_resistor_15_node = show ? register_7_q : 32'bz;  // Controlled_Buffer controlled_buffer_7
  assign or_18_out = register_7_q | in_10;  // OR_Gate or_18, 32 bits wide
  assign or_19_out = or_18_out | or_17_out;  // OR_Gate or_19, 32 bits wide
  Multiplexer #(.width(32), .enable("false")) multiplexer_7 (
    .in0(register_7_q), .in1(or_20_out), .out(out_44), .sel(1'b1));
  assign or_20_out = in_10 | pull_resistor_15_node;  // OR_Gate or_20, 32 bits wide
  Register #(.width(32)) register_8 (.D(register_7_q), .en(1'b1), .Q(register_8_q), .clk(clk), .clr(clr));
  assign or_21_out = in_11 | pull_resistor_17_node;  // OR_Gate or_21, 32 bits wide
  Pull_Resistor pull_resistor_16 (.node(in_11));
  Pull_Resistor pull_resistor_17 (.node(pull_resistor_17_node));
  assign pull_resistor_17_node = show ? register_8_q : 32'bz;  // Controlled_Buffer controlled_buffer_8
  assign or_22_out = register_8_q | in_11;  // OR_Gate or_22, 32 bits wide
  assign or_23_out = or_22_out | or_19_out;  // OR_Gate or_23, 32 bits wide
  Multiplexer #(.width(32), .enable("false")) multiplexer_8 (
    .in0(register_8_q), .in1(or_21_out), .out(out_45), .sel(1'b1));
  Pull_Resistor pull_resistor_18 (.node(in_12));
  Pull_Resistor pull_resistor_19 (.node(pull_resistor_19_node));
  assign pull_resistor_19_node = show ? register_9_q : 32'bz;  // Controlled_Buffer controlled_buffer_9
  Register #(.width(32)) register_9 (.D(register_8_q), .en(1'b1), .Q(register_9_q), .clk(clk), .clr(clr));
  assign or_24_out = register_9_q | in_12;  // OR_Gate or_24, 32 bits wide
  assign or_25_out = in_12 | pull_resistor_19_node;  // OR_Gate or_25, 32 bits wide
  assign or_26_out = or_24_out | or_23_out;  // OR_Gate or_26, 32 bits wide
  Multiplexer #(.width(32), .enable("false")) multiplexer_9 (
    .in0(register_9_q), .in1(or_25_out), .out(out_46), .sel(1'b1));
  Register #(.width(32)) register_10 (.D(register_9_q), .en(1'b1), .Q(register_10_q), .clk(clk), .clr(clr));
  Pull_Resistor pull_resistor_20 (.node(in_13));
  Pull_Resistor pull_resistor_21 (.node(pull_resistor_21_node));
  assign pull_resistor_21_node = show ? register_10_q : 32'bz;  // Controlled_Buffer controlled_buffer_10
  assign or_27_out = register_10_q | in_13;  // OR_Gate or_27, 32 bits wide
  assign or_28_out = or_27_out | or_26_out;  // OR_Gate or_28, 32 bits wide
  Multiplexer #(.width(32), .enable("false")) multiplexer_10 (
    .in0(register_10_q), .in1(or_29_out), .out(out_47), .sel(1'b1));
  assign or_29_out = in_13 | pull_resistor_21_node;  // OR_Gate or_29, 32 bits wide
  Register #(.width(32)) register_11 (.D(register_10_q), .en(1'b1), .Q(register_11_q), .clk(clk), .clr(clr));
  assign or_30_out = register_11_q | in_14;  // OR_Gate or_30, 32 bits wide
  Pull_Resistor pull_resistor_22 (.node(in_14));
  assign or_31_out = in_14 | pull_resistor_23_node;  // OR_Gate or_31, 32 bits wide
  Pull_Resistor pull_resistor_23 (.node(pull_resistor_23_node));
  assign pull_resistor_23_node = show ? register_11_q : 32'bz;  // Controlled_Buffer controlled_buffer_11
  assign or_32_out = or_30_out | or_28_out;  // OR_Gate or_32, 32 bits wide
  Multiplexer #(.width(32), .enable("false")) multiplexer_11 (
    .in0(register_11_q), .in1(or_31_out), .out(out_48), .sel(1'b1));
  Pull_Resistor pull_resistor_24 (.node(in_15));
  Pull_Resistor pull_resistor_25 (.node(pull_resistor_25_node));
  assign pull_resistor_25_node = show ? register_12_q : 32'bz;  // Controlled_Buffer controlled_buffer_12
  Register #(.width(32)) register_12 (.D(register_11_q), .en(1'b1), .Q(register_12_q), .clk(clk), .clr(clr));
  assign or_33_out = register_12_q | in_15;  // OR_Gate or_33, 32 bits wide
  Multiplexer #(.width(32), .enable("false")) multiplexer_12 (
    .in0(register_12_q), .in1(or_34_out), .out(out_49), .sel(1'b1));
  assign or_34_out = in_15 | pull_resistor_25_node;  // OR_Gate or_34, 32 bits wide
  assign or_35_out = or_33_out | or_32_out;  // OR_Gate or_35, 32 bits wide
  Register #(.width(32)) register_13 (.D(register_12_q), .en(1'b1), .Q(register_13_q), .clk(clk), .clr(clr));
  Pull_Resistor pull_resistor_26 (.node(in_16));
  assign or_36_out = in_16 | pull_resistor_27_node;  // OR_Gate or_36, 32 bits wide
  Pull_Resistor pull_resistor_27 (.node(pull_resistor_27_node));
  assign pull_resistor_27_node = show ? register_13_q : 32'bz;  // Controlled_Buffer controlled_buffer_13
  assign or_37_out = register_13_q | in_16;  // OR_Gate or_37, 32 bits wide
  assign or_38_out = or_37_out | or_35_out;  // OR_Gate or_38, 32 bits wide
  Multiplexer #(.width(32), .enable("false")) multiplexer_13 (
    .in0(register_13_q), .in1(or_36_out), .out(out_50), .sel(1'b1));
  Pull_Resistor pull_resistor_28 (.node(in_17));
  Register #(.width(32)) register_14 (.D(register_13_q), .en(1'b1), .Q(register_14_q), .clk(clk), .clr(clr));
  assign or_39_out = register_14_q | in_17;  // OR_Gate or_39, 32 bits wide
  assign or_40_out = in_17 | pull_resistor_29_node;  // OR_Gate or_40, 32 bits wide
  Pull_Resistor pull_resistor_29 (.node(pull_resistor_29_node));
  assign pull_resistor_29_node = show ? register_14_q : 32'bz;  // Controlled_Buffer controlled_buffer_14
  assign or_41_out = or_39_out | or_38_out;  // OR_Gate or_41, 32 bits wide
  Multiplexer #(.width(32), .enable("false")) multiplexer_14 (
    .in0(register_14_q), .in1(or_40_out), .out(out_51), .sel(1'b1));
  Register #(.width(32)) register_15 (.D(register_14_q), .en(1'b1), .Q(register_15_q), .clk(clk), .clr(clr));
  Pull_Resistor pull_resistor_30 (.node(in_18));
  Pull_Resistor pull_resistor_31 (.node(pull_resistor_31_node));
  assign pull_resistor_31_node = show ? register_15_q : 32'bz;  // Controlled_Buffer controlled_buffer_15
  assign or_42_out = register_15_q | in_18;  // OR_Gate or_42, 32 bits wide
  assign or_43_out = or_42_out | or_41_out;  // OR_Gate or_43, 32 bits wide
  Multiplexer #(.width(32), .enable("false")) multiplexer_15 (
    .in0(register_15_q), .in1(or_44_out), .out(out_52), .sel(1'b1));
  assign or_44_out = in_18 | pull_resistor_31_node;  // OR_Gate or_44, 32 bits wide
  Register #(.width(32)) register_16 (.D(register_15_q), .en(1'b1), .Q(register_16_q), .clk(clk), .clr(clr));
  assign or_45_out = in_19 | pull_resistor_33_node;  // OR_Gate or_45, 32 bits wide
  Pull_Resistor pull_resistor_32 (.node(in_19));
  Pull_Resistor pull_resistor_33 (.node(pull_resistor_33_node));
  assign pull_resistor_33_node = show ? register_16_q : 32'bz;  // Controlled_Buffer controlled_buffer_16
  assign or_46_out = register_16_q | in_19;  // OR_Gate or_46, 32 bits wide
  assign or_47_out = or_46_out | or_43_out;  // OR_Gate or_47, 32 bits wide
  Multiplexer #(.width(32), .enable("false")) multiplexer_16 (
    .in0(register_16_q), .in1(or_45_out), .out(out_53), .sel(1'b1));
  Pull_Resistor pull_resistor_34 (.node(in_20));
  Pull_Resistor pull_resistor_35 (.node(pull_resistor_35_node));
  assign pull_resistor_35_node = show ? register_17_q : 32'bz;  // Controlled_Buffer controlled_buffer_17
  Register #(.width(32)) register_17 (.D(register_16_q), .en(1'b1), .Q(register_17_q), .clk(clk), .clr(clr));
  assign or_48_out = register_17_q | in_20;  // OR_Gate or_48, 32 bits wide
  assign or_49_out = in_20 | pull_resistor_35_node;  // OR_Gate or_49, 32 bits wide
  assign or_50_out = or_48_out | or_47_out;  // OR_Gate or_50, 32 bits wide
  Multiplexer #(.width(32), .enable("false")) multiplexer_17 (
    .in0(register_17_q), .in1(or_49_out), .out(out_54), .sel(1'b1));
  Register #(.width(32)) register_18 (.D(register_17_q), .en(1'b1), .Q(register_18_q), .clk(clk), .clr(clr));
  Pull_Resistor pull_resistor_36 (.node(in_21));
  Pull_Resistor pull_resistor_37 (.node(pull_resistor_37_node));
  assign pull_resistor_37_node = show ? register_18_q : 32'bz;  // Controlled_Buffer controlled_buffer_18
  assign or_51_out = register_18_q | in_21;  // OR_Gate or_51, 32 bits wide
  assign or_52_out = or_51_out | or_50_out;  // OR_Gate or_52, 32 bits wide
  Multiplexer #(.width(32), .enable("false")) multiplexer_18 (
    .in0(register_18_q), .in1(or_53_out), .out(out_55), .sel(1'b1));
  assign or_53_out = in_21 | pull_resistor_37_node;  // OR_Gate or_53, 32 bits wide
  Register #(.width(32)) register_19 (.D(register_18_q), .en(1'b1), .Q(register_19_q), .clk(clk), .clr(clr));
  assign or_54_out = register_19_q | in_22;  // OR_Gate or_54, 32 bits wide
  assign or_55_out = in_22 | pull_resistor_39_node;  // OR_Gate or_55, 32 bits wide
  Pull_Resistor pull_resistor_38 (.node(in_22));
  Pull_Resistor pull_resistor_39 (.node(pull_resistor_39_node));
  assign pull_resistor_39_node = show ? register_19_q : 32'bz;  // Controlled_Buffer controlled_buffer_19
  assign or_56_out = or_54_out | or_52_out;  // OR_Gate or_56, 32 bits wide
  Multiplexer #(.width(32), .enable("false")) multiplexer_19 (
    .in0(register_19_q), .in1(or_55_out), .out(out_56), .sel(1'b1));
  Pull_Resistor pull_resistor_40 (.node(in_23));
  Pull_Resistor pull_resistor_41 (.node(pull_resistor_41_node));
  assign pull_resistor_41_node = show ? register_20_q : 32'bz;  // Controlled_Buffer controlled_buffer_20
  Register #(.width(32)) register_20 (.D(register_19_q), .en(1'b1), .Q(register_20_q), .clk(clk), .clr(clr));
  assign or_57_out = register_20_q | in_23;  // OR_Gate or_57, 32 bits wide
  Multiplexer #(.width(32), .enable("false")) multiplexer_20 (
    .in0(register_20_q), .in1(or_58_out), .out(out_57), .sel(1'b1));
  assign or_58_out = in_23 | pull_resistor_41_node;  // OR_Gate or_58, 32 bits wide
  assign or_59_out = or_57_out | or_56_out;  // OR_Gate or_59, 32 bits wide
  Register #(.width(32)) register_21 (.D(register_20_q), .en(1'b1), .Q(register_21_q), .clk(clk), .clr(clr));
  assign or_60_out = in_24 | pull_resistor_43_node;  // OR_Gate or_60, 32 bits wide
  Pull_Resistor pull_resistor_42 (.node(in_24));
  Pull_Resistor pull_resistor_43 (.node(pull_resistor_43_node));
  assign pull_resistor_43_node = show ? register_21_q : 32'bz;  // Controlled_Buffer controlled_buffer_21
  assign or_61_out = register_21_q | in_24;  // OR_Gate or_61, 32 bits wide
  assign or_62_out = or_61_out | or_59_out;  // OR_Gate or_62, 32 bits wide
  Multiplexer #(.width(32), .enable("false")) multiplexer_21 (
    .in0(register_21_q), .in1(or_60_out), .out(out_58), .sel(1'b1));
  Pull_Resistor pull_resistor_44 (.node(in_25));
  Register #(.width(32)) register_22 (.D(register_21_q), .en(1'b1), .Q(register_22_q), .clk(clk), .clr(clr));
  assign or_63_out = register_22_q | in_25;  // OR_Gate or_63, 32 bits wide
  assign or_64_out = in_25 | pull_resistor_45_node;  // OR_Gate or_64, 32 bits wide
  Pull_Resistor pull_resistor_45 (.node(pull_resistor_45_node));
  assign pull_resistor_45_node = show ? register_22_q : 32'bz;  // Controlled_Buffer controlled_buffer_22
  assign or_65_out = or_63_out | or_62_out;  // OR_Gate or_65, 32 bits wide
  Multiplexer #(.width(32), .enable("false")) multiplexer_22 (
    .in0(register_22_q), .in1(or_64_out), .out(out_59), .sel(1'b1));
  Register #(.width(32)) register_23 (.D(register_22_q), .en(1'b1), .Q(register_23_q), .clk(clk), .clr(clr));
  Pull_Resistor pull_resistor_46 (.node(in_26));
  Pull_Resistor pull_resistor_47 (.node(pull_resistor_47_node));
  assign pull_resistor_47_node = show ? register_23_q : 32'bz;  // Controlled_Buffer controlled_buffer_23
  assign or_66_out = register_23_q | in_26;  // OR_Gate or_66, 32 bits wide
  assign or_67_out = or_66_out | or_65_out;  // OR_Gate or_67, 32 bits wide
  Multiplexer #(.width(32), .enable("false")) multiplexer_23 (
    .in0(register_23_q), .in1(or_68_out), .out(out_60), .sel(1'b1));
  assign or_68_out = in_26 | pull_resistor_47_node;  // OR_Gate or_68, 32 bits wide
  Register #(.width(32)) register_24 (.D(register_23_q), .en(1'b1), .Q(register_24_q), .clk(clk), .clr(clr));
  Pull_Resistor pull_resistor_48 (.node(in_27));
  assign or_69_out = in_27 | pull_resistor_49_node;  // OR_Gate or_69, 32 bits wide
  Pull_Resistor pull_resistor_49 (.node(pull_resistor_49_node));
  assign pull_resistor_49_node = show ? register_24_q : 32'bz;  // Controlled_Buffer controlled_buffer_24
  assign or_70_out = register_24_q | in_27;  // OR_Gate or_70, 32 bits wide
  assign or_71_out = or_70_out | or_67_out;  // OR_Gate or_71, 32 bits wide
  Multiplexer #(.width(32), .enable("false")) multiplexer_24 (
    .in0(register_24_q), .in1(or_69_out), .out(out_61), .sel(1'b1));
  Pull_Resistor pull_resistor_50 (.node(in_28));
  Pull_Resistor pull_resistor_51 (.node(pull_resistor_51_node));
  assign pull_resistor_51_node = show ? register_25_q : 32'bz;  // Controlled_Buffer controlled_buffer_25
  Register #(.width(32)) register_25 (.D(register_24_q), .en(1'b1), .Q(register_25_q), .clk(clk), .clr(clr));
  assign or_72_out = register_25_q | in_28;  // OR_Gate or_72, 32 bits wide
  assign or_73_out = in_28 | pull_resistor_51_node;  // OR_Gate or_73, 32 bits wide
  assign or_74_out = or_72_out | or_71_out;  // OR_Gate or_74, 32 bits wide
  Multiplexer #(.width(32), .enable("false")) multiplexer_25 (
    .in0(register_25_q), .in1(or_73_out), .out(out_62), .sel(1'b1));
  Register #(.width(32)) register_26 (.D(register_25_q), .en(1'b1), .Q(register_26_q), .clk(clk), .clr(clr));
  Pull_Resistor pull_resistor_52 (.node(in_29));
  Pull_Resistor pull_resistor_53 (.node(pull_resistor_53_node));
  assign pull_resistor_53_node = show ? register_26_q : 32'bz;  // Controlled_Buffer controlled_buffer_26
  assign or_75_out = register_26_q | in_29;  // OR_Gate or_75, 32 bits wide
  assign or_76_out = or_75_out | or_74_out;  // OR_Gate or_76, 32 bits wide
  Multiplexer #(.width(32), .enable("false")) multiplexer_26 (
    .in0(register_26_q), .in1(or_77_out), .out(out_63), .sel(1'b1));
  assign or_77_out = in_29 | pull_resistor_53_node;  // OR_Gate or_77, 32 bits wide
  Register #(.width(32)) register_27 (.D(register_26_q), .en(1'b1), .Q(register_27_q), .clk(clk), .clr(clr));
  assign or_78_out = register_27_q | in_30;  // OR_Gate or_78, 32 bits wide
  Pull_Resistor pull_resistor_54 (.node(in_30));
  assign or_79_out = in_30 | pull_resistor_55_node;  // OR_Gate or_79, 32 bits wide
  Pull_Resistor pull_resistor_55 (.node(pull_resistor_55_node));
  assign pull_resistor_55_node = show ? register_27_q : 32'bz;  // Controlled_Buffer controlled_buffer_27
  assign or_80_out = or_78_out | or_76_out;  // OR_Gate or_80, 32 bits wide
  Multiplexer #(.width(32), .enable("false")) multiplexer_27 (
    .in0(register_27_q), .in1(or_79_out), .out(out_64), .sel(1'b1));
  Pull_Resistor pull_resistor_56 (.node(in_31));
  Pull_Resistor pull_resistor_57 (.node(pull_resistor_57_node));
  assign pull_resistor_57_node = show ? register_28_q : 32'bz;  // Controlled_Buffer controlled_buffer_28
  Register #(.width(32)) register_28 (.D(register_27_q), .en(1'b1), .Q(register_28_q), .clk(clk), .clr(clr));
  assign or_81_out = register_28_q | in_31;  // OR_Gate or_81, 32 bits wide
  Multiplexer #(.width(32), .enable("false")) multiplexer_28 (
    .in0(register_28_q), .in1(or_82_out), .out(out_65), .sel(1'b1));
  assign or_82_out = in_31 | pull_resistor_57_node;  // OR_Gate or_82, 32 bits wide
  assign or_83_out = or_81_out | or_80_out;  // OR_Gate or_83, 32 bits wide
  Register #(.width(32)) register_29 (.D(register_28_q), .en(1'b1), .Q(register_29_q), .clk(clk), .clr(clr));
  Pull_Resistor pull_resistor_58 (.node(in_32));
  assign or_84_out = in_32 | pull_resistor_59_node;  // OR_Gate or_84, 32 bits wide
  Pull_Resistor pull_resistor_59 (.node(pull_resistor_59_node));
  assign pull_resistor_59_node = show ? register_29_q : 32'bz;  // Controlled_Buffer controlled_buffer_29
  assign or_85_out = register_29_q | in_32;  // OR_Gate or_85, 32 bits wide
  assign or_86_out = or_85_out | or_83_out;  // OR_Gate or_86, 32 bits wide
  Multiplexer #(.width(32), .enable("false")) multiplexer_29 (
    .in0(register_29_q), .in1(or_84_out), .out(out_66), .sel(1'b1));
  Pull_Resistor pull_resistor_60 (.node(in_33));
  Register #(.width(32)) register_30 (.D(register_29_q), .en(1'b1), .Q(register_30_q), .clk(clk), .clr(clr));
  assign or_87_out = register_30_q | in_33;  // OR_Gate or_87, 32 bits wide
  assign or_88_out = in_33 | pull_resistor_61_node;  // OR_Gate or_88, 32 bits wide
  Pull_Resistor pull_resistor_61 (.node(pull_resistor_61_node));
  assign pull_resistor_61_node = show ? register_30_q : 32'bz;  // Controlled_Buffer controlled_buffer_30
  assign or_89_out = or_87_out | or_86_out;  // OR_Gate or_89, 32 bits wide
  Multiplexer #(.width(32), .enable("false")) multiplexer_30 (
    .in0(register_30_q), .in1(or_88_out), .out(out_67), .sel(1'b1));
  Register #(.width(32)) register_31 (.D(register_30_q), .en(1'b1), .Q(register_31_q), .clk(clk), .clr(clr));
  Pull_Resistor pull_resistor_62 (.node(in_34));
  Pull_Resistor pull_resistor_63 (.node(pull_resistor_63_node));
  assign pull_resistor_63_node = show ? register_31_q : 32'bz;  // Controlled_Buffer controlled_buffer_31
  assign or_90_out = register_31_q | in_34;  // OR_Gate or_90, 32 bits wide
  assign or_91_out = or_90_out | or_89_out;  // OR_Gate or_91, 32 bits wide
  Multiplexer #(.width(32), .enable("false")) multiplexer_31 (
    .in0(register_31_q), .in1(or_92_out), .out(out_68), .sel(1'b1));
  assign or_92_out = in_34 | pull_resistor_63_node;  // OR_Gate or_92, 32 bits wide
  Register #(.width(32)) register_32 (.D(register_31_q), .en(1'b1), .Q(shift_out), .clk(clk), .clr(clr));
  Pull_Resistor pull_resistor_64 (.node(in_35));
  assign or_93_out = in_35 | pull_resistor_65_node;  // OR_Gate or_93, 32 bits wide
  Pull_Resistor pull_resistor_65 (.node(pull_resistor_65_node));
  assign pull_resistor_65_node = show ? shift_out : 32'bz;  // Controlled_Buffer controlled_buffer_32
  assign or_94_out = shift_out | in_35;  // OR_Gate or_94, 32 bits wide
  assign or_95_out = or_94_out | or_91_out;  // OR_Gate or_95, 32 bits wide
  Multiplexer #(.width(32), .enable("false")) multiplexer_32 (
    .in0(shift_out), .in1(or_93_out), .out(out_69), .sel(1'b1));
  nor nor_1 (nor_1_out, or_95_out[0], or_95_out[1], or_95_out[2], or_95_out[3], or_95_out[4], or_95_out[5], or_95_out[6], or_95_out[7], or_95_out[8], or_95_out[9], or_95_out[10], or_95_out[11], or_95_out[12], or_95_out[13], or_95_out[14], or_95_out[15], or_95_out[16], or_95_out[17], or_95_out[18], or_95_out[19], or_95_out[20], or_95_out[21], or_95_out[22], or_95_out[23], or_95_out[24], or_95_out[25], or_95_out[26], or_95_out[27], or_95_out[28], or_95_out[29], or_95_out[30], or_95_out[31]);
  Pull_Resistor #(.pull(1)) pull_resistor_66 (.node(prev_clear));
  and and_1 (clear, prev_clear, nor_1_out);

  // Notes on the sheet:
  //   collisions
endmodule

module dino (
  input  clr,
  input  [31:0] in_2,
  input  [31:0] in_3,
  input  [31:0] in_4,
  input  clk,
  input  is_crouch,
  input  [31:0] in_7,
  input  cls,
  input  [31:0] in_9,
  input  [31:0] in_10,
  input  [31:0] in_11,
  input  [31:0] in_12,
  input  [31:0] in_13,
  input  [31:0] in_14,
  input  [31:0] in_15,
  input  [4:0] Y,
  input  is_jump,
  output [31:0] out_18,
  output [31:0] out_19,
  output [31:0] out_20,
  output [31:0] out_21,
  output [31:0] out_22,
  output [31:0] out_23,
  output [31:0] out_24,
  output [31:0] out_25,
  output [31:0] out_26,
  output [31:0] out_27,
  output [31:0] out_28,
  output collision
);

  wire demultiplexer_1_out8, demultiplexer_1_out9, demultiplexer_1_out10, demultiplexer_1_out11,
       demultiplexer_1_out12, demultiplexer_1_out13, demultiplexer_1_out14, demultiplexer_1_out15,
       demultiplexer_1_out24, demultiplexer_1_out25, demultiplexer_1_out26, demultiplexer_1_out27,
       demultiplexer_1_out28, demultiplexer_1_out29, demultiplexer_1_out30, demultiplexer_1_out31, or_1_out,
       or_2_out, or_3_out;
  wire [0:0] xor_1_out, xor_2_out;
  wire [4:0] counter_1_q;
  wire [31:0] and_1_out, and_2_out, and_3_out, and_4_out, and_5_out, and_6_out, and_7_out, and_8_out,
       and_9_out, and_10_out, and_11_out, multiplexer_1_out, multiplexer_2_out, multiplexer_3_out,
       multiplexer_4_out, multiplexer_5_out, multiplexer_6_out, multiplexer_7_out, multiplexer_8_out,
       multiplexer_9_out, multiplexer_10_out, multiplexer_11_out, multiplexer_12_out, multiplexer_13_out,
       multiplexer_14_out, multiplexer_15_out, multiplexer_16_out, multiplexer_17_out, multiplexer_18_out,
       multiplexer_19_out, multiplexer_20_out, multiplexer_21_out, multiplexer_22_out, multiplexer_23_out,
       multiplexer_24_out, or_6_out, or_8_out, or_10_out, or_12_out, or_14_out, or_16_out, or_18_out,
       or_20_out, or_22_out, or_24_out, shifter_1_out, shifter_2_out, shifter_3_out, shifter_4_out,
       shifter_5_out, shifter_6_out, shifter_7_out, shifter_8_out, shifter_9_out, shifter_10_out,
       shifter_11_out;

  DotMatrix #(.matrixcols(11), .matrixrows(32)) dotmatrix_1 (
    .col0(32'h4), .col1(32'h6), .col2(32'h73), .col3(32'h7e), .col4(multiplexer_1_out), .col5(32'h70),
    .col6(32'h70), .col7({32{1'b0}}), .col8({32{1'b0}}), .col9({32{1'b0}}), .col10({32{1'b0}}));
  Pull_Resistor pull_resistor_1 (.node(is_crouch));
  Pull_Resistor pull_resistor_2 (.node(is_jump));
  Multiplexer #(.width(32), .enable("false")) multiplexer_1 (
    .in0(32'h55), .in1(32'h45), .out(multiplexer_1_out), .sel(cls));
  DotMatrix #(.matrixcols(11), .matrixrows(32)) dotmatrix_2 (
    .col0(32'h4), .col1(32'h6), .col2(32'h3), .col3(32'h2), .col4(32'h3), .col5(32'h2), .col6(32'he),
    .col7(32'he), .col8(multiplexer_2_out), .col9(32'he), .col10(32'he));
  Multiplexer #(.width(32), .enable("false")) multiplexer_2 (
    .in0(32'ha), .in1(32'h8), .out(multiplexer_2_out), .sel(cls));
  Multiplexer #(.width(32), .enable("false")) multiplexer_3 (
    .in0(32'h4), .in1(32'h4), .out(multiplexer_3_out), .sel(is_crouch));
  Multiplexer #(.width(32), .enable("false")) multiplexer_4 (
    .in0(32'h6), .in1(32'h6), .out(multiplexer_4_out), .sel(is_crouch));
  Multiplexer #(.width(32), .enable("false")) multiplexer_5 (
    .in0(32'h73), .in1(32'h3), .out(multiplexer_5_out), .sel(is_crouch));
  Multiplexer #(.width(32), .enable("false")) multiplexer_6 (
    .in0(32'h7e), .in1(32'h2), .out(multiplexer_6_out), .sel(is_crouch));
  Multiplexer #(.width(32), .enable("false")) multiplexer_7 (
    .in0(multiplexer_1_out), .in1(32'h3), .out(multiplexer_7_out), .sel(is_crouch));
  Multiplexer #(.width(32), .enable("false")) multiplexer_8 (
    .in0(32'h70), .in1(32'h2), .out(multiplexer_8_out), .sel(is_crouch));
  Multiplexer #(.width(32), .enable("false")) multiplexer_9 (
    .in0(32'h70), .in1(32'he), .out(multiplexer_9_out), .sel(is_crouch));
  Multiplexer #(.width(32), .enable("false")) multiplexer_10 (
    .in0({32{1'b0}}), .in1(32'he), .out(multiplexer_10_out), .sel(is_crouch));
  Multiplexer #(.width(32), .enable("false")) multiplexer_11 (
    .in0({32{1'b0}}), .in1(multiplexer_2_out), .out(multiplexer_11_out), .sel(is_crouch));
  Multiplexer #(.width(32), .enable("false")) multiplexer_12 (
    .in0({32{1'b0}}), .in1(32'he), .out(multiplexer_12_out), .sel(is_crouch));
  Multiplexer #(.width(32), .enable("false")) multiplexer_13 (
    .in0({32{1'b0}}), .in1(32'he), .out(multiplexer_13_out), .sel(is_crouch));
  or or_1 (or_1_out, clr, is_jump);
  Counter #(.width(5), .max('h1f)) counter_1 (
    .load(1'b0), .count(1'b1), .Q(counter_1_q), .clk(clk), .clr(or_1_out));  // open: D, carry
  or or_2 (or_2_out, demultiplexer_1_out11, demultiplexer_1_out8, demultiplexer_1_out9, demultiplexer_1_out10, demultiplexer_1_out12, demultiplexer_1_out13, demultiplexer_1_out14, demultiplexer_1_out15);
  xor xor_1 (xor_1_out[0], or_3_out, multiplexer_5_out[0]);
  xor xor_2 (xor_2_out[0], or_2_out, multiplexer_7_out[0]);
  Demultiplexer #(.select(5), .enable("false")) demultiplexer_1 (
    .out8(demultiplexer_1_out8), .out9(demultiplexer_1_out9), .out10(demultiplexer_1_out10),
    .out11(demultiplexer_1_out11), .out12(demultiplexer_1_out12), .out13(demultiplexer_1_out13),
    .out14(demultiplexer_1_out14), .out15(demultiplexer_1_out15), .out24(demultiplexer_1_out24),
    .out25(demultiplexer_1_out25), .out26(demultiplexer_1_out26), .out27(demultiplexer_1_out27),
    .out28(demultiplexer_1_out28), .out29(demultiplexer_1_out29), .out30(demultiplexer_1_out30),
    .out31(demultiplexer_1_out31), .in(1'b1), .sel(counter_1_q));  // open: out0, out1, out2, out3, out4, out5, out6, out7, out16, out17, out18, out19, out20, out21, out22, out23
  or or_3 (or_3_out, demultiplexer_1_out27, demultiplexer_1_out24, demultiplexer_1_out25, demultiplexer_1_out26, demultiplexer_1_out28, demultiplexer_1_out29, demultiplexer_1_out30, demultiplexer_1_out31);
  Shifter #(.width(32)) shifter_1 (.in(multiplexer_3_out), .\dist (Y), .out(shifter_1_out));
  Shifter #(.width(32)) shifter_2 (.in(multiplexer_4_out), .\dist (Y), .out(shifter_2_out));
  Shifter #(.width(32)) shifter_3 (.in({multiplexer_5_out[31:1], xor_1_out[0]}), .\dist (Y), .out(shifter_3_out));
  Shifter #(.width(32)) shifter_4 (.in(multiplexer_6_out), .\dist (Y), .out(shifter_4_out));
  Shifter #(.width(32)) shifter_5 (.in({multiplexer_7_out[31:1], xor_2_out[0]}), .\dist (Y), .out(shifter_5_out));
  Shifter #(.width(32)) shifter_6 (.in(multiplexer_8_out), .\dist (Y), .out(shifter_6_out));
  Shifter #(.width(32)) shifter_7 (.in(multiplexer_9_out), .\dist (Y), .out(shifter_7_out));
  Shifter #(.width(32)) shifter_8 (.in(multiplexer_10_out), .\dist (Y), .out(shifter_8_out));
  Shifter #(.width(32)) shifter_9 (.in(multiplexer_11_out), .\dist (Y), .out(shifter_9_out));
  Shifter #(.width(32)) shifter_10 (.in(multiplexer_12_out), .\dist (Y), .out(shifter_10_out));
  Shifter #(.width(32)) shifter_11 (.in(multiplexer_13_out), .\dist (Y), .out(shifter_11_out));
  Pull_Resistor pull_resistor_3 (.node(in_2));
  Multiplexer #(.width(32), .enable("false")) multiplexer_14 (
    .in0(multiplexer_3_out), .in1(shifter_1_out), .out(multiplexer_14_out), .sel(is_jump));
  assign and_1_out = in_2 & multiplexer_14_out;  // AND_Gate and_1, 32 bits wide
  Pull_Resistor pull_resistor_4 (.node(in_3));
  Multiplexer #(.width(32), .enable("false")) multiplexer_15 (
    .in0(multiplexer_4_out), .in1(shifter_2_out), .out(multiplexer_15_out), .sel(is_jump));
  assign and_2_out = in_3 & multiplexer_15_out;  // AND_Gate and_2, 32 bits wide
  Pull_Resistor pull_resistor_5 (.node(in_4));
  Multiplexer #(.width(32), .enable("false")) multiplexer_16 (
    .in0({multiplexer_5_out[31:1], xor_1_out[0]}), .in1(shifter_3_out), .out(multiplexer_16_out),
    .sel(is_jump));
  assign and_3_out = in_4 & multiplexer_16_out;  // AND_Gate and_3, 32 bits wide
  Pull_Resistor pull_resistor_6 (.node(in_7));
  Multiplexer #(.width(32), .enable("false")) multiplexer_17 (
    .in0(multiplexer_6_out), .in1(shifter_4_out), .out(multiplexer_17_out), .sel(is_jump));
  assign and_4_out = in_7 & multiplexer_17_out;  // AND_Gate and_4, 32 bits wide
  Pull_Resistor pull_resistor_7 (.node(in_9));
  Multiplexer #(.width(32), .enable("false")) multiplexer_18 (
    .in0({multiplexer_7_out[31:1], xor_2_out[0]}), .in1(shifter_5_out), .out(multiplexer_18_out),
    .sel(is_jump));
  assign and_5_out = in_9 & multiplexer_18_out;  // AND_Gate and_5, 32 bits wide
  Pull_Resistor pull_resistor_8 (.node(in_10));
  Multiplexer #(.width(32), .enable("false")) multiplexer_19 (
    .in0(multiplexer_8_out), .in1(shifter_6_out), .out(multiplexer_19_out), .sel(is_jump));
  assign and_6_out = in_10 & multiplexer_19_out;  // AND_Gate and_6, 32 bits wide
  Pull_Resistor pull_resistor_9 (.node(in_11));
  Multiplexer #(.width(32), .enable("false")) multiplexer_20 (
    .in0(multiplexer_9_out), .in1(shifter_7_out), .out(multiplexer_20_out), .sel(is_jump));
  assign and_7_out = in_11 & multiplexer_20_out;  // AND_Gate and_7, 32 bits wide
  Pull_Resistor pull_resistor_10 (.node(in_12));
  Multiplexer #(.width(32), .enable("false")) multiplexer_21 (
    .in0(multiplexer_10_out), .in1(shifter_8_out), .out(multiplexer_21_out), .sel(is_jump));
  assign and_8_out = in_12 & multiplexer_21_out;  // AND_Gate and_8, 32 bits wide
  Pull_Resistor pull_resistor_11 (.node(in_13));
  Multiplexer #(.width(32), .enable("false")) multiplexer_22 (
    .in0(multiplexer_11_out), .in1(shifter_9_out), .out(multiplexer_22_out), .sel(is_jump));
  assign and_9_out = in_13 & multiplexer_22_out;  // AND_Gate and_9, 32 bits wide
  Pull_Resistor pull_resistor_12 (.node(in_14));
  Multiplexer #(.width(32), .enable("false")) multiplexer_23 (
    .in0(multiplexer_12_out), .in1(shifter_10_out), .out(multiplexer_23_out), .sel(is_jump));
  assign and_10_out = in_14 & multiplexer_23_out;  // AND_Gate and_10, 32 bits wide
  Pull_Resistor pull_resistor_13 (.node(in_15));
  Multiplexer #(.width(32), .enable("false")) multiplexer_24 (
    .in0(multiplexer_13_out), .in1(shifter_11_out), .out(multiplexer_24_out), .sel(is_jump));
  assign and_11_out = in_15 & multiplexer_24_out;  // AND_Gate and_11, 32 bits wide
  assign out_18 = in_2 | multiplexer_14_out;  // OR_Gate or_4, 32 bits wide
  assign out_19 = in_3 | multiplexer_15_out;  // OR_Gate or_5, 32 bits wide
  assign or_6_out = and_2_out | and_1_out;  // OR_Gate or_6, 32 bits wide
  assign out_20 = in_4 | multiplexer_16_out;  // OR_Gate or_7, 32 bits wide
  assign or_8_out = and_3_out | or_6_out;  // OR_Gate or_8, 32 bits wide
  assign out_21 = in_7 | multiplexer_17_out;  // OR_Gate or_9, 32 bits wide
  assign or_10_out = and_4_out | or_8_out;  // OR_Gate or_10, 32 bits wide
  assign out_22 = in_9 | multiplexer_18_out;  // OR_Gate or_11, 32 bits wide
  assign or_12_out = and_5_out | or_10_out;  // OR_Gate or_12, 32 bits wide
  assign out_23 = in_10 | multiplexer_19_out;  // OR_Gate or_13, 32 bits wide
  assign or_14_out = and_6_out | or_12_out;  // OR_Gate or_14, 32 bits wide
  assign out_24 = in_11 | multiplexer_20_out;  // OR_Gate or_15, 32 bits wide
  assign or_16_out = and_7_out | or_14_out;  // OR_Gate or_16, 32 bits wide
  assign out_25 = in_12 | multiplexer_21_out;  // OR_Gate or_17, 32 bits wide
  assign or_18_out = and_8_out | or_16_out;  // OR_Gate or_18, 32 bits wide
  assign out_26 = in_13 | multiplexer_22_out;  // OR_Gate or_19, 32 bits wide
  assign or_20_out = and_9_out | or_18_out;  // OR_Gate or_20, 32 bits wide
  assign out_27 = in_14 | multiplexer_23_out;  // OR_Gate or_21, 32 bits wide
  assign or_22_out = and_10_out | or_20_out;  // OR_Gate or_22, 32 bits wide
  assign out_28 = in_15 | multiplexer_24_out;  // OR_Gate or_23, 32 bits wide
  assign or_24_out = or_22_out | and_11_out;  // OR_Gate or_24, 32 bits wide
  or or_25 (collision, or_24_out[0], or_24_out[1], or_24_out[2], or_24_out[3], or_24_out[4], or_24_out[5], or_24_out[6], or_24_out[7], or_24_out[8], or_24_out[9], or_24_out[10], or_24_out[11], or_24_out[12], or_24_out[13], or_24_out[14], or_24_out[15], or_24_out[16], or_24_out[17], or_24_out[18], or_24_out[19], or_24_out[20], or_24_out[21], or_24_out[22], or_24_out[23], or_24_out[24], or_24_out[25], or_24_out[26], or_24_out[27], or_24_out[28], or_24_out[29], or_24_out[30], or_24_out[31]);
endmodule

module dino_jump (
  input  clk,
  input  clr,
  input  jump,
  input  crouch,
  output is_jump,
  output [4:0] Y,
  output is_crouch
);

  wire comparator_1_gt, not_1_out, or_1_out;
  wire [4:0] adder_1_out, multiplexer_1_out, multiplexer_2_out, multiplexer_3_out, register_2_q,
       subtractor_1_out;

  Multiplexer #(.width(5), .enable("false")) multiplexer_1 (
    .in0({5{1'b0}}), .in1(adder_1_out), .out(multiplexer_1_out), .sel(comparator_1_gt));
  Comparator #(.width(5), .mode("unsigned")) comparator_1 (
    .a(adder_1_out), .b({5{1'b0}}), .gt(comparator_1_gt));  // open: eq, lt
  Multiplexer #(.width(5), .enable("false")) multiplexer_2 (
    .in0({5{1'b0}}), .in1(5'b00110), .out(multiplexer_2_out), .sel(jump));
  Multiplexer #(.width(5), .enable("false")) multiplexer_3 (
    .in0(multiplexer_2_out), .in1(subtractor_1_out), .out(multiplexer_3_out), .sel(comparator_1_gt));
  not not_1 (not_1_out, comparator_1_gt);
  // Probe on Y
  Register #(.width(5)) register_1 (.D(multiplexer_1_out), .Q(Y), .clk(clk), .clr(clr));  // open: en
  // Probe on register_2_q
  Register #(.width(5)) register_2 (.D(multiplexer_3_out), .Q(register_2_q), .clk(clk), .clr(clr));  // open: en
  T_Flip_Flop t_ff_1 (.clk(crouch), .T(crouch), .Q(is_crouch), .reset(or_1_out), .en(not_1_out));  // open: Qn, preset
  or or_1 (or_1_out, clr, comparator_1_gt);
  Comparator #(.width(5), .mode("unsigned")) comparator_2 (.a(Y), .b({5{1'b0}}), .gt(is_jump));  // open: eq, lt
  Adder #(.width(5)) adder_1 (.a(Y), .b(register_2_q), .out(adder_1_out));  // open: cin, cout
  Subtractor #(.width(5)) subtractor_1 (.a(register_2_q), .b(5'b00001), .out(subtractor_1_out));  // open: bin, bout
endmodule

module keyboard_handler (
  input  [6:0] key,
  input  is_jump,
  input  sen_kboard,
  output crouch,
  output jump,
  output pause,
  output reset
);

  wire and_1_out, comparator_1_eq, comparator_2_eq, comparator_3_eq, comparator_4_eq, comparator_5_eq,
       comparator_6_eq, comparator_7_eq, comparator_8_eq, comparator_9_eq, not_1_out, or_2_out, or_3_out;

  Comparator #(.width(7)) comparator_1 (.a(key), .b(7'b1110011), .eq(comparator_1_eq));  // open: gt, lt
  Comparator #(.width(7)) comparator_2 (.a(key), .b(7'b1001011), .eq(comparator_2_eq));  // open: gt, lt
  Comparator #(.width(7)) comparator_3 (.a(key), .b(7'b1000110), .eq(comparator_3_eq));  // open: gt, lt
  Comparator #(.width(7)) comparator_4 (.a(key), .b(7'b0100000), .eq(comparator_4_eq));  // open: gt, lt
  Comparator #(.width(7)) comparator_5 (.a(key), .b(7'b1110111), .eq(comparator_5_eq));  // open: gt, lt
  Comparator #(.width(7)) comparator_6 (.a(key), .b(7'b1110000), .eq(comparator_6_eq));  // open: gt, lt
  Comparator #(.width(7)) comparator_7 (.a(key), .b(7'b0110111), .eq(comparator_7_eq));  // open: gt, lt
  and and_1 (and_1_out, ~pause, reset);  // AND_Gate
  Comparator #(.width(7)) comparator_8 (.a(key), .b(7'b1110010), .eq(comparator_8_eq));  // open: gt, lt
  Comparator #(.width(7)) comparator_9 (.a(key), .b(7'b0111010), .eq(comparator_9_eq));  // open: gt, lt
  or or_1 (crouch, comparator_1_eq, comparator_2_eq);
  or or_2 (or_2_out, comparator_3_eq, comparator_4_eq, comparator_5_eq);
  T_Flip_Flop t_ff_1 (.clk(or_3_out), .T(or_3_out), .Qn(pause), .reset(sen_kboard));  // open: Q, preset, en
  or or_3 (or_3_out, comparator_6_eq, comparator_7_eq, and_1_out);
  or or_4 (reset, comparator_8_eq, comparator_9_eq);
  D_Flip_Flop d_ff_1 (.clk(or_2_out), .D(or_2_out), .Q(jump), .en(not_1_out), .reset(is_jump));  // open: Qn, preset
  not not_1 (not_1_out, pause);
endmodule

module random_spawn (
  input  clk,
  input  allow,
  input  [3:0] level,
  output spawn_cactus,
  output spawn_bird
);

  wire and_1_out, comparator_1_lt, counter_1_carry, demultiplexer_1_out0, multiplexer_2_out, not_1_out,
       pull_resistor_2_node, shift_register_1_out;
  wire [1:0] random_2_out;
  wire [5:0] random_1_out;
  wire [7:0] adder_1_out, bit_extender_1_out, multiplexer_1_out;

  Random #(.width(6)) random_1 (.clk(clk), .next(counter_1_carry), .out(random_1_out));  // open: clr
  Multiplexer #(.select(4), .width(8), .enable("false")) multiplexer_1 (
    .in0(8'h70), .in1(8'h75), .in2(8'h80), .in3(8'h85), .in4(8'h90), .in5(8'h95), .in6(8'ha0),
    .out(multiplexer_1_out), .sel(level));  // open: in7, in8, in9, in10, in11, in12, in13, in14, in15
  // Probe on multiplexer_1_out
  assign bit_extender_1_out = {{2{1'b0}}, random_1_out};  // Bit_Extender bit_extender_1
  Adder adder_1 (.a(multiplexer_1_out), .b(bit_extender_1_out), .out(adder_1_out));  // open: cin, cout
  Counter #(.ongoal("load")) counter_1 (
    .load(1'b1), .D(adder_1_out), .count(1'b1), .carry(counter_1_carry), .clk(clk));  // open: Q, clr
  Demultiplexer #(.select(2), .enable("false")) demultiplexer_1 (
    .out0(demultiplexer_1_out0), .in(1'b1), .sel(random_2_out));  // open: out1, out2, out3
  Random #(.width(2)) random_2 (.clk(counter_1_carry), .next(counter_1_carry), .out(random_2_out));  // open: clr
  Comparator #(.width(4), .mode("unsigned")) comparator_1 (
    .a(level), .b(4'b0010), .lt(comparator_1_lt));  // open: gt, eq
  and and_1 (and_1_out, demultiplexer_1_out0, ~comparator_1_lt);  // AND_Gate
  Multiplexer #(.enable("false")) multiplexer_2 (
    .in0(shift_register_1_out), .in1(pull_resistor_2_node), .out(multiplexer_2_out),
    .sel(pull_resistor_2_node));
  not not_1 (not_1_out, pull_resistor_2_node);
  Pull_Resistor pull_resistor_1 (.node(spawn_cactus));
  assign spawn_cactus = allow ? counter_1_carry : 1'bz;  // Controlled_Buffer controlled_buffer_1
  Pull_Resistor pull_resistor_2 (.node(pull_resistor_2_node));
  assign pull_resistor_2_node = allow ? and_1_out : 1'bz;  // Controlled_Buffer controlled_buffer_2
  Shift_Register #(.length(30)) shift_register_1 (
    .shift(1'b1), .in(multiplexer_2_out), .clk(clk), .out(shift_register_1_out), .clr(not_1_out),
    .q28(spawn_bird));  // open: load, d0, q0, d1, q1, d2, q2, d3, q3, d4, q4, d5, q5, d6, q6, d7, q7, d8, q8, d9, q9, d10, q10, d11, q11, d12, q12, d13, q13, d14, q14, d15, q15, d16, q16, d17, q17, d18, q18, d19, q19, d20, q20, d21, q21, d22, q22, d23, q23, d24, q24, d25, q25, d26, q26, d27, q27, d28, d29, q29

  // Notes on the sheet:
  //   LEVELS
  //   BIRD CHANCE 1/8
  //   BIRDS ONLY FROM LVL2
endmodule

module obstacles (
  input  clk,
  input  gen_obst,
  output [31:0] out
);

  wire big_cactus_1_done, cactus_1_done, controlled_buffer_1_out, demultiplexer_1_out0, demultiplexer_1_out1,
       demultiplexer_1_out2, demultiplexer_1_out3, not_1_out, or_1_out, or_2_out, or_3_out, or_4_out,
       small_cactus_1_done, t_ff_1_q, wide_cactus_1_done;
  wire [3:0] divider_1_rem, random_1_out;
  wire [31:0] big_cactus_1_out, cactus_1_out_3, small_cactus_1_out, wide_cactus_1_out;

  assign controlled_buffer_1_out = not_1_out ? gen_obst : 1'bz;  // Controlled_Buffer controlled_buffer_1
  Pull_Resistor pull_resistor_1 (.node(controlled_buffer_1_out));
  not not_1 (not_1_out, t_ff_1_q);
  Random #(.width(4)) random_1 (
    .clk(controlled_buffer_1_out), .next(controlled_buffer_1_out), .out(random_1_out));  // open: clr
  or or_1 (or_1_out, controlled_buffer_1_out, or_4_out);
  Divider #(.width(4)) divider_1 (.a(random_1_out), .b(4'b0100), .rem(divider_1_rem));  // open: out, upper
  Demultiplexer #(.select(2), .disabled(0)) demultiplexer_1 (
    .out0(demultiplexer_1_out0), .out1(demultiplexer_1_out1), .out2(demultiplexer_1_out2),
    .out3(demultiplexer_1_out3), .in(1'b1), .sel(divider_1_rem[1:0]), .en(t_ff_1_q));
  T_Flip_Flop t_ff_1 (.clk(clk), .T(or_1_out), .Q(t_ff_1_q));  // open: Qn, preset, reset, en
  cactus cactus_1 (.clk(clk), .\generate (demultiplexer_1_out0), .done(cactus_1_done), .out_3(cactus_1_out_3));
  small_cactus small_cactus_1 (
    .clk(clk), .\generate (demultiplexer_1_out1), .out(small_cactus_1_out), .done(small_cactus_1_done));
  or or_2 (or_2_out, small_cactus_1_done, cactus_1_done);
  big_cactus big_cactus_1 (
    .out(big_cactus_1_out), .\generate (demultiplexer_1_out2), .done(big_cactus_1_done), .clk(clk));
  wide_cactus wide_cactus_1 (
    .\generate (demultiplexer_1_out3), .out(wide_cactus_1_out), .done(wide_cactus_1_done), .clk(clk));
  or or_3 (or_3_out, big_cactus_1_done, or_2_out);
  or or_4 (or_4_out, wide_cactus_1_done, or_3_out);
  Multiplexer #(.select(2), .width(32), .disabled(0)) multiplexer_1 (
    .in0(cactus_1_out_3), .in1(small_cactus_1_out), .in2(big_cactus_1_out), .in3(wide_cactus_1_out),
    .out(out), .sel(divider_1_rem[1:0]), .en(t_ff_1_q));

  // Notes on the sheet:
  //   Amount of kinds of obstacles
endmodule

module cactus (
  input  \generate ,
  input  clk,
  output [31:0] out_3,
  output done
);

  wire [1:0] counter_1_q;

  DotMatrix #(.matrixcols(3), .matrixrows(32)) dotmatrix_1 (.col0(32'h7a), .col1(32'hf), .col2(32'h18));
  Multiplexer #(.select(2), .width(32), .enable("false")) multiplexer_1 (
    .in0(32'h7a), .in1(32'hf), .in2(32'h18), .out(out_3), .sel(counter_1_q));  // open: in3
  Counter #(.width(2), .max('h2)) counter_1 (
    .count(\generate ), .Q(counter_1_q), .carry(done), .clk(clk));  // open: load, D, clr
endmodule

module big_cactus (
  input  \generate ,
  input  clk,
  output [31:0] out,
  output done
);

  wire [2:0] counter_1_q;

  DotMatrix #(.matrixrows(32)) dotmatrix_1 (.col0(32'h6), .col1(32'h2), .col2(32'h3f), .col3(32'h8), .col4(32'h78));
  Counter #(.width(3), .max('h4)) counter_1 (
    .count(\generate ), .Q(counter_1_q), .carry(done), .clk(clk));  // open: load, D, clr
  Multiplexer #(.select(3), .width(32), .enable("false")) multiplexer_1 (
    .in0(32'h6), .in1(32'h2), .in2(32'h3f), .in3(32'h8), .in4(32'h78), .out(out), .sel(counter_1_q));  // open: in5, in6, in7
endmodule

module small_cactus (
  input  \generate ,
  input  clk,
  output [31:0] out,
  output done
);

  wire [2:0] counter_1_q;

  DotMatrix #(.matrixrows(32)) dotmatrix_1 (.col0(32'he), .col1(32'h2), .col2(32'h7), .col3(32'h2), .col4(32'h6));
  Multiplexer #(.select(3), .width(32), .enable("false")) multiplexer_1 (
    .in0(32'he), .in1(32'h2), .in2(32'h7), .in3(32'h2), .in4(32'h6), .out(out), .sel(counter_1_q));  // open: in5, in6, in7
  Counter #(.width(3), .max('h4)) counter_1 (
    .count(\generate ), .Q(counter_1_q), .carry(done), .clk(clk));  // open: load, D, clr
endmodule

module wide_cactus (
  input  \generate ,
  input  clk,
  output [31:0] out,
  output done
);

  wire [2:0] counter_1_q;

  DotMatrix #(.matrixcols(7), .matrixrows(32)) dotmatrix_1 (
    .col0(32'hc), .col1(32'h7), .col2(32'h3c), .col3(32'h8), .col4(32'h1f), .col5(32'h4), .col6(32'hc));
  Counter #(.width(3), .max('h6)) counter_1 (
    .count(\generate ), .Q(counter_1_q), .carry(done), .clk(clk));  // open: load, D, clr
  Multiplexer #(.select(3), .width(32), .enable("false")) multiplexer_1 (
    .in0(32'hc), .in1(32'h7), .in2(32'h3c), .in3(32'h8), .in4(32'h1f), .in5(32'h4), .in6(32'hc), .out(out),
    .sel(counter_1_q));  // open: in7
endmodule

module birds (
  input  gen_obst,
  input  [3:0] speed,
  input  pause,
  output [31:0] up,
  output [31:0] down,
  output birds_clk
);

  wire counter_1_carry, multiplexer_1_out, not_1_out, not_2_out, not_3_out, pull_resistor_1_node,
       speed_1_clk, t_ff_1_q;
  wire [1:0] random_2_out;
  wire [3:0] counter_1_q, divider_1_rem, random_1_out;
  wire [31:0] bird_wings_up_1_out_1, bird_wings_up_1_out_2, bird_wings_up_1_out_3, bird_wings_up_1_out_4,
       bird_wings_up_1_out_5, bird_wings_up_1_out_6, bird_wings_up_1_out_7, bird_wings_up_1_out_8,
       bird_wings_up_1_out_9, bird_wings_up_1_out_10, bird_wingsdown_1_out_1, bird_wingsdown_1_out_2,
       bird_wingsdown_1_out_3, bird_wingsdown_1_out_4, bird_wingsdown_1_out_5, bird_wingsdown_1_out_6,
       bird_wingsdown_1_out_7, bird_wingsdown_1_out_8, bird_wingsdown_1_out_9, bird_wingsdown_1_out_10,
       multiplexer_2_out, multiplexer_4_out, shifter_1_out, shifter_2_out, shifter_3_out, shifter_4_out,
       shifter_5_out, shifter_6_out;

  Pull_Resistor pull_resistor_1 (.node(pull_resistor_1_node));
  assign pull_resistor_1_node = not_1_out ? gen_obst : 1'bz;  // Controlled_Buffer controlled_buffer_1
  not not_1 (not_1_out, t_ff_1_q);
  Random #(.width(4)) random_1 (
    .clk(pull_resistor_1_node), .next(pull_resistor_1_node), .out(random_1_out));  // open: clr
  Divider #(.width(4)) divider_1 (.a(random_1_out), .b(speed), .rem(divider_1_rem));  // open: out, upper
  speed speed_1 (.speed(divider_1_rem), .clk(speed_1_clk));
  not not_2 (not_2_out, t_ff_1_q);
  T_Flip_Flop t_ff_1 (
    .clk(speed_1_clk), .T(counter_1_carry), .Q(t_ff_1_q), .preset(pull_resistor_1_node));  // open: Qn, reset, en
  Counter #(.width(4), .max('h9)) counter_1 (
    .count(t_ff_1_q), .Q(counter_1_q), .carry(counter_1_carry), .clk(speed_1_clk));  // open: load, D, clr
  Pull_Resistor pull_resistor_2 (.node(birds_clk));
  assign birds_clk = not_3_out ? speed_1_clk : 1'bz;  // Controlled_Buffer controlled_buffer_2
  not not_3 (not_3_out, pause);
  Multiplexer #(.enable("false")) multiplexer_1 (.in0(1'b0), .in1(gen_obst), .out(multiplexer_1_out), .sel(not_2_out));
  bird_wings_up bird_wings_up_1 (
    .out_1(bird_wings_up_1_out_1), .out_2(bird_wings_up_1_out_2), .out_3(bird_wings_up_1_out_3),
    .out_4(bird_wings_up_1_out_4), .out_5(bird_wings_up_1_out_5), .out_6(bird_wings_up_1_out_6),
    .out_7(bird_wings_up_1_out_7), .out_8(bird_wings_up_1_out_8), .out_9(bird_wings_up_1_out_9),
    .out_10(bird_wings_up_1_out_10));
  Multiplexer #(.select(4), .width(32)) multiplexer_2 (
    .in0(bird_wings_up_1_out_1), .in1(bird_wings_up_1_out_2), .in2(bird_wings_up_1_out_3),
    .in3(bird_wings_up_1_out_4), .in4(bird_wings_up_1_out_5), .in5(bird_wings_up_1_out_6),
    .in6(bird_wings_up_1_out_7), .in7(bird_wings_up_1_out_8), .in8(bird_wings_up_1_out_9),
    .in9(bird_wings_up_1_out_10), .out(multiplexer_2_out), .sel(counter_1_q), .en(t_ff_1_q));  // open: in10, in11, in12, in13, in14, in15
  Pull_Resistor pull_resistor_3 (.node(multiplexer_2_out));
  Shifter #(.width(32)) shifter_1 (.in(multiplexer_2_out), .\dist (5'b00100), .out(shifter_1_out));
  Shifter #(.width(32)) shifter_2 (.in(multiplexer_2_out), .\dist (5'b00111), .out(shifter_2_out));
  Shifter #(.width(32)) shifter_3 (.in(multiplexer_2_out), .\dist (5'b10000), .out(shifter_3_out));
  Random #(.width(2)) random_2 (.clk(multiplexer_1_out), .next(multiplexer_1_out), .out(random_2_out));  // open: clr
  Multiplexer #(.select(2), .width(32), .enable("false")) multiplexer_3 (
    .in0(multiplexer_2_out), .in1(shifter_1_out), .in2(shifter_2_out), .in3(shifter_3_out), .out(up),
    .sel(random_2_out));
  bird_wingsdown bird_wingsdown_1 (
    .out_1(bird_wingsdown_1_out_1), .out_2(bird_wingsdown_1_out_2), .out_3(bird_wingsdown_1_out_3),
    .out_4(bird_wingsdown_1_out_4), .out_5(bird_wingsdown_1_out_5), .out_6(bird_wingsdown_1_out_6),
    .out_7(bird_wingsdown_1_out_7), .out_8(bird_wingsdown_1_out_8), .out_9(bird_wingsdown_1_out_9),
    .out_10(bird_wingsdown_1_out_10));
  Multiplexer #(.select(4), .width(32)) multiplexer_4 (
    .in0(bird_wingsdown_1_out_1), .in1(bird_wingsdown_1_out_2), .in2(bird_wingsdown_1_out_3),
    .in3(bird_wingsdown_1_out_4), .in4(bird_wingsdown_1_out_5), .in5(bird_wingsdown_1_out_6),
    .in6(bird_wingsdown_1_out_7), .in7(bird_wingsdown_1_out_8), .in8(bird_wingsdown_1_out_9),
    .in9(bird_wingsdown_1_out_10), .out(multiplexer_4_out), .sel(counter_1_q), .en(t_ff_1_q));  // open: in10, in11, in12, in13, in14, in15
  Pull_Resistor pull_resistor_4 (.node(multiplexer_4_out));
  Shifter #(.width(32)) shifter_4 (.in(multiplexer_4_out), .\dist (5'b00100), .out(shifter_4_out));
  Shifter #(.width(32)) shifter_5 (.in(multiplexer_4_out), .\dist (5'b00111), .out(shifter_5_out));
  Shifter #(.width(32)) shifter_6 (.in(multiplexer_4_out), .\dist (5'b10000), .out(shifter_6_out));
  Multiplexer #(.select(2), .width(32), .enable("false")) multiplexer_5 (
    .in0(multiplexer_4_out), .in1(shifter_4_out), .in2(shifter_5_out), .in3(shifter_6_out), .out(down),
    .sel(random_2_out));

  // Notes on the sheet:
  //   BIRDS
endmodule

module bird (
  output [31:0] out_1,
  output [31:0] out_2,
  output [31:0] out_3,
  output [31:0] out_4,
  output [31:0] out_5,
  output [31:0] out_6,
  output [31:0] out_7,
  output [31:0] out_8,
  output [31:0] out_9,
  output [31:0] out_10,
  output [31:0] out_11,
  output [31:0] out_12,
  output [31:0] out_13,
  output [31:0] out_14,
  output [31:0] out_15,
  output [31:0] out_16,
  output [31:0] out_17,
  output [31:0] out_18
);

  DotMatrix #(.matrixcols(9), .matrixrows(32)) dotmatrix_1 (
    .col0(32'h8), .col1(32'h18), .col2(32'h18), .col3(32'hc), .col4(32'h7c), .col5(32'h3c), .col6(32'h38),
    .col7(32'h18), .col8(32'h8));
  DotMatrix #(.matrixcols(9), .matrixrows(32)) dotmatrix_2 (
    .col0(32'h8), .col1(32'h18), .col2(32'h18), .col3(32'h8), .col4(32'hf), .col5(32'he), .col6(32'he),
    .col7(32'hc), .col8(32'h8));

  assign out_1 = 32'h8;
  assign out_2 = 32'h18;
  assign out_3 = 32'h18;
  assign out_4 = 32'hc;
  assign out_5 = 32'h7c;
  assign out_6 = 32'h3c;
  assign out_7 = 32'h38;
  assign out_8 = 32'h18;
  assign out_9 = 32'h8;
  assign out_10 = 32'h8;
  assign out_11 = 32'h18;
  assign out_12 = 32'h18;
  assign out_13 = 32'h8;
  assign out_14 = 32'hf;
  assign out_15 = 32'he;
  assign out_16 = 32'he;
  assign out_17 = 32'hc;
  assign out_18 = 32'h8;
endmodule

module bird_wings_up (
  output [31:0] out_1,
  output [31:0] out_2,
  output [31:0] out_3,
  output [31:0] out_4,
  output [31:0] out_5,
  output [31:0] out_6,
  output [31:0] out_7,
  output [31:0] out_8,
  output [31:0] out_9,
  output [31:0] out_10
);

  wire [31:0] shifter_1_out, shifter_2_out, shifter_3_out, shifter_4_out, shifter_5_out, shifter_6_out,
       shifter_7_out, shifter_8_out, shifter_9_out;

  DotMatrix #(.matrixcols(10), .matrixrows(32)) dotmatrix_1 (
    .col0({32{1'b0}}), .col1(32'h8), .col2(32'h18), .col3(32'h18), .col4(32'hc), .col5(32'h7c),
    .col6(32'h3c), .col7(32'h38), .col8(32'h18), .col9(32'h8));
  DotMatrix #(.matrixcols(9), .matrixrows(32)) dotmatrix_2 (
    .col0(shifter_9_out), .col1(shifter_8_out), .col2(shifter_7_out), .col3(shifter_6_out),
    .col4(shifter_5_out), .col5(shifter_4_out), .col6(shifter_3_out), .col7(shifter_2_out),
    .col8(shifter_1_out));
  // Probe on shifter_1_out
  Shifter #(.width(32)) shifter_1 (.in(32'h8), .\dist (5'b00100), .out(shifter_1_out));
  Shifter #(.width(32)) shifter_2 (.in(32'h18), .\dist (5'b00100), .out(shifter_2_out));
  // Probe on shifter_2_out
  // Probe on shifter_3_out
  Shifter #(.width(32)) shifter_3 (.in(32'h38), .\dist (5'b00100), .out(shifter_3_out));
  Shifter #(.width(32)) shifter_4 (.in(32'h3c), .\dist (5'b00100), .out(shifter_4_out));
  // Probe on shifter_4_out
  // Probe on shifter_5_out
  Shifter #(.width(32)) shifter_5 (.in(32'h7c), .\dist (5'b00100), .out(shifter_5_out));
  // Probe on shifter_6_out
  Shifter #(.width(32)) shifter_6 (.in(32'hc), .\dist (5'b00100), .out(shifter_6_out));
  Shifter #(.width(32)) shifter_7 (.in(32'h18), .\dist (5'b00100), .out(shifter_7_out));
  // Probe on shifter_7_out
  Shifter #(.width(32)) shifter_8 (.in(32'h18), .\dist (5'b00100), .out(shifter_8_out));
  // Probe on shifter_8_out
  // Probe on shifter_9_out
  Shifter #(.width(32)) shifter_9 (.in(32'h8), .\dist (5'b00100), .out(shifter_9_out));

  assign out_1 = {32{1'b0}};
  assign out_2 = 32'h8;
  assign out_3 = 32'h18;
  assign out_4 = 32'h18;
  assign out_5 = 32'hc;
  assign out_6 = 32'h7c;
  assign out_7 = 32'h3c;
  assign out_8 = 32'h38;
  assign out_9 = 32'h18;
  assign out_10 = 32'h8;
endmodule

module bird_wingsdown (
  output [31:0] out_1,
  output [31:0] out_2,
  output [31:0] out_3,
  output [31:0] out_4,
  output [31:0] out_5,
  output [31:0] out_6,
  output [31:0] out_7,
  output [31:0] out_8,
  output [31:0] out_9,
  output [31:0] out_10
);

  DotMatrix #(.matrixcols(9), .matrixrows(32)) dotmatrix_1 (
    .col0(32'h8), .col1(32'h18), .col2(32'h18), .col3(32'h8), .col4(32'hf), .col5(32'he), .col6(32'he),
    .col7(32'hc), .col8(32'h8));

  assign out_1 = {32{1'b0}};
  assign out_2 = 32'h8;
  assign out_3 = 32'h18;
  assign out_4 = 32'h18;
  assign out_5 = 32'h8;
  assign out_6 = 32'hf;
  assign out_7 = 32'he;
  assign out_8 = 32'he;
  assign out_9 = 32'hc;
  assign out_10 = 32'h8;
endmodule

module speed (
  input  [3:0] speed,
  output clk
);

  wire _1_LEVEL_out, _2_LEVEL_out, _3_LEVEL_out, _4_LEVEL_out, _5_LEVEL_out;

  Clock #(.lowDuration(6)) _1_LEVEL (.out(_1_LEVEL_out));
  Clock #(.lowDuration(5)) _2_LEVEL (.out(_2_LEVEL_out));
  Clock #(.lowDuration(4)) _3_LEVEL (.out(_3_LEVEL_out));
  Clock #(.lowDuration(3)) _4_LEVEL (.out(_4_LEVEL_out));
  Clock #(.lowDuration(2)) _5_LEVEL (.out(_5_LEVEL_out));
  Multiplexer #(.select(4), .enable("false")) multiplexer_1 (
    .in0(_1_LEVEL_out), .in1(_2_LEVEL_out), .in2(_3_LEVEL_out), .in3(_4_LEVEL_out), .in4(_5_LEVEL_out),
    .out(clk), .sel(speed));  // open: in5, in6, in7, in8, in9, in10, in11, in12, in13, in14, in15

  // Notes on the sheet:
  //   LEVELS
endmodule

module speeddino (
  input  [3:0] speed,
  output clk
);

  wire _1_2_LEVEL_out, _3_5_LEVEL_out;

  Clock #(.lowDuration(20)) _1_2_LEVEL (.out(_1_2_LEVEL_out));
  Clock #(.lowDuration(15)) _3_5_LEVEL (.out(_3_5_LEVEL_out));
  Multiplexer #(.select(4), .enable("false")) multiplexer_1 (
    .in0(_1_2_LEVEL_out), .in1(_1_2_LEVEL_out), .in2(_3_5_LEVEL_out), .in3(_3_5_LEVEL_out),
    .in4(_3_5_LEVEL_out), .out(clk), .sel(speed));  // open: in5, in6, in7, in8, in9, in10, in11, in12, in13, in14, in15

  // Notes on the sheet:
  //   LEVELS
endmodule

module invertor (
  input  switch,
  input  clr,
  input  [31:0] in_3,
  input  [31:0] in_4,
  input  [31:0] in_5,
  input  [31:0] in_6,
  input  [31:0] in_7,
  input  [31:0] in_8,
  input  [31:0] in_9,
  input  [31:0] in_10,
  input  [31:0] in_11,
  input  [31:0] in_12,
  input  [31:0] in_13,
  input  [31:0] in_14,
  input  [31:0] in_15,
  input  [31:0] in_16,
  input  [31:0] in_17,
  input  [31:0] in_18,
  input  [31:0] in_19,
  input  [31:0] in_20,
  input  [31:0] in_21,
  input  [31:0] in_22,
  input  [31:0] in_23,
  input  [31:0] in_24,
  input  [31:0] in_25,
  input  [31:0] in_26,
  input  [31:0] in_27,
  input  [31:0] in_28,
  input  [31:0] in_29,
  input  [31:0] in_30,
  input  [31:0] in_31,
  input  [31:0] in_32,
  input  [31:0] in_33,
  input  [31:0] in_34,
  input  [31:0] in_35,
  input  [31:0] in_36,
  input  [31:0] in_37,
  input  [31:0] in_38,
  input  [31:0] in_39,
  input  [31:0] in_40,
  input  [31:0] in_41,
  input  [31:0] in_42,
  input  [31:0] in_43,
  input  [31:0] in_44,
  input  [31:0] in_45,
  input  [31:0] in_46,
  input  [31:0] in_47,
  input  [31:0] in_48,
  input  [31:0] in_49,
  input  [31:0] in_50,
  input  [31:0] in_51,
  input  [31:0] in_52,
  input  [31:0] in_53,
  input  [31:0] in_54,
  input  [31:0] in_55,
  input  [31:0] in_56,
  input  [31:0] in_57,
  input  [31:0] in_58,
  input  [31:0] in_59,
  input  [31:0] in_60,
  input  [31:0] in_61,
  input  [31:0] in_62,
  input  [31:0] in_63,
  input  [31:0] in_64,
  input  [31:0] in_65,
  input  [31:0] in_66,
  input  [31:0] in_67,
  input  [31:0] in_68,
  input  [31:0] in_69,
  input  [31:0] in_70,
  input  [31:0] in_71,
  input  [31:0] in_72,
  input  [31:0] in_73,
  input  [31:0] in_74,
  input  [31:0] in_75,
  input  [31:0] in_76,
  input  [31:0] in_77,
  input  [31:0] in_78,
  input  [31:0] in_79,
  input  [31:0] in_80,
  input  [31:0] in_81,
  input  [31:0] in_82,
  input  [31:0] in_83,
  input  [31:0] in_84,
  input  [31:0] in_85,
  input  [31:0] in_86,
  input  [31:0] in_87,
  input  [31:0] in_88,
  input  [31:0] in_89,
  input  [31:0] in_90,
  input  [31:0] in_91,
  input  [31:0] in_92,
  input  [31:0] in_93,
  input  [31:0] in_94,
  input  [31:0] in_95,
  input  [31:0] in_96,
  input  [31:0] in_97,
  input  [31:0] in_98,
  input  [31:0] in_99,
  input  [31:0] in_100,
  input  [31:0] in_101,
  input  [31:0] in_102,
  input  [31:0] in_103,
  input  [31:0] in_104,
  input  [31:0] in_105,
  input  [31:0] in_106,
  input  [31:0] in_107,
  input  [31:0] in_108,
  input  [31:0] in_109,
  input  [31:0] in_110,
  input  [31:0] in_111,
  input  [31:0] in_112,
  input  [31:0] in_113,
  input  [31:0] in_114,
  input  [31:0] in_115,
  input  [31:0] in_116,
  input  [31:0] in_117,
  input  [31:0] in_118,
  input  [31:0] in_119,
  input  [31:0] in_120,
  input  [31:0] in_121,
  input  [31:0] in_122,
  input  [31:0] in_123,
  input  [31:0] in_124,
  input  [31:0] in_125,
  input  [31:0] in_126,
  input  [31:0] in_127,
  input  [31:0] in_128,
  input  [31:0] in_129,
  input  [31:0] in_130,
  output [31:0] out_131,
  output [31:0] out_132,
  output [31:0] out_133,
  output [31:0] out_134,
  output [31:0] out_135,
  output [31:0] out_136,
  output [31:0] out_137,
  output [31:0] out_138,
  output [31:0] out_139,
  output [31:0] out_140,
  output [31:0] out_141,
  output [31:0] out_142,
  output [31:0] out_143,
  output [31:0] out_144,
  output [31:0] out_145,
  output [31:0] out_146,
  output [31:0] out_147,
  output [31:0] out_148,
  output [31:0] out_149,
  output [31:0] out_150,
  output [31:0] out_151,
  output [31:0] out_152,
  output [31:0] out_153,
  output [31:0] out_154,
  output [31:0] out_155,
  output [31:0] out_156,
  output [31:0] out_157,
  output [31:0] out_158,
  output [31:0] out_159,
  output [31:0] out_160,
  output [31:0] out_161,
  output [31:0] out_162,
  output [31:0] out_163,
  output [31:0] out_164,
  output [31:0] out_165,
  output [31:0] out_166,
  output [31:0] out_167,
  output [31:0] out_168,
  output [31:0] out_169,
  output [31:0] out_170,
  output [31:0] out_171,
  output [31:0] out_172,
  output [31:0] out_173,
  output [31:0] out_174,
  output [31:0] out_175,
  output [31:0] out_176,
  output [31:0] out_177,
  output [31:0] out_178,
  output [31:0] out_179,
  output [31:0] out_180,
  output [31:0] out_181,
  output [31:0] out_182,
  output [31:0] out_183,
  output [31:0] out_184,
  output [31:0] out_185,
  output [31:0] out_186,
  output [31:0] out_187,
  output [31:0] out_188,
  output [31:0] out_189,
  output [31:0] out_190,
  output [31:0] out_191,
  output [31:0] out_192,
  output [31:0] out_193,
  output [31:0] out_194,
  output [31:0] out_195,
  output [31:0] out_196,
  output [31:0] out_197,
  output [31:0] out_198,
  output [31:0] out_199,
  output [31:0] out_200,
  output [31:0] out_201,
  output [31:0] out_202,
  output [31:0] out_203,
  output [31:0] out_204,
  output [31:0] out_205,
  output [31:0] out_206,
  output [31:0] out_207,
  output [31:0] out_208,
  output [31:0] out_209,
  output [31:0] out_210,
  output [31:0] out_211,
  output [31:0] out_212,
  output [31:0] out_213,
  output [31:0] out_214,
  output [31:0] out_215,
  output [31:0] out_216,
  output [31:0] out_217,
  output [31:0] out_218,
  output [31:0] out_219,
  output [31:0] out_220,
  output [31:0] out_221,
  output [31:0] out_222,
  output [31:0] out_223,
  output [31:0] out_224,
  output [31:0] out_225,
  output [31:0] out_226,
  output [31:0] out_227,
  output [31:0] out_228,
  output [31:0] out_229,
  output [31:0] out_230,
  output [31:0] out_231,
  output [31:0] out_232,
  output [31:0] out_233,
  output [31:0] out_234,
  output [31:0] out_235,
  output [31:0] out_236,
  output [31:0] out_237,
  output [31:0] out_238,
  output [31:0] out_239,
  output [31:0] out_240,
  output [31:0] out_241,
  output [31:0] out_242,
  output [31:0] out_243,
  output [31:0] out_244,
  output [31:0] out_245,
  output [31:0] out_246,
  output [31:0] out_247,
  output [31:0] out_248,
  output [31:0] out_249,
  output [31:0] out_250,
  output [31:0] out_251,
  output [31:0] out_252,
  output [31:0] out_253,
  output [31:0] out_254,
  output [31:0] out_255,
  output [31:0] out_256,
  output [31:0] out_257,
  output [31:0] out_258
);

  wire t_ff_1_q;
  wire [31:0] not_1_out, not_2_out, not_3_out, not_4_out, not_5_out, not_6_out, not_7_out, not_8_out,
       not_9_out, not_10_out, not_11_out, not_12_out, not_13_out, not_14_out, not_15_out, not_16_out,
       not_17_out, not_18_out, not_19_out, not_20_out, not_21_out, not_22_out, not_23_out, not_24_out,
       not_25_out, not_26_out, not_27_out, not_28_out, not_29_out, not_30_out, not_31_out, not_32_out,
       not_33_out, not_34_out, not_35_out, not_36_out, not_37_out, not_38_out, not_39_out, not_40_out,
       not_41_out, not_42_out, not_43_out, not_44_out, not_45_out, not_46_out, not_47_out, not_48_out,
       not_49_out, not_50_out, not_51_out, not_52_out, not_53_out, not_54_out, not_55_out, not_56_out,
       not_57_out, not_58_out, not_59_out, not_60_out, not_61_out, not_62_out, not_63_out, not_64_out,
       not_65_out, not_66_out, not_67_out, not_68_out, not_69_out, not_70_out, not_71_out, not_72_out,
       not_73_out, not_74_out, not_75_out, not_76_out, not_77_out, not_78_out, not_79_out, not_80_out,
       not_81_out, not_82_out, not_83_out, not_84_out, not_85_out, not_86_out, not_87_out, not_88_out,
       not_89_out, not_90_out, not_91_out, not_92_out, not_93_out, not_94_out, not_95_out, not_96_out,
       not_97_out, not_98_out, not_99_out, not_100_out, not_101_out, not_102_out, not_103_out, not_104_out,
       not_105_out, not_106_out, not_107_out, not_108_out, not_109_out, not_110_out, not_111_out,
       not_112_out, not_113_out, not_114_out, not_115_out, not_116_out, not_117_out, not_118_out,
       not_119_out, not_120_out, not_121_out, not_122_out, not_123_out, not_124_out, not_125_out,
       not_126_out, not_127_out, not_128_out;

  T_Flip_Flop t_ff_1 (.clk(switch), .T(switch), .Q(t_ff_1_q), .reset(clr));  // open: Qn, preset, en
  Multiplexer #(.width(32), .enable("false")) multiplexer_1 (
    .in0(in_3), .in1(not_1_out), .out(out_131), .sel(t_ff_1_q));
  assign not_1_out = ~in_3;  // NOT_Gate not_1, 32 bits wide
  Multiplexer #(.width(32), .enable("false")) multiplexer_2 (
    .in0(in_5), .in1(not_3_out), .out(out_133), .sel(t_ff_1_q));
  Multiplexer #(.width(32), .enable("false")) multiplexer_3 (
    .in0(in_4), .in1(not_2_out), .out(out_132), .sel(t_ff_1_q));
  assign not_2_out = ~in_4;  // NOT_Gate not_2, 32 bits wide
  Multiplexer #(.width(32), .enable("false")) multiplexer_4 (
    .in0(in_6), .in1(not_4_out), .out(out_134), .sel(t_ff_1_q));
  assign not_3_out = ~in_5;  // NOT_Gate not_3, 32 bits wide
  assign not_4_out = ~in_6;  // NOT_Gate not_4, 32 bits wide
  Multiplexer #(.width(32), .enable("false")) multiplexer_5 (
    .in0(in_7), .in1(not_5_out), .out(out_135), .sel(t_ff_1_q));
  assign not_5_out = ~in_7;  // NOT_Gate not_5, 32 bits wide
  Multiplexer #(.width(32), .enable("false")) multiplexer_6 (
    .in0(in_9), .in1(not_7_out), .out(out_137), .sel(t_ff_1_q));
  Multiplexer #(.width(32), .enable("false")) multiplexer_7 (
    .in0(in_8), .in1(not_6_out), .out(out_136), .sel(t_ff_1_q));
  assign not_6_out = ~in_8;  // NOT_Gate not_6, 32 bits wide
  Multiplexer #(.width(32), .enable("false")) multiplexer_8 (
    .in0(in_10), .in1(not_8_out), .out(out_138), .sel(t_ff_1_q));
  assign not_7_out = ~in_9;  // NOT_Gate not_7, 32 bits wide
  assign not_8_out = ~in_10;  // NOT_Gate not_8, 32 bits wide
  Multiplexer #(.width(32), .enable("false")) multiplexer_9 (
    .in0(in_11), .in1(not_9_out), .out(out_139), .sel(t_ff_1_q));
  assign not_9_out = ~in_11;  // NOT_Gate not_9, 32 bits wide
  Multiplexer #(.width(32), .enable("false")) multiplexer_10 (
    .in0(in_13), .in1(not_12_out), .out(out_141), .sel(t_ff_1_q));
  Multiplexer #(.width(32), .enable("false")) multiplexer_11 (
    .in0(in_12), .in1(not_10_out), .out(out_140), .sel(t_ff_1_q));
  assign not_10_out = ~in_12;  // NOT_Gate not_10, 32 bits wide
  Multiplexer #(.width(32), .enable("false")) multiplexer_12 (
    .in0(in_14), .in1(not_11_out), .out(out_142), .sel(t_ff_1_q));
  assign not_11_out = ~in_14;  // NOT_Gate not_11, 32 bits wide
  assign not_12_out = ~in_13;  // NOT_Gate not_12, 32 bits wide
  Multiplexer #(.width(32), .enable("false")) multiplexer_13 (
    .in0(in_15), .in1(not_13_out), .out(out_143), .sel(t_ff_1_q));
  assign not_13_out = ~in_15;  // NOT_Gate not_13, 32 bits wide
  Multiplexer #(.width(32), .enable("false")) multiplexer_14 (
    .in0(in_17), .in1(not_15_out), .out(out_145), .sel(t_ff_1_q));
  Multiplexer #(.width(32), .enable("false")) multiplexer_15 (
    .in0(in_16), .in1(not_14_out), .out(out_144), .sel(t_ff_1_q));
  assign not_14_out = ~in_16;  // NOT_Gate not_14, 32 bits wide
  Multiplexer #(.width(32), .enable("false")) multiplexer_16 (
    .in0(in_18), .in1(not_16_out), .out(out_146), .sel(t_ff_1_q));
  assign not_15_out = ~in_17;  // NOT_Gate not_15, 32 bits wide
  assign not_16_out = ~in_18;  // NOT_Gate not_16, 32 bits wide
  Multiplexer #(.width(32), .enable("false")) multiplexer_17 (
    .in0(in_19), .in1(not_17_out), .out(out_147), .sel(t_ff_1_q));
  assign not_17_out = ~in_19;  // NOT_Gate not_17, 32 bits wide
  Multiplexer #(.width(32), .enable("false")) multiplexer_18 (
    .in0(in_21), .in1(not_19_out), .out(out_149), .sel(t_ff_1_q));
  Multiplexer #(.width(32), .enable("false")) multiplexer_19 (
    .in0(in_20), .in1(not_18_out), .out(out_148), .sel(t_ff_1_q));
  assign not_18_out = ~in_20;  // NOT_Gate not_18, 32 bits wide
  assign not_19_out = ~in_21;  // NOT_Gate not_19, 32 bits wide
  Multiplexer #(.width(32), .enable("false")) multiplexer_20 (
    .in0(in_22), .in1(not_20_out), .out(out_150), .sel(t_ff_1_q));
  assign not_20_out = ~in_22;  // NOT_Gate not_20, 32 bits wide
  Multiplexer #(.width(32), .enable("false")) multiplexer_21 (
    .in0(in_23), .in1(not_21_out), .out(out_151), .sel(t_ff_1_q));
  assign not_21_out = ~in_23;  // NOT_Gate not_21, 32 bits wide
  Multiplexer #(.width(32), .enable("false")) multiplexer_22 (
    .in0(in_24), .in1(not_22_out), .out(out_152), .sel(t_ff_1_q));
  Multiplexer #(.width(32), .enable("false")) multiplexer_23 (
    .in0(in_25), .in1(not_23_out), .out(out_153), .sel(t_ff_1_q));
  assign not_22_out = ~in_24;  // NOT_Gate not_22, 32 bits wide
  assign not_23_out = ~in_25;  // NOT_Gate not_23, 32 bits wide
  Multiplexer #(.width(32), .enable("false")) multiplexer_24 (
    .in0(in_26), .in1(not_24_out), .out(out_154), .sel(t_ff_1_q));
  assign not_24_out = ~in_26;  // NOT_Gate not_24, 32 bits wide
  Multiplexer #(.width(32), .enable("false")) multiplexer_25 (
    .in0(in_27), .in1(not_25_out), .out(out_155), .sel(t_ff_1_q));
  assign not_25_out = ~in_27;  // NOT_Gate not_25, 32 bits wide
  Multiplexer #(.width(32), .enable("false")) multiplexer_26 (
    .in0(in_29), .in1(not_27_out), .out(out_157), .sel(t_ff_1_q));
  Multiplexer #(.width(32), .enable("false")) multiplexer_27 (
    .in0(in_28), .in1(not_26_out), .out(out_156), .sel(t_ff_1_q));
  assign not_26_out = ~in_28;  // NOT_Gate not_26, 32 bits wide
  assign not_27_out = ~in_29;  // NOT_Gate not_27, 32 bits wide
  Multiplexer #(.width(32), .enable("false")) multiplexer_28 (
    .in0(in_30), .in1(not_28_out), .out(out_158), .sel(t_ff_1_q));
  assign not_28_out = ~in_30;  // NOT_Gate not_28, 32 bits wide
  Multiplexer #(.width(32), .enable("false")) multiplexer_29 (
    .in0(in_31), .in1(not_29_out), .out(out_159), .sel(t_ff_1_q));
  assign not_29_out = ~in_31;  // NOT_Gate not_29, 32 bits wide
  Multiplexer #(.width(32), .enable("false")) multiplexer_30 (
    .in0(in_33), .in1(not_31_out), .out(out_161), .sel(t_ff_1_q));
  Multiplexer #(.width(32), .enable("false")) multiplexer_31 (
    .in0(in_32), .in1(not_30_out), .out(out_160), .sel(t_ff_1_q));
  assign not_30_out = ~in_32;  // NOT_Gate not_30, 32 bits wide
  assign not_31_out = ~in_33;  // NOT_Gate not_31, 32 bits wide
  Multiplexer #(.width(32), .enable("false")) multiplexer_32 (
    .in0(in_34), .in1(not_32_out), .out(out_162), .sel(t_ff_1_q));
  assign not_32_out = ~in_34;  // NOT_Gate not_32, 32 bits wide
  Multiplexer #(.width(32), .enable("false")) multiplexer_33 (
    .in0(in_36), .in1(not_34_out), .out(out_164), .sel(t_ff_1_q));
  Multiplexer #(.width(32), .enable("false")) multiplexer_34 (
    .in0(in_35), .in1(not_33_out), .out(out_163), .sel(t_ff_1_q));
  assign not_33_out = ~in_35;  // NOT_Gate not_33, 32 bits wide
  Multiplexer #(.width(32), .enable("false")) multiplexer_35 (
    .in0(in_37), .in1(not_35_out), .out(out_165), .sel(t_ff_1_q));
  assign not_34_out = ~in_36;  // NOT_Gate not_34, 32 bits wide
  assign not_35_out = ~in_37;  // NOT_Gate not_35, 32 bits wide
  Multiplexer #(.width(32), .enable("false")) multiplexer_36 (
    .in0(in_38), .in1(not_36_out), .out(out_166), .sel(t_ff_1_q));
  assign not_36_out = ~in_38;  // NOT_Gate not_36, 32 bits wide
  Multiplexer #(.width(32), .enable("false")) multiplexer_37 (
    .in0(in_39), .in1(not_37_out), .out(out_167), .sel(t_ff_1_q));
  Multiplexer #(.width(32), .enable("false")) multiplexer_38 (
    .in0(in_40), .in1(not_39_out), .out(out_168), .sel(t_ff_1_q));
  assign not_37_out = ~in_39;  // NOT_Gate not_37, 32 bits wide
  Multiplexer #(.width(32), .enable("false")) multiplexer_39 (
    .in0(in_41), .in1(not_38_out), .out(out_169), .sel(t_ff_1_q));
  assign not_38_out = ~in_41;  // NOT_Gate not_38, 32 bits wide
  assign not_39_out = ~in_40;  // NOT_Gate not_39, 32 bits wide
  Multiplexer #(.width(32), .enable("false")) multiplexer_40 (
    .in0(in_42), .in1(not_40_out), .out(out_170), .sel(t_ff_1_q));
  assign not_40_out = ~in_42;  // NOT_Gate not_40, 32 bits wide
  Multiplexer #(.width(32), .enable("false")) multiplexer_41 (
    .in0(in_43), .in1(not_41_out), .out(out_171), .sel(t_ff_1_q));
  Multiplexer #(.width(32), .enable("false")) multiplexer_42 (
    .in0(in_44), .in1(not_42_out), .out(out_172), .sel(t_ff_1_q));
  assign not_41_out = ~in_43;  // NOT_Gate not_41, 32 bits wide
  Multiplexer #(.width(32), .enable("false")) multiplexer_43 (
    .in0(in_45), .in1(not_43_out), .out(out_173), .sel(t_ff_1_q));
  assign not_42_out = ~in_44;  // NOT_Gate not_42, 32 bits wide
  assign not_43_out = ~in_45;  // NOT_Gate not_43, 32 bits wide
  Multiplexer #(.width(32), .enable("false")) multiplexer_44 (
    .in0(in_46), .in1(not_44_out), .out(out_174), .sel(t_ff_1_q));
  assign not_44_out = ~in_46;  // NOT_Gate not_44, 32 bits wide
  Multiplexer #(.width(32), .enable("false")) multiplexer_45 (
    .in0(in_48), .in1(not_46_out), .out(out_176), .sel(t_ff_1_q));
  Multiplexer #(.width(32), .enable("false")) multiplexer_46 (
    .in0(in_47), .in1(not_45_out), .out(out_175), .sel(t_ff_1_q));
  assign not_45_out = ~in_47;  // NOT_Gate not_45, 32 bits wide
  Multiplexer #(.width(32), .enable("false")) multiplexer_47 (
    .in0(in_49), .in1(not_47_out), .out(out_177), .sel(t_ff_1_q));
  assign not_46_out = ~in_48;  // NOT_Gate not_46, 32 bits wide
  assign not_47_out = ~in_49;  // NOT_Gate not_47, 32 bits wide
  Multiplexer #(.width(32), .enable("false")) multiplexer_48 (
    .in0(in_50), .in1(not_48_out), .out(out_178), .sel(t_ff_1_q));
  assign not_48_out = ~in_50;  // NOT_Gate not_48, 32 bits wide
  Multiplexer #(.width(32), .enable("false")) multiplexer_49 (
    .in0(in_51), .in1(not_49_out), .out(out_179), .sel(t_ff_1_q));
  Multiplexer #(.width(32), .enable("false")) multiplexer_50 (
    .in0(in_52), .in1(not_50_out), .out(out_180), .sel(t_ff_1_q));
  assign not_49_out = ~in_51;  // NOT_Gate not_49, 32 bits wide
  assign not_50_out = ~in_52;  // NOT_Gate not_50, 32 bits wide
  Multiplexer #(.width(32), .enable("false")) multiplexer_51 (
    .in0(in_53), .in1(not_51_out), .out(out_181), .sel(t_ff_1_q));
  assign not_51_out = ~in_53;  // NOT_Gate not_51, 32 bits wide
  Multiplexer #(.width(32), .enable("false")) multiplexer_52 (
    .in0(in_54), .in1(not_52_out), .out(out_182), .sel(t_ff_1_q));
  assign not_52_out = ~in_54;  // NOT_Gate not_52, 32 bits wide
  Multiplexer #(.width(32), .enable("false")) multiplexer_53 (
    .in0(in_56), .in1(not_53_out), .out(out_184), .sel(t_ff_1_q));
  Multiplexer #(.width(32), .enable("false")) multiplexer_54 (
    .in0(in_55), .in1(not_54_out), .out(out_183), .sel(t_ff_1_q));
  assign not_53_out = ~in_56;  // NOT_Gate not_53, 32 bits wide
  assign not_54_out = ~in_55;  // NOT_Gate not_54, 32 bits wide
  Multiplexer #(.width(32), .enable("false")) multiplexer_55 (
    .in0(in_57), .in1(not_55_out), .out(out_185), .sel(t_ff_1_q));
  assign not_55_out = ~in_57;  // NOT_Gate not_55, 32 bits wide
  Multiplexer #(.width(32), .enable("false")) multiplexer_56 (
    .in0(in_58), .in1(not_56_out), .out(out_186), .sel(t_ff_1_q));
  assign not_56_out = ~in_58;  // NOT_Gate not_56, 32 bits wide
  Multiplexer #(.width(32), .enable("false")) multiplexer_57 (
    .in0(in_59), .in1(not_57_out), .out(out_187), .sel(t_ff_1_q));
  Multiplexer #(.width(32), .enable("false")) multiplexer_58 (
    .in0(in_60), .in1(not_58_out), .out(out_188), .sel(t_ff_1_q));
  assign not_57_out = ~in_59;  // NOT_Gate not_57, 32 bits wide
  assign not_58_out = ~in_60;  // NOT_Gate not_58, 32 bits wide
  Multiplexer #(.width(32), .enable("false")) multiplexer_59 (
    .in0(in_61), .in1(not_59_out), .out(out_189), .sel(t_ff_1_q));
  assign not_59_out = ~in_61;  // NOT_Gate not_59, 32 bits wide
  Multiplexer #(.width(32), .enable("false")) multiplexer_60 (
    .in0(in_62), .in1(not_60_out), .out(out_190), .sel(t_ff_1_q));
  assign not_60_out = ~in_62;  // NOT_Gate not_60, 32 bits wide
  Multiplexer #(.width(32), .enable("false")) multiplexer_61 (
    .in0(in_63), .in1(not_61_out), .out(out_191), .sel(t_ff_1_q));
  Multiplexer #(.width(32), .enable("false")) multiplexer_62 (
    .in0(in_64), .in1(not_62_out), .out(out_192), .sel(t_ff_1_q));
  assign not_61_out = ~in_63;  // NOT_Gate not_61, 32 bits wide
  assign not_62_out = ~in_64;  // NOT_Gate not_62, 32 bits wide
  Multiplexer #(.width(32), .enable("false")) multiplexer_63 (
    .in0(in_65), .in1(not_63_out), .out(out_193), .sel(t_ff_1_q));
  assign not_63_out = ~in_65;  // NOT_Gate not_63, 32 bits wide
  Multiplexer #(.width(32), .enable("false")) multiplexer_64 (
    .in0(in_66), .in1(not_64_out), .out(out_194), .sel(t_ff_1_q));
  assign not_64_out = ~in_66;  // NOT_Gate not_64, 32 bits wide
  Multiplexer #(.width(32), .enable("false")) multiplexer_65 (
    .in0(in_67), .in1(not_65_out), .out(out_195), .sel(t_ff_1_q));
  assign not_65_out = ~in_67;  // NOT_Gate not_65, 32 bits wide
  Multiplexer #(.width(32), .enable("false")) multiplexer_66 (
    .in0(in_69), .in1(not_67_out), .out(out_197), .sel(t_ff_1_q));
  Multiplexer #(.width(32), .enable("false")) multiplexer_67 (
    .in0(in_68), .in1(not_66_out), .out(out_196), .sel(t_ff_1_q));
  assign not_66_out = ~in_68;  // NOT_Gate not_66, 32 bits wide
  assign not_67_out = ~in_69;  // NOT_Gate not_67, 32 bits wide
  Multiplexer #(.width(32), .enable("false")) multiplexer_68 (
    .in0(in_70), .in1(not_68_out), .out(out_198), .sel(t_ff_1_q));
  assign not_68_out = ~in_70;  // NOT_Gate not_68, 32 bits wide
  Multiplexer #(.width(32), .enable("false")) multiplexer_69 (
    .in0(in_71), .in1(not_69_out), .out(out_199), .sel(t_ff_1_q));
  assign not_69_out = ~in_71;  // NOT_Gate not_69, 32 bits wide
  Multiplexer #(.width(32), .enable("false")) multiplexer_70 (
    .in0(in_72), .in1(not_71_out), .out(out_200), .sel(t_ff_1_q));
  Multiplexer #(.width(32), .enable("false")) multiplexer_71 (
    .in0(in_73), .in1(not_70_out), .out(out_201), .sel(t_ff_1_q));
  assign not_70_out = ~in_73;  // NOT_Gate not_70, 32 bits wide
  assign not_71_out = ~in_72;  // NOT_Gate not_71, 32 bits wide
  Multiplexer #(.width(32), .enable("false")) multiplexer_72 (
    .in0(in_74), .in1(not_72_out), .out(out_202), .sel(t_ff_1_q));
  assign not_72_out = ~in_74;  // NOT_Gate not_72, 32 bits wide
  Multiplexer #(.width(32), .enable("false")) multiplexer_73 (
    .in0(in_75), .in1(not_73_out), .out(out_203), .sel(t_ff_1_q));
  assign not_73_out = ~in_75;  // NOT_Gate not_73, 32 bits wide
  Multiplexer #(.width(32), .enable("false")) multiplexer_74 (
    .in0(in_77), .in1(not_75_out), .out(out_205), .sel(t_ff_1_q));
  Multiplexer #(.width(32), .enable("false")) multiplexer_75 (
    .in0(in_76), .in1(not_74_out), .out(out_204), .sel(t_ff_1_q));
  assign not_74_out = ~in_76;  // NOT_Gate not_74, 32 bits wide
  assign not_75_out = ~in_77;  // NOT_Gate not_75, 32 bits wide
  Multiplexer #(.width(32), .enable("false")) multiplexer_76 (
    .in0(in_78), .in1(not_76_out), .out(out_206), .sel(t_ff_1_q));
  assign not_76_out = ~in_78;  // NOT_Gate not_76, 32 bits wide
  Multiplexer #(.width(32), .enable("false")) multiplexer_77 (
    .in0(in_79), .in1(not_77_out), .out(out_207), .sel(t_ff_1_q));
  assign not_77_out = ~in_79;  // NOT_Gate not_77, 32 bits wide
  Multiplexer #(.width(32), .enable("false")) multiplexer_78 (
    .in0(in_81), .in1(not_79_out), .out(out_209), .sel(t_ff_1_q));
  Multiplexer #(.width(32), .enable("false")) multiplexer_79 (
    .in0(in_80), .in1(not_78_out), .out(out_208), .sel(t_ff_1_q));
  assign not_78_out = ~in_80;  // NOT_Gate not_78, 32 bits wide
  assign not_79_out = ~in_81;  // NOT_Gate not_79, 32 bits wide
  Multiplexer #(.width(32), .enable("false")) multiplexer_80 (
    .in0(in_82), .in1(not_80_out), .out(out_210), .sel(t_ff_1_q));
  assign not_80_out = ~in_82;  // NOT_Gate not_80, 32 bits wide
  Multiplexer #(.width(32), .enable("false")) multiplexer_81 (
    .in0(in_83), .in1(not_81_out), .out(out_211), .sel(t_ff_1_q));
  Multiplexer #(.width(32), .enable("false")) multiplexer_82 (
    .in0(in_84), .in1(not_82_out), .out(out_212), .sel(t_ff_1_q));
  assign not_81_out = ~in_83;  // NOT_Gate not_81, 32 bits wide
  Multiplexer #(.width(32), .enable("false")) multiplexer_83 (
    .in0(in_85), .in1(not_83_out), .out(out_213), .sel(t_ff_1_q));
  assign not_82_out = ~in_84;  // NOT_Gate not_82, 32 bits wide
  assign not_83_out = ~in_85;  // NOT_Gate not_83, 32 bits wide
  Multiplexer #(.width(32), .enable("false")) multiplexer_84 (
    .in0(in_86), .in1(not_84_out), .out(out_214), .sel(t_ff_1_q));
  assign not_84_out = ~in_86;  // NOT_Gate not_84, 32 bits wide
  Multiplexer #(.width(32), .enable("false")) multiplexer_85 (
    .in0(in_88), .in1(not_87_out), .out(out_216), .sel(t_ff_1_q));
  Multiplexer #(.width(32), .enable("false")) multiplexer_86 (
    .in0(in_87), .in1(not_85_out), .out(out_215), .sel(t_ff_1_q));
  assign not_85_out = ~in_87;  // NOT_Gate not_85, 32 bits wide
  Multiplexer #(.width(32), .enable("false")) multiplexer_87 (
    .in0(in_89), .in1(not_86_out), .out(out_217), .sel(t_ff_1_q));
  assign not_86_out = ~in_89;  // NOT_Gate not_86, 32 bits wide
  assign not_87_out = ~in_88;  // NOT_Gate not_87, 32 bits wide
  Multiplexer #(.width(32), .enable("false")) multiplexer_88 (
    .in0(in_90), .in1(not_88_out), .out(out_218), .sel(t_ff_1_q));
  assign not_88_out = ~in_90;  // NOT_Gate not_88, 32 bits wide
  Multiplexer #(.width(32), .enable("false")) multiplexer_89 (
    .in0(in_91), .in1(not_89_out), .out(out_219), .sel(t_ff_1_q));
  Multiplexer #(.width(32), .enable("false")) multiplexer_90 (
    .in0(in_92), .in1(not_91_out), .out(out_220), .sel(t_ff_1_q));
  assign not_89_out = ~in_91;  // NOT_Gate not_89, 32 bits wide
  Multiplexer #(.width(32), .enable("false")) multiplexer_91 (
    .in0(in_93), .in1(not_90_out), .out(out_221), .sel(t_ff_1_q));
  assign not_90_out = ~in_93;  // NOT_Gate not_90, 32 bits wide
  assign not_91_out = ~in_92;  // NOT_Gate not_91, 32 bits wide
  Multiplexer #(.width(32), .enable("false")) multiplexer_92 (
    .in0(in_94), .in1(not_92_out), .out(out_222), .sel(t_ff_1_q));
  assign not_92_out = ~in_94;  // NOT_Gate not_92, 32 bits wide
  Multiplexer #(.width(32), .enable("false")) multiplexer_93 (
    .in0(in_96), .in1(not_94_out), .out(out_224), .sel(t_ff_1_q));
  Multiplexer #(.width(32), .enable("false")) multiplexer_94 (
    .in0(in_95), .in1(not_93_out), .out(out_223), .sel(t_ff_1_q));
  assign not_93_out = ~in_95;  // NOT_Gate not_93, 32 bits wide
  Multiplexer #(.width(32), .enable("false")) multiplexer_95 (
    .in0(in_97), .in1(not_95_out), .out(out_225), .sel(t_ff_1_q));
  assign not_94_out = ~in_96;  // NOT_Gate not_94, 32 bits wide
  assign not_95_out = ~in_97;  // NOT_Gate not_95, 32 bits wide
  Multiplexer #(.width(32), .enable("false")) multiplexer_96 (
    .in0(in_98), .in1(not_96_out), .out(out_226), .sel(t_ff_1_q));
  assign not_96_out = ~in_98;  // NOT_Gate not_96, 32 bits wide
  Multiplexer #(.width(32), .enable("false")) multiplexer_97 (
    .in0(in_100), .in1(not_97_out), .out(out_228), .sel(t_ff_1_q));
  Multiplexer #(.width(32), .enable("false")) multiplexer_98 (
    .in0(in_99), .in1(not_98_out), .out(out_227), .sel(t_ff_1_q));
  assign not_97_out = ~in_100;  // NOT_Gate not_97, 32 bits wide
  assign not_98_out = ~in_99;  // NOT_Gate not_98, 32 bits wide
  Multiplexer #(.width(32), .enable("false")) multiplexer_99 (
    .in0(in_101), .in1(not_99_out), .out(out_229), .sel(t_ff_1_q));
  assign not_99_out = ~in_101;  // NOT_Gate not_99, 32 bits wide
  Multiplexer #(.width(32), .enable("false")) multiplexer_100 (
    .in0(in_102), .in1(not_100_out), .out(out_230), .sel(t_ff_1_q));
  assign not_100_out = ~in_102;  // NOT_Gate not_100, 32 bits wide
  Multiplexer #(.width(32), .enable("false")) multiplexer_101 (
    .in0(in_104), .in1(not_102_out), .out(out_232), .sel(t_ff_1_q));
  Multiplexer #(.width(32), .enable("false")) multiplexer_102 (
    .in0(in_103), .in1(not_101_out), .out(out_231), .sel(t_ff_1_q));
  assign not_101_out = ~in_103;  // NOT_Gate not_101, 32 bits wide
  assign not_102_out = ~in_104;  // NOT_Gate not_102, 32 bits wide
  Multiplexer #(.width(32), .enable("false")) multiplexer_103 (
    .in0(in_105), .in1(not_103_out), .out(out_233), .sel(t_ff_1_q));
  assign not_103_out = ~in_105;  // NOT_Gate not_103, 32 bits wide
  Multiplexer #(.width(32), .enable("false")) multiplexer_104 (
    .in0(in_106), .in1(not_104_out), .out(out_234), .sel(t_ff_1_q));
  assign not_104_out = ~in_106;  // NOT_Gate not_104, 32 bits wide
  Multiplexer #(.width(32), .enable("false")) multiplexer_105 (
    .in0(in_107), .in1(not_105_out), .out(out_235), .sel(t_ff_1_q));
  Multiplexer #(.width(32), .enable("false")) multiplexer_106 (
    .in0(in_108), .in1(not_106_out), .out(out_236), .sel(t_ff_1_q));
  assign not_105_out = ~in_107;  // NOT_Gate not_105, 32 bits wide
  assign not_106_out = ~in_108;  // NOT_Gate not_106, 32 bits wide
  Multiplexer #(.width(32), .enable("false")) multiplexer_107 (
    .in0(in_109), .in1(not_107_out), .out(out_237), .sel(t_ff_1_q));
  assign not_107_out = ~in_109;  // NOT_Gate not_107, 32 bits wide
  Multiplexer #(.width(32), .enable("false")) multiplexer_108 (
    .in0(in_110), .in1(not_108_out), .out(out_238), .sel(t_ff_1_q));
  assign not_108_out = ~in_110;  // NOT_Gate not_108, 32 bits wide
  Multiplexer #(.width(32), .enable("false")) multiplexer_109 (
    .in0(in_112), .in1(not_110_out), .out(out_240), .sel(t_ff_1_q));
  Multiplexer #(.width(32), .enable("false")) multiplexer_110 (
    .in0(in_111), .in1(not_109_out), .out(out_239), .sel(t_ff_1_q));
  assign not_109_out = ~in_111;  // NOT_Gate not_109, 32 bits wide
  assign not_110_out = ~in_112;  // NOT_Gate not_110, 32 bits wide
  Multiplexer #(.width(32), .enable("false")) multiplexer_111 (
    .in0(in_113), .in1(not_111_out), .out(out_241), .sel(t_ff_1_q));
  assign not_111_out = ~in_113;  // NOT_Gate not_111, 32 bits wide
  Multiplexer #(.width(32), .enable("false")) multiplexer_112 (
    .in0(in_114), .in1(not_112_out), .out(out_242), .sel(t_ff_1_q));
  Multiplexer #(.width(32), .enable("false")) multiplexer_113 (
    .in0(in_115), .in1(not_114_out), .out(out_243), .sel(t_ff_1_q));
  assign not_112_out = ~in_114;  // NOT_Gate not_112, 32 bits wide
  Multiplexer #(.width(32), .enable("false")) multiplexer_114 (
    .in0(in_116), .in1(not_113_out), .out(out_244), .sel(t_ff_1_q));
  assign not_113_out = ~in_116;  // NOT_Gate not_113, 32 bits wide
  assign not_114_out = ~in_115;  // NOT_Gate not_114, 32 bits wide
  Multiplexer #(.width(32), .enable("false")) multiplexer_115 (
    .in0(in_117), .in1(not_115_out), .out(out_245), .sel(t_ff_1_q));
  assign not_115_out = ~in_117;  // NOT_Gate not_115, 32 bits wide
  Multiplexer #(.width(32), .enable("false")) multiplexer_116 (
    .in0(in_118), .in1(not_116_out), .out(out_246), .sel(t_ff_1_q));
  Multiplexer #(.width(32), .enable("false")) multiplexer_117 (
    .in0(in_119), .in1(not_117_out), .out(out_247), .sel(t_ff_1_q));
  assign not_116_out = ~in_118;  // NOT_Gate not_116, 32 bits wide
  Multiplexer #(.width(32), .enable("false")) multiplexer_118 (
    .in0(in_120), .in1(not_118_out), .out(out_248), .sel(t_ff_1_q));
  assign not_117_out = ~in_119;  // NOT_Gate not_117, 32 bits wide
  assign not_118_out = ~in_120;  // NOT_Gate not_118, 32 bits wide
  Multiplexer #(.width(32), .enable("false")) multiplexer_119 (
    .in0(in_121), .in1(not_119_out), .out(out_249), .sel(t_ff_1_q));
  assign not_119_out = ~in_121;  // NOT_Gate not_119, 32 bits wide
  Multiplexer #(.width(32), .enable("false")) multiplexer_120 (
    .in0(in_123), .in1(not_121_out), .out(out_251), .sel(t_ff_1_q));
  Multiplexer #(.width(32), .enable("false")) multiplexer_121 (
    .in0(in_122), .in1(not_120_out), .out(out_250), .sel(t_ff_1_q));
  assign not_120_out = ~in_122;  // NOT_Gate not_120, 32 bits wide
  Multiplexer #(.width(32), .enable("false")) multiplexer_122 (
    .in0(in_124), .in1(not_122_out), .out(out_252), .sel(t_ff_1_q));
  assign not_121_out = ~in_123;  // NOT_Gate not_121, 32 bits wide
  assign not_122_out = ~in_124;  // NOT_Gate not_122, 32 bits wide
  Multiplexer #(.width(32), .enable("false")) multiplexer_123 (
    .in0(in_125), .in1(not_123_out), .out(out_253), .sel(t_ff_1_q));
  assign not_123_out = ~in_125;  // NOT_Gate not_123, 32 bits wide
  Multiplexer #(.width(32), .enable("false")) multiplexer_124 (
    .in0(in_127), .in1(not_125_out), .out(out_255), .sel(t_ff_1_q));
  Multiplexer #(.width(32), .enable("false")) multiplexer_125 (
    .in0(in_126), .in1(not_124_out), .out(out_254), .sel(t_ff_1_q));
  assign not_124_out = ~in_126;  // NOT_Gate not_124, 32 bits wide
  Multiplexer #(.width(32), .enable("false")) multiplexer_126 (
    .in0(in_128), .in1(not_126_out), .out(out_256), .sel(t_ff_1_q));
  assign not_125_out = ~in_127;  // NOT_Gate not_125, 32 bits wide
  assign not_126_out = ~in_128;  // NOT_Gate not_126, 32 bits wide
  Multiplexer #(.width(32), .enable("false")) multiplexer_127 (
    .in0(in_129), .in1(not_127_out), .out(out_257), .sel(t_ff_1_q));
  assign not_127_out = ~in_129;  // NOT_Gate not_127, 32 bits wide
  Multiplexer #(.width(32), .enable("false")) multiplexer_128 (
    .in0(in_130), .in1(not_128_out), .out(out_258), .sel(t_ff_1_q));
  assign not_128_out = ~in_130;  // NOT_Gate not_128, 32 bits wide
endmodule
module gameover (
  input  is_gameover,
  input  [31:0] in_2,
  input  [31:0] in_3,
  input  [31:0] in_4,
  input  [31:0] in_5,
  input  [31:0] in_6,
  input  [31:0] in_7,
  input  [31:0] in_8,
  input  [31:0] in_9,
  input  [31:0] in_10,
  input  [31:0] in_11,
  input  [31:0] in_12,
  input  [31:0] in_13,
  input  [31:0] in_14,
  input  [31:0] in_15,
  input  [31:0] in_16,
  input  [31:0] in_17,
  input  [31:0] in_18,
  input  [31:0] in_19,
  input  [31:0] in_20,
  input  [31:0] in_21,
  input  [31:0] in_22,
  input  [31:0] in_23,
  input  [31:0] in_24,
  input  [31:0] in_25,
  input  [31:0] in_26,
  input  [31:0] in_27,
  input  [31:0] in_28,
  input  [31:0] in_29,
  input  [31:0] in_30,
  input  [31:0] in_31,
  input  [31:0] in_32,
  input  [31:0] in_33,
  input  [31:0] in_34,
  input  [31:0] in_35,
  input  [31:0] in_36,
  input  [31:0] in_37,
  input  [31:0] in_38,
  input  [31:0] in_39,
  input  [31:0] in_40,
  input  [31:0] in_41,
  input  [31:0] in_42,
  input  [31:0] in_43,
  input  [31:0] in_44,
  input  [31:0] in_45,
  input  [31:0] in_46,
  input  [31:0] in_47,
  input  [31:0] in_48,
  input  [31:0] in_49,
  input  [31:0] in_50,
  input  [31:0] in_51,
  input  [31:0] in_52,
  input  [31:0] in_53,
  input  [31:0] in_54,
  input  [31:0] in_55,
  input  [31:0] in_56,
  input  [31:0] in_57,
  input  [31:0] in_58,
  input  [31:0] in_59,
  input  [31:0] in_60,
  input  [31:0] in_61,
  input  [31:0] in_62,
  input  [31:0] in_63,
  input  [31:0] in_64,
  input  [31:0] in_65,
  output [31:0] out_66,
  output [31:0] out_67,
  output [31:0] out_68,
  output [31:0] out_69,
  output [31:0] out_70,
  output [31:0] out_71,
  output [31:0] out_72,
  output [31:0] out_73,
  output [31:0] out_74,
  output [31:0] out_75,
  output [31:0] out_76,
  output [31:0] out_77,
  output [31:0] out_78,
  output [31:0] out_79,
  output [31:0] out_80,
  output [31:0] out_81,
  output [31:0] out_82,
  output [31:0] out_83,
  output [31:0] out_84,
  output [31:0] out_85,
  output [31:0] out_86,
  output [31:0] out_87,
  output [31:0] out_88,
  output [31:0] out_89,
  output [31:0] out_90,
  output [31:0] out_91,
  output [31:0] out_92,
  output [31:0] out_93,
  output [31:0] out_94,
  output [31:0] out_95,
  output [31:0] out_96,
  output [31:0] out_97,
  output [31:0] out_98,
  output [31:0] out_99,
  output [31:0] out_100,
  output [31:0] out_101,
  output [31:0] out_102,
  output [31:0] out_103,
  output [31:0] out_104,
  output [31:0] out_105,
  output [31:0] out_106,
  output [31:0] out_107,
  output [31:0] out_108,
  output [31:0] out_109,
  output [31:0] out_110,
  output [31:0] out_111,
  output [31:0] out_112,
  output [31:0] out_113,
  output [31:0] out_114,
  output [31:0] out_115,
  output [31:0] out_116,
  output [31:0] out_117,
  output [31:0] out_118,
  output [31:0] out_119,
  output [31:0] out_120,
  output [31:0] out_121,
  output [31:0] out_122,
  output [31:0] out_123,
  output [31:0] out_124,
  output [31:0] out_125,
  output [31:0] out_126,
  output [31:0] out_127,
  output [31:0] out_128,
  output [31:0] out_129
);

  wire [31:0] xor_1_out, xor_2_out, xor_3_out, xor_4_out, xor_5_out, xor_6_out, xor_7_out, xor_8_out,
       xor_9_out, xor_10_out, xor_11_out, xor_12_out, xor_13_out, xor_14_out, xor_15_out, xor_16_out,
       xor_17_out, xor_18_out, xor_19_out, xor_20_out, xor_21_out, xor_22_out, xor_23_out, xor_24_out,
       xor_25_out, xor_26_out, xor_27_out, xor_28_out, xor_29_out, xor_30_out, xor_31_out, xor_32_out,
       xor_33_out, xor_34_out, xor_35_out, xor_36_out, xor_37_out, xor_38_out, xor_39_out, xor_40_out,
       xor_41_out, xor_42_out, xor_43_out, xor_44_out, xor_45_out, xor_46_out, xor_47_out, xor_48_out,
       xor_49_out, xor_50_out, xor_51_out, xor_52_out, xor_53_out, xor_54_out, xor_55_out, xor_56_out,
       xor_57_out, xor_58_out, xor_59_out, xor_60_out, xor_61_out, xor_62_out, xor_63_out, xor_64_out;

  Multiplexer #(.width(32), .enable("false")) multiplexer_1 (
    .in0(in_2), .in1(xor_1_out), .out(out_66), .sel(is_gameover));
  assign xor_1_out = in_2 ^ {32{1'b0}};  // XOR_Gate xor_1, 32 bits wide
  Pull_Resistor pull_resistor_1 (.node(in_2));
  DotMatrix #(.matrixcols(32), .matrixrows(32)) dotmatrix_1 (
    .col0({32{1'b0}}), .col1({32{1'b0}}), .col2({32{1'b0}}), .col3({32{1'b0}}), .col4({32{1'b0}}),
    .col5({32{1'b0}}), .col6({32{1'b0}}), .col7({32{1'b0}}), .col8(32'hfe000), .col9(32'h82000),
    .col10(32'h82000), .col11(32'h92000), .col12(32'h9e000), .col13({32{1'b0}}), .col14(32'h7e000),
    .col15(32'h90000), .col16(32'h90000), .col17(32'h90000), .col18(32'h7e000), .col19({32{1'b0}}),
    .col20(32'hfe000), .col21(32'h40000), .col22(32'h20000), .col23(32'h40000), .col24(32'hfe000),
    .col25({32{1'b0}}), .col26(32'hfe000), .col27(32'h92000), .col28(32'h92000), .col29(32'h92000),
    .col30(32'h92000), .col31({32{1'b0}}));
  Multiplexer #(.width(32), .enable("false")) multiplexer_2 (
    .in0(in_3), .in1(xor_2_out), .out(out_67), .sel(is_gameover));
  assign xor_2_out = in_3 ^ {32{1'b0}};  // XOR_Gate xor_2, 32 bits wide
  Pull_Resistor pull_resistor_2 (.node(in_3));
  Multiplexer #(.width(32), .enable("false")) multiplexer_3 (
    .in0(in_4), .in1(xor_3_out), .out(out_68), .sel(is_gameover));
  assign xor_3_out = in_4 ^ {32{1'b0}};  // XOR_Gate xor_3, 32 bits wide
  Pull_Resistor pull_resistor_3 (.node(in_4));
  Multiplexer #(.width(32), .enable("false")) multiplexer_4 (
    .in0(in_5), .in1(xor_4_out), .out(out_69), .sel(is_gameover));
  assign xor_4_out = in_5 ^ {32{1'b0}};  // XOR_Gate xor_4, 32 bits wide
  Pull_Resistor pull_resistor_4 (.node(in_5));
  DotMatrix #(.matrixcols(32), .matrixrows(32)) dotmatrix_2 (
    .col0({32{1'b0}}), .col1(32'hfe000), .col2(32'h82000), .col3(32'h82000), .col4(32'h82000),
    .col5(32'hfe000), .col6({32{1'b0}}), .col7(32'hf8000), .col8(32'h4000), .col9(32'h2000),
    .col10(32'h4000), .col11(32'hf8000), .col12({32{1'b0}}), .col13(32'hfe000), .col14(32'h92000),
    .col15(32'h92000), .col16(32'h92000), .col17(32'h92000), .col18({32{1'b0}}), .col19(32'hfe000),
    .col20(32'h90000), .col21(32'h90000), .col22(32'h90000), .col23(32'h6e000), .col24({32{1'b0}}),
    .col25({32{1'b0}}), .col26({32{1'b0}}), .col27({32{1'b0}}), .col28({32{1'b0}}), .col29({32{1'b0}}),
    .col30({32{1'b0}}), .col31({32{1'b0}}));
  Multiplexer #(.width(32), .enable("false")) multiplexer_5 (
    .in0(in_6), .in1(xor_5_out), .out(out_70), .sel(is_gameover));
  assign xor_5_out = in_6 ^ {32{1'b0}};  // XOR_Gate xor_5, 32 bits wide
  Pull_Resistor pull_resistor_5 (.node(in_6));
  Multiplexer #(.width(32), .enable("false")) multiplexer_6 (
    .in0(in_7), .in1(xor_6_out), .out(out_71), .sel(is_gameover));
  assign xor_6_out = in_7 ^ {32{1'b0}};  // XOR_Gate xor_6, 32 bits wide
  Pull_Resistor pull_resistor_6 (.node(in_7));
  Multiplexer #(.width(32), .enable("false")) multiplexer_7 (
    .in0(in_8), .in1(xor_7_out), .out(out_72), .sel(is_gameover));
  assign xor_7_out = in_8 ^ {32{1'b0}};  // XOR_Gate xor_7, 32 bits wide
  Pull_Resistor pull_resistor_7 (.node(in_8));
  Multiplexer #(.width(32), .enable("false")) multiplexer_8 (
    .in0(in_9), .in1(xor_8_out), .out(out_73), .sel(is_gameover));
  assign xor_8_out = in_9 ^ {32{1'b0}};  // XOR_Gate xor_8, 32 bits wide
  Pull_Resistor pull_resistor_8 (.node(in_9));
  Multiplexer #(.width(32), .enable("false")) multiplexer_9 (
    .in0(in_10), .in1(xor_9_out), .out(out_74), .sel(is_gameover));
  assign xor_9_out = in_10 ^ 32'hfe000;  // XOR_Gate xor_9, 32 bits wide
  Pull_Resistor pull_resistor_9 (.node(in_10));
  Multiplexer #(.width(32), .enable("false")) multiplexer_10 (
    .in0(in_11), .in1(xor_10_out), .out(out_75), .sel(is_gameover));
  assign xor_10_out = in_11 ^ 32'h82000;  // XOR_Gate xor_10, 32 bits wide
  Pull_Resistor pull_resistor_10 (.node(in_11));
  Multiplexer #(.width(32), .enable("false")) multiplexer_11 (
    .in0(in_12), .in1(xor_11_out), .out(out_76), .sel(is_gameover));
  assign xor_11_out = in_12 ^ 32'h82000;  // XOR_Gate xor_11, 32 bits wide
  Pull_Resistor pull_resistor_11 (.node(in_12));
  Multiplexer #(.width(32), .enable("false")) multiplexer_12 (
    .in0(in_13), .in1(xor_12_out), .out(out_77), .sel(is_gameover));
  assign xor_12_out = in_13 ^ 32'h92000;  // XOR_Gate xor_12, 32 bits wide
  Pull_Resistor pull_resistor_12 (.node(in_13));
  Multiplexer #(.width(32), .enable("false")) multiplexer_13 (
    .in0(in_14), .in1(xor_13_out), .out(out_78), .sel(is_gameover));
  assign xor_13_out = in_14 ^ 32'h9e000;  // XOR_Gate xor_13, 32 bits wide
  Pull_Resistor pull_resistor_13 (.node(in_14));
  Multiplexer #(.width(32), .enable("false")) multiplexer_14 (
    .in0(in_15), .in1(xor_14_out), .out(out_79), .sel(is_gameover));
  assign xor_14_out = in_15 ^ {32{1'b0}};  // XOR_Gate xor_14, 32 bits wide
  Pull_Resistor pull_resistor_14 (.node(in_15));
  Multiplexer #(.width(32), .enable("false")) multiplexer_15 (
    .in0(in_16), .in1(xor_15_out), .out(out_80), .sel(is_gameover));
  assign xor_15_out = in_16 ^ 32'h7e000;  // XOR_Gate xor_15, 32 bits wide
  Pull_Resistor pull_resistor_15 (.node(in_16));
  Multiplexer #(.width(32), .enable("false")) multiplexer_16 (
    .in0(in_17), .in1(xor_16_out), .out(out_81), .sel(is_gameover));
  assign xor_16_out = in_17 ^ 32'h90000;  // XOR_Gate xor_16, 32 bits wide
  Pull_Resistor pull_resistor_16 (.node(in_17));
  Multiplexer #(.width(32), .enable("false")) multiplexer_17 (
    .in0(in_18), .in1(xor_17_out), .out(out_82), .sel(is_gameover));
  assign xor_17_out = in_18 ^ 32'h90000;  // XOR_Gate xor_17, 32 bits wide
  Pull_Resistor pull_resistor_17 (.node(in_18));
  Multiplexer #(.width(32), .enable("false")) multiplexer_18 (
    .in0(in_19), .in1(xor_18_out), .out(out_83), .sel(is_gameover));
  assign xor_18_out = in_19 ^ 32'h90000;  // XOR_Gate xor_18, 32 bits wide
  Pull_Resistor pull_resistor_18 (.node(in_19));
  Multiplexer #(.width(32), .enable("false")) multiplexer_19 (
    .in0(in_20), .in1(xor_19_out), .out(out_84), .sel(is_gameover));
  assign xor_19_out = in_20 ^ 32'h7e000;  // XOR_Gate xor_19, 32 bits wide
  Pull_Resistor pull_resistor_19 (.node(in_20));
  Multiplexer #(.width(32), .enable("false")) multiplexer_20 (
    .in0(in_21), .in1(xor_20_out), .out(out_85), .sel(is_gameover));
  assign xor_20_out = in_21 ^ {32{1'b0}};  // XOR_Gate xor_20, 32 bits wide
  Pull_Resistor pull_resistor_20 (.node(in_21));
  Multiplexer #(.width(32), .enable("false")) multiplexer_21 (
    .in0(in_22), .in1(xor_21_out), .out(out_86), .sel(is_gameover));
  assign xor_21_out = in_22 ^ 32'hfe000;  // XOR_Gate xor_21, 32 bits wide
  Pull_Resistor pull_resistor_21 (.node(in_22));
  Multiplexer #(.width(32), .enable("false")) multiplexer_22 (
    .in0(in_23), .in1(xor_22_out), .out(out_87), .sel(is_gameover));
  assign xor_22_out = in_23 ^ 32'h40000;  // XOR_Gate xor_22, 32 bits wide
  Pull_Resistor pull_resistor_22 (.node(in_23));
  Multiplexer #(.width(32), .enable("false")) multiplexer_23 (
    .in0(in_24), .in1(xor_23_out), .out(out_88), .sel(is_gameover));
  assign xor_23_out = in_24 ^ 32'h20000;  // XOR_Gate xor_23, 32 bits wide
  Pull_Resistor pull_resistor_23 (.node(in_24));
  Multiplexer #(.width(32), .enable("false")) multiplexer_24 (
    .in0(in_25), .in1(xor_24_out), .out(out_89), .sel(is_gameover));
  assign xor_24_out = in_25 ^ 32'h40000;  // XOR_Gate xor_24, 32 bits wide
  Pull_Resistor pull_resistor_24 (.node(in_25));
  Multiplexer #(.width(32), .enable("false")) multiplexer_25 (
    .in0(in_26), .in1(xor_25_out), .out(out_90), .sel(is_gameover));
  assign xor_25_out = in_26 ^ 32'hfe000;  // XOR_Gate xor_25, 32 bits wide
  Pull_Resistor pull_resistor_25 (.node(in_26));
  Multiplexer #(.width(32), .enable("false")) multiplexer_26 (
    .in0(in_27), .in1(xor_26_out), .out(out_91), .sel(is_gameover));
  assign xor_26_out = in_27 ^ {32{1'b0}};  // XOR_Gate xor_26, 32 bits wide
  Pull_Resistor pull_resistor_26 (.node(in_27));
  Multiplexer #(.width(32), .enable("false")) multiplexer_27 (
    .in0(in_28), .in1(xor_27_out), .out(out_92), .sel(is_gameover));
  assign xor_27_out = in_28 ^ 32'hfe000;  // XOR_Gate xor_27, 32 bits wide
  Pull_Resistor pull_resistor_27 (.node(in_28));
  Multiplexer #(.width(32), .enable("false")) multiplexer_28 (
    .in0(in_29), .in1(xor_28_out), .out(out_93), .sel(is_gameover));
  assign xor_28_out = in_29 ^ 32'h92000;  // XOR_Gate xor_28, 32 bits wide
  Pull_Resistor pull_resistor_28 (.node(in_29));
  Multiplexer #(.width(32), .enable("false")) multiplexer_29 (
    .in0(in_30), .in1(xor_29_out), .out(out_94), .sel(is_gameover));
  assign xor_29_out = in_30 ^ 32'h92000;  // XOR_Gate xor_29, 32 bits wide
  Pull_Resistor pull_resistor_29 (.node(in_30));
  Multiplexer #(.width(32), .enable("false")) multiplexer_30 (
    .in0(in_31), .in1(xor_30_out), .out(out_95), .sel(is_gameover));
  assign xor_30_out = in_31 ^ 32'h92000;  // XOR_Gate xor_30, 32 bits wide
  Pull_Resistor pull_resistor_30 (.node(in_31));
  Multiplexer #(.width(32), .enable("false")) multiplexer_31 (
    .in0(in_32), .in1(xor_31_out), .out(out_96), .sel(is_gameover));
  assign xor_31_out = in_32 ^ 32'h92000;  // XOR_Gate xor_31, 32 bits wide
  Pull_Resistor pull_resistor_31 (.node(in_32));
  Multiplexer #(.width(32), .enable("false")) multiplexer_32 (
    .in0(in_33), .in1(xor_32_out), .out(out_97), .sel(is_gameover));
  assign xor_32_out = in_33 ^ {32{1'b0}};  // XOR_Gate xor_32, 32 bits wide
  Pull_Resistor pull_resistor_32 (.node(in_33));
  Multiplexer #(.width(32), .enable("false")) multiplexer_33 (
    .in0(in_34), .in1(xor_33_out), .out(out_98), .sel(is_gameover));
  assign xor_33_out = in_34 ^ {32{1'b0}};  // XOR_Gate xor_33, 32 bits wide
  Pull_Resistor pull_resistor_33 (.node(in_34));
  Multiplexer #(.width(32), .enable("false")) multiplexer_34 (
    .in0(in_35), .in1(xor_34_out), .out(out_99), .sel(is_gameover));
  assign xor_34_out = in_35 ^ 32'hfe000;  // XOR_Gate xor_34, 32 bits wide
  Pull_Resistor pull_resistor_34 (.node(in_35));
  Multiplexer #(.width(32), .enable("false")) multiplexer_35 (
    .in0(in_36), .in1(xor_35_out), .out(out_100), .sel(is_gameover));
  assign xor_35_out = in_36 ^ 32'h82000;  // XOR_Gate xor_35, 32 bits wide
  Pull_Resistor pull_resistor_35 (.node(in_36));
  Multiplexer #(.width(32), .enable("false")) multiplexer_36 (
    .in0(in_37), .in1(xor_36_out), .out(out_101), .sel(is_gameover));
  assign xor_36_out = in_37 ^ 32'h82000;  // XOR_Gate xor_36, 32 bits wide
  Pull_Resistor pull_resistor_36 (.node(in_37));
  Multiplexer #(.width(32), .enable("false")) multiplexer_37 (
    .in0(in_38), .in1(xor_37_out), .out(out_102), .sel(is_gameover));
  assign xor_37_out = in_38 ^ 32'h82000;  // XOR_Gate xor_37, 32 bits wide
  Pull_Resistor pull_resistor_37 (.node(in_38));
  Multiplexer #(.width(32), .enable("false")) multiplexer_38 (
    .in0(in_39), .in1(xor_38_out), .out(out_103), .sel(is_gameover));
  assign xor_38_out = in_39 ^ 32'hfe000;  // XOR_Gate xor_38, 32 bits wide
  Pull_Resistor pull_resistor_38 (.node(in_39));
  Multiplexer #(.width(32), .enable("false")) multiplexer_39 (
    .in0(in_40), .in1(xor_39_out), .out(out_104), .sel(is_gameover));
  assign xor_39_out = in_40 ^ {32{1'b0}};  // XOR_Gate xor_39, 32 bits wide
  Pull_Resistor pull_resistor_39 (.node(in_40));
  Multiplexer #(.width(32), .enable("false")) multiplexer_40 (
    .in0(in_41), .in1(xor_40_out), .out(out_105), .sel(is_gameover));
  assign xor_40_out = in_41 ^ 32'hf8000;  // XOR_Gate xor_40, 32 bits wide
  Pull_Resistor pull_resistor_40 (.node(in_41));
  Multiplexer #(.width(32), .enable("false")) multiplexer_41 (
    .in0(in_42), .in1(xor_41_out), .out(out_106), .sel(is_gameover));
  assign xor_41_out = in_42 ^ 32'h4000;  // XOR_Gate xor_41, 32 bits wide
  Pull_Resistor pull_resistor_41 (.node(in_42));
  Multiplexer #(.width(32), .enable("false")) multiplexer_42 (
    .in0(in_43), .in1(xor_42_out), .out(out_107), .sel(is_gameover));
  assign xor_42_out = in_43 ^ 32'h2000;  // XOR_Gate xor_42, 32 bits wide
  Pull_Resistor pull_resistor_42 (.node(in_43));
  Multiplexer #(.width(32), .enable("false")) multiplexer_43 (
    .in0(in_44), .in1(xor_43_out), .out(out_108), .sel(is_gameover));
  assign xor_43_out = in_44 ^ 32'h4000;  // XOR_Gate xor_43, 32 bits wide
  Pull_Resistor pull_resistor_43 (.node(in_44));
  Multiplexer #(.width(32), .enable("false")) multiplexer_44 (
    .in0(in_45), .in1(xor_44_out), .out(out_109), .sel(is_gameover));
  assign xor_44_out = in_45 ^ 32'hf8000;  // XOR_Gate xor_44, 32 bits wide
  Pull_Resistor pull_resistor_44 (.node(in_45));
  Multiplexer #(.width(32), .enable("false")) multiplexer_45 (
    .in0(in_46), .in1(xor_45_out), .out(out_110), .sel(is_gameover));
  assign xor_45_out = in_46 ^ {32{1'b0}};  // XOR_Gate xor_45, 32 bits wide
  Pull_Resistor pull_resistor_45 (.node(in_46));
  Multiplexer #(.width(32), .enable("false")) multiplexer_46 (
    .in0(in_47), .in1(xor_46_out), .out(out_111), .sel(is_gameover));
  assign xor_46_out = in_47 ^ 32'hfe000;  // XOR_Gate xor_46, 32 bits wide
  Pull_Resistor pull_resistor_46 (.node(in_47));
  Multiplexer #(.width(32), .enable("false")) multiplexer_47 (
    .in0(in_48), .in1(xor_47_out), .out(out_112), .sel(is_gameover));
  assign xor_47_out = in_48 ^ 32'h92000;  // XOR_Gate xor_47, 32 bits wide
  Pull_Resistor pull_resistor_47 (.node(in_48));
  Multiplexer #(.width(32), .enable("false")) multiplexer_48 (
    .in0(in_49), .in1(xor_48_out), .out(out_113), .sel(is_gameover));
  assign xor_48_out = in_49 ^ 32'h92000;  // XOR_Gate xor_48, 32 bits wide
  Pull_Resistor pull_resistor_48 (.node(in_49));
  Multiplexer #(.width(32), .enable("false")) multiplexer_49 (
    .in0(in_50), .in1(xor_49_out), .out(out_114), .sel(is_gameover));
  assign xor_49_out = in_50 ^ 32'h92000;  // XOR_Gate xor_49, 32 bits wide
  Pull_Resistor pull_resistor_49 (.node(in_50));
  Multiplexer #(.width(32), .enable("false")) multiplexer_50 (
    .in0(in_51), .in1(xor_50_out), .out(out_115), .sel(is_gameover));
  assign xor_50_out = in_51 ^ 32'h92000;  // XOR_Gate xor_50, 32 bits wide
  Pull_Resistor pull_resistor_50 (.node(in_51));
  Multiplexer #(.width(32), .enable("false")) multiplexer_51 (
    .in0(in_52), .in1(xor_51_out), .out(out_116), .sel(is_gameover));
  assign xor_51_out = in_52 ^ {32{1'b0}};  // XOR_Gate xor_51, 32 bits wide
  Pull_Resistor pull_resistor_51 (.node(in_52));
  Multiplexer #(.width(32), .enable("false")) multiplexer_52 (
    .in0(in_53), .in1(xor_52_out), .out(out_117), .sel(is_gameover));
  assign xor_52_out = in_53 ^ 32'hfe000;  // XOR_Gate xor_52, 32 bits wide
  Pull_Resistor pull_resistor_52 (.node(in_53));
  Multiplexer #(.width(32), .enable("false")) multiplexer_53 (
    .in0(in_54), .in1(xor_53_out), .out(out_118), .sel(is_gameover));
  assign xor_53_out = in_54 ^ 32'h90000;  // XOR_Gate xor_53, 32 bits wide
  Pull_Resistor pull_resistor_53 (.node(in_54));
  Multiplexer #(.width(32), .enable("false")) multiplexer_54 (
    .in0(in_55), .in1(xor_54_out), .out(out_119), .sel(is_gameover));
  assign xor_54_out = in_55 ^ 32'h90000;  // XOR_Gate xor_54, 32 bits wide
  Pull_Resistor pull_resistor_54 (.node(in_55));
  Multiplexer #(.width(32), .enable("false")) multiplexer_55 (
    .in0(in_56), .in1(xor_55_out), .out(out_120), .sel(is_gameover));
  assign xor_55_out = in_56 ^ 32'h90000;  // XOR_Gate xor_55, 32 bits wide
  Pull_Resistor pull_resistor_55 (.node(in_56));
  Multiplexer #(.width(32), .enable("false")) multiplexer_56 (
    .in0(in_57), .in1(xor_56_out), .out(out_121), .sel(is_gameover));
  assign xor_56_out = in_57 ^ 32'h6e000;  // XOR_Gate xor_56, 32 bits wide
  Pull_Resistor pull_resistor_56 (.node(in_57));
  Multiplexer #(.width(32), .enable("false")) multiplexer_57 (
    .in0(in_58), .in1(xor_57_out), .out(out_122), .sel(is_gameover));
  assign xor_57_out = in_58 ^ {32{1'b0}};  // XOR_Gate xor_57, 32 bits wide
  Pull_Resistor pull_resistor_57 (.node(in_58));
  Multiplexer #(.width(32), .enable("false")) multiplexer_58 (
    .in0(in_59), .in1(xor_58_out), .out(out_123), .sel(is_gameover));
  assign xor_58_out = in_59 ^ {32{1'b0}};  // XOR_Gate xor_58, 32 bits wide
  Pull_Resistor pull_resistor_58 (.node(in_59));
  Multiplexer #(.width(32), .enable("false")) multiplexer_59 (
    .in0(in_60), .in1(xor_59_out), .out(out_124), .sel(is_gameover));
  assign xor_59_out = in_60 ^ {32{1'b0}};  // XOR_Gate xor_59, 32 bits wide
  Pull_Resistor pull_resistor_59 (.node(in_60));
  Multiplexer #(.width(32), .enable("false")) multiplexer_60 (
    .in0(in_61), .in1(xor_60_out), .out(out_125), .sel(is_gameover));
  assign xor_60_out = in_61 ^ {32{1'b0}};  // XOR_Gate xor_60, 32 bits wide
  Pull_Resistor pull_resistor_60 (.node(in_61));
  Multiplexer #(.width(32), .enable("false")) multiplexer_61 (
    .in0(in_62), .in1(xor_61_out), .out(out_126), .sel(is_gameover));
  assign xor_61_out = in_62 ^ {32{1'b0}};  // XOR_Gate xor_61, 32 bits wide
  Pull_Resistor pull_resistor_61 (.node(in_62));
  Multiplexer #(.width(32), .enable("false")) multiplexer_62 (
    .in0(in_63), .in1(xor_62_out), .out(out_127), .sel(is_gameover));
  assign xor_62_out = in_63 ^ {32{1'b0}};  // XOR_Gate xor_62, 32 bits wide
  Pull_Resistor pull_resistor_62 (.node(in_63));
  Multiplexer #(.width(32), .enable("false")) multiplexer_63 (
    .in0(in_64), .in1(xor_63_out), .out(out_128), .sel(is_gameover));
  assign xor_63_out = in_64 ^ {32{1'b0}};  // XOR_Gate xor_63, 32 bits wide
  Pull_Resistor pull_resistor_63 (.node(in_64));
  Multiplexer #(.width(32), .enable("false")) multiplexer_64 (
    .in0(in_65), .in1(xor_64_out), .out(out_129), .sel(is_gameover));
  assign xor_64_out = in_65 ^ {32{1'b0}};  // XOR_Gate xor_64, 32 bits wide
  Pull_Resistor pull_resistor_64 (.node(in_65));
endmodule

module pause (
  input  is_pause,
  input  [31:0] in_2,
  input  [31:0] in_3,
  input  [31:0] in_4,
  input  [31:0] in_5,
  input  [31:0] in_6,
  input  [31:0] in_7,
  input  [31:0] in_8,
  input  [31:0] in_9,
  input  [31:0] in_10,
  input  [31:0] in_11,
  input  [31:0] in_12,
  input  [31:0] in_13,
  input  [31:0] in_14,
  input  [31:0] in_15,
  input  [31:0] in_16,
  input  [31:0] in_17,
  input  [31:0] in_18,
  input  [31:0] in_19,
  input  [31:0] in_20,
  input  [31:0] in_21,
  input  [31:0] in_22,
  input  [31:0] in_23,
  input  [31:0] in_24,
  input  [31:0] in_25,
  input  [31:0] in_26,
  input  [31:0] in_27,
  input  [31:0] in_28,
  input  [31:0] in_29,
  input  [31:0] in_30,
  input  [31:0] in_31,
  input  [31:0] in_32,
  input  [31:0] in_33,
  input  [31:0] in_34,
  input  [31:0] in_35,
  input  [31:0] in_36,
  input  [31:0] in_37,
  input  [31:0] in_38,
  input  [31:0] in_39,
  input  [31:0] in_40,
  input  [31:0] in_41,
  input  [31:0] in_42,
  input  [31:0] in_43,
  input  [31:0] in_44,
  input  [31:0] in_45,
  input  [31:0] in_46,
  input  [31:0] in_47,
  input  [31:0] in_48,
  input  [31:0] in_49,
  input  [31:0] in_50,
  input  [31:0] in_51,
  input  [31:0] in_52,
  input  [31:0] in_53,
  input  [31:0] in_54,
  input  [31:0] in_55,
  input  [31:0] in_56,
  input  [31:0] in_57,
  input  [31:0] in_58,
  input  [31:0] in_59,
  input  [31:0] in_60,
  input  [31:0] in_61,
  input  [31:0] in_62,
  input  [31:0] in_63,
  input  [31:0] in_64,
  input  [31:0] in_65,
  output [31:0] out_66,
  output [31:0] out_67,
  output [31:0] out_68,
  output [31:0] out_69,
  output [31:0] out_70,
  output [31:0] out_71,
  output [31:0] out_72,
  output [31:0] out_73,
  output [31:0] out_74,
  output [31:0] out_75,
  output [31:0] out_76,
  output [31:0] out_77,
  output [31:0] out_78,
  output [31:0] out_79,
  output [31:0] out_80,
  output [31:0] out_81,
  output [31:0] out_82,
  output [31:0] out_83,
  output [31:0] out_84,
  output [31:0] out_85,
  output [31:0] out_86,
  output [31:0] out_87,
  output [31:0] out_88,
  output [31:0] out_89,
  output [31:0] out_90,
  output [31:0] out_91,
  output [31:0] out_92,
  output [31:0] out_93,
  output [31:0] out_94,
  output [31:0] out_95,
  output [31:0] out_96,
  output [31:0] out_97,
  output [31:0] out_98,
  output [31:0] out_99,
  output [31:0] out_100,
  output [31:0] out_101,
  output [31:0] out_102,
  output [31:0] out_103,
  output [31:0] out_104,
  output [31:0] out_105,
  output [31:0] out_106,
  output [31:0] out_107,
  output [31:0] out_108,
  output [31:0] out_109,
  output [31:0] out_110,
  output [31:0] out_111,
  output [31:0] out_112,
  output [31:0] out_113,
  output [31:0] out_114,
  output [31:0] out_115,
  output [31:0] out_116,
  output [31:0] out_117,
  output [31:0] out_118,
  output [31:0] out_119,
  output [31:0] out_120,
  output [31:0] out_121,
  output [31:0] out_122,
  output [31:0] out_123,
  output [31:0] out_124,
  output [31:0] out_125,
  output [31:0] out_126,
  output [31:0] out_127,
  output [31:0] out_128,
  output [31:0] out_129
);

  wire [31:0] xor_1_out, xor_2_out, xor_3_out, xor_4_out, xor_5_out, xor_6_out, xor_7_out, xor_8_out,
       xor_9_out, xor_10_out, xor_11_out, xor_12_out, xor_13_out, xor_14_out, xor_15_out, xor_16_out,
       xor_17_out, xor_18_out, xor_19_out, xor_20_out, xor_21_out, xor_22_out, xor_23_out, xor_24_out,
       xor_25_out, xor_26_out, xor_27_out, xor_28_out, xor_29_out, xor_30_out, xor_31_out, xor_32_out,
       xor_33_out, xor_34_out, xor_35_out, xor_36_out, xor_37_out, xor_38_out, xor_39_out, xor_40_out,
       xor_41_out, xor_42_out, xor_43_out, xor_44_out, xor_45_out, xor_46_out, xor_47_out, xor_48_out,
       xor_49_out, xor_50_out, xor_51_out, xor_52_out, xor_53_out, xor_54_out, xor_55_out, xor_56_out,
       xor_57_out, xor_58_out, xor_59_out, xor_60_out, xor_61_out, xor_62_out, xor_63_out, xor_64_out;

  Multiplexer #(.width(32), .enable("false")) multiplexer_1 (.in0(in_2), .in1(xor_1_out), .out(out_66), .sel(is_pause));
  assign xor_1_out = in_2 ^ {32{1'b0}};  // XOR_Gate xor_1, 32 bits wide
  Pull_Resistor pull_resistor_1 (.node(in_2));
  DotMatrix #(.matrixcols(32), .matrixrows(32)) dotmatrix_1 (
    .col0({32{1'b0}}), .col1({32{1'b0}}), .col2({32{1'b0}}), .col3({32{1'b0}}), .col4({32{1'b0}}),
    .col5({32{1'b0}}), .col6({32{1'b0}}), .col7({32{1'b0}}), .col8({32{1'b0}}), .col9({32{1'b0}}),
    .col10({32{1'b0}}), .col11({32{1'b0}}), .col12({32{1'b0}}), .col13({32{1'b0}}), .col14({32{1'b0}}),
    .col15({32{1'b0}}), .col16({32{1'b0}}), .col17(32'hfe000), .col18(32'h90000), .col19(32'h90000),
    .col20(32'h90000), .col21(32'h60000), .col22({32{1'b0}}), .col23(32'h7e000), .col24(32'h90000),
    .col25(32'h90000), .col26(32'h90000), .col27(32'h7e000), .col28({32{1'b0}}), .col29(32'hfc000),
    .col30(32'h2000), .col31(32'h2000));
  Multiplexer #(.width(32), .enable("false")) multiplexer_2 (.in0(in_3), .in1(xor_2_out), .out(out_67), .sel(is_pause));
  assign xor_2_out = in_3 ^ {32{1'b0}};  // XOR_Gate xor_2, 32 bits wide
  Pull_Resistor pull_resistor_2 (.node(in_3));
  Multiplexer #(.width(32), .enable("false")) multiplexer_3 (.in0(in_4), .in1(xor_3_out), .out(out_68), .sel(is_pause));
  assign xor_3_out = in_4 ^ {32{1'b0}};  // XOR_Gate xor_3, 32 bits wide
  Pull_Resistor pull_resistor_3 (.node(in_4));
  Multiplexer #(.width(32), .enable("false")) multiplexer_4 (.in0(in_5), .in1(xor_4_out), .out(out_69), .sel(is_pause));
  assign xor_4_out = in_5 ^ {32{1'b0}};  // XOR_Gate xor_4, 32 bits wide
  Pull_Resistor pull_resistor_4 (.node(in_5));
  DotMatrix #(.matrixcols(32), .matrixrows(32)) dotmatrix_2 (
    .col0(32'h2000), .col1(32'hfc000), .col2({32{1'b0}}), .col3(32'h62000), .col4(32'h92000),
    .col5(32'h92000), .col6(32'h92000), .col7(32'h8c000), .col8({32{1'b0}}), .col9(32'hfe000),
    .col10(32'h92000), .col11(32'h92000), .col12(32'h92000), .col13(32'h92000), .col14({32{1'b0}}),
    .col15({32{1'b0}}), .col16({32{1'b0}}), .col17({32{1'b0}}), .col18({32{1'b0}}), .col19({32{1'b0}}),
    .col20({32{1'b0}}), .col21({32{1'b0}}), .col22({32{1'b0}}), .col23({32{1'b0}}), .col24({32{1'b0}}),
    .col25({32{1'b0}}), .col26({32{1'b0}}), .col27({32{1'b0}}), .col28({32{1'b0}}), .col29({32{1'b0}}),
    .col30({32{1'b0}}), .col31({32{1'b0}}));
  Multiplexer #(.width(32), .enable("false")) multiplexer_5 (.in0(in_6), .in1(xor_5_out), .out(out_70), .sel(is_pause));
  assign xor_5_out = in_6 ^ {32{1'b0}};  // XOR_Gate xor_5, 32 bits wide
  Pull_Resistor pull_resistor_5 (.node(in_6));
  Multiplexer #(.width(32), .enable("false")) multiplexer_6 (.in0(in_7), .in1(xor_6_out), .out(out_71), .sel(is_pause));
  assign xor_6_out = in_7 ^ {32{1'b0}};  // XOR_Gate xor_6, 32 bits wide
  Pull_Resistor pull_resistor_6 (.node(in_7));
  Multiplexer #(.width(32), .enable("false")) multiplexer_7 (.in0(in_8), .in1(xor_7_out), .out(out_72), .sel(is_pause));
  assign xor_7_out = in_8 ^ {32{1'b0}};  // XOR_Gate xor_7, 32 bits wide
  Pull_Resistor pull_resistor_7 (.node(in_8));
  Multiplexer #(.width(32), .enable("false")) multiplexer_8 (.in0(in_9), .in1(xor_8_out), .out(out_73), .sel(is_pause));
  assign xor_8_out = in_9 ^ {32{1'b0}};  // XOR_Gate xor_8, 32 bits wide
  Pull_Resistor pull_resistor_8 (.node(in_9));
  Multiplexer #(.width(32), .enable("false")) multiplexer_9 (
    .in0(in_10), .in1(xor_9_out), .out(out_74), .sel(is_pause));
  assign xor_9_out = in_10 ^ {32{1'b0}};  // XOR_Gate xor_9, 32 bits wide
  Pull_Resistor pull_resistor_9 (.node(in_10));
  Multiplexer #(.width(32), .enable("false")) multiplexer_10 (
    .in0(in_11), .in1(xor_10_out), .out(out_75), .sel(is_pause));
  assign xor_10_out = in_11 ^ {32{1'b0}};  // XOR_Gate xor_10, 32 bits wide
  Pull_Resistor pull_resistor_10 (.node(in_11));
  Multiplexer #(.width(32), .enable("false")) multiplexer_11 (
    .in0(in_12), .in1(xor_11_out), .out(out_76), .sel(is_pause));
  assign xor_11_out = in_12 ^ {32{1'b0}};  // XOR_Gate xor_11, 32 bits wide
  Pull_Resistor pull_resistor_11 (.node(in_12));
  Multiplexer #(.width(32), .enable("false")) multiplexer_12 (
    .in0(in_13), .in1(xor_12_out), .out(out_77), .sel(is_pause));
  assign xor_12_out = in_13 ^ {32{1'b0}};  // XOR_Gate xor_12, 32 bits wide
  Pull_Resistor pull_resistor_12 (.node(in_13));
  Multiplexer #(.width(32), .enable("false")) multiplexer_13 (
    .in0(in_14), .in1(xor_13_out), .out(out_78), .sel(is_pause));
  assign xor_13_out = in_14 ^ {32{1'b0}};  // XOR_Gate xor_13, 32 bits wide
  Pull_Resistor pull_resistor_13 (.node(in_14));
  Multiplexer #(.width(32), .enable("false")) multiplexer_14 (
    .in0(in_15), .in1(xor_14_out), .out(out_79), .sel(is_pause));
  assign xor_14_out = in_15 ^ {32{1'b0}};  // XOR_Gate xor_14, 32 bits wide
  Pull_Resistor pull_resistor_14 (.node(in_15));
  Multiplexer #(.width(32), .enable("false")) multiplexer_15 (
    .in0(in_16), .in1(xor_15_out), .out(out_80), .sel(is_pause));
  assign xor_15_out = in_16 ^ {32{1'b0}};  // XOR_Gate xor_15, 32 bits wide
  Pull_Resistor pull_resistor_15 (.node(in_16));
  Multiplexer #(.width(32), .enable("false")) multiplexer_16 (
    .in0(in_17), .in1(xor_16_out), .out(out_81), .sel(is_pause));
  assign xor_16_out = in_17 ^ {32{1'b0}};  // XOR_Gate xor_16, 32 bits wide
  Pull_Resistor pull_resistor_16 (.node(in_17));
  Multiplexer #(.width(32), .enable("false")) multiplexer_17 (
    .in0(in_18), .in1(xor_17_out), .out(out_82), .sel(is_pause));
  assign xor_17_out = in_18 ^ {32{1'b0}};  // XOR_Gate xor_17, 32 bits wide
  Pull_Resistor pull_resistor_17 (.node(in_18));
  Multiplexer #(.width(32), .enable("false")) multiplexer_18 (
    .in0(in_19), .in1(xor_18_out), .out(out_83), .sel(is_pause));
  assign xor_18_out = in_19 ^ 32'hfe000;  // XOR_Gate xor_18, 32 bits wide
  Pull_Resistor pull_resistor_18 (.node(in_19));
  Multiplexer #(.width(32), .enable("false")) multiplexer_19 (
    .in0(in_20), .in1(xor_19_out), .out(out_84), .sel(is_pause));
  assign xor_19_out = in_20 ^ 32'h90000;  // XOR_Gate xor_19, 32 bits wide
  Pull_Resistor pull_resistor_19 (.node(in_20));
  Multiplexer #(.width(32), .enable("false")) multiplexer_20 (
    .in0(in_21), .in1(xor_20_out), .out(out_85), .sel(is_pause));
  assign xor_20_out = in_21 ^ 32'h90000;  // XOR_Gate xor_20, 32 bits wide
  Pull_Resistor pull_resistor_20 (.node(in_21));
  Multiplexer #(.width(32), .enable("false")) multiplexer_21 (
    .in0(in_22), .in1(xor_21_out), .out(out_86), .sel(is_pause));
  assign xor_21_out = in_22 ^ 32'h90000;  // XOR_Gate xor_21, 32 bits wide
  Pull_Resistor pull_resistor_21 (.node(in_22));
  Multiplexer #(.width(32), .enable("false")) multiplexer_22 (
    .in0(in_23), .in1(xor_22_out), .out(out_87), .sel(is_pause));
  assign xor_22_out = in_23 ^ 32'h60000;  // XOR_Gate xor_22, 32 bits wide
  Pull_Resistor pull_resistor_22 (.node(in_23));
  Multiplexer #(.width(32), .enable("false")) multiplexer_23 (
    .in0(in_24), .in1(xor_23_out), .out(out_88), .sel(is_pause));
  assign xor_23_out = in_24 ^ {32{1'b0}};  // XOR_Gate xor_23, 32 bits wide
  Pull_Resistor pull_resistor_23 (.node(in_24));
  Multiplexer #(.width(32), .enable("false")) multiplexer_24 (
    .in0(in_25), .in1(xor_24_out), .out(out_89), .sel(is_pause));
  assign xor_24_out = in_25 ^ 32'h7e000;  // XOR_Gate xor_24, 32 bits wide
  Pull_Resistor pull_resistor_24 (.node(in_25));
  Multiplexer #(.width(32), .enable("false")) multiplexer_25 (
    .in0(in_26), .in1(xor_25_out), .out(out_90), .sel(is_pause));
  assign xor_25_out = in_26 ^ 32'h90000;  // XOR_Gate xor_25, 32 bits wide
  Pull_Resistor pull_resistor_25 (.node(in_26));
  Multiplexer #(.width(32), .enable("false")) multiplexer_26 (
    .in0(in_27), .in1(xor_26_out), .out(out_91), .sel(is_pause));
  assign xor_26_out = in_27 ^ 32'h90000;  // XOR_Gate xor_26, 32 bits wide
  Pull_Resistor pull_resistor_26 (.node(in_27));
  Multiplexer #(.width(32), .enable("false")) multiplexer_27 (
    .in0(in_28), .in1(xor_27_out), .out(out_92), .sel(is_pause));
  assign xor_27_out = in_28 ^ 32'h90000;  // XOR_Gate xor_27, 32 bits wide
  Pull_Resistor pull_resistor_27 (.node(in_28));
  Multiplexer #(.width(32), .enable("false")) multiplexer_28 (
    .in0(in_29), .in1(xor_28_out), .out(out_93), .sel(is_pause));
  assign xor_28_out = in_29 ^ 32'h7e000;  // XOR_Gate xor_28, 32 bits wide
  Pull_Resistor pull_resistor_28 (.node(in_29));
  Multiplexer #(.width(32), .enable("false")) multiplexer_29 (
    .in0(in_30), .in1(xor_29_out), .out(out_94), .sel(is_pause));
  assign xor_29_out = in_30 ^ {32{1'b0}};  // XOR_Gate xor_29, 32 bits wide
  Pull_Resistor pull_resistor_29 (.node(in_30));
  Multiplexer #(.width(32), .enable("false")) multiplexer_30 (
    .in0(in_31), .in1(xor_30_out), .out(out_95), .sel(is_pause));
  assign xor_30_out = in_31 ^ 32'hfc000;  // XOR_Gate xor_30, 32 bits wide
  Pull_Resistor pull_resistor_30 (.node(in_31));
  Multiplexer #(.width(32), .enable("false")) multiplexer_31 (
    .in0(in_32), .in1(xor_31_out), .out(out_96), .sel(is_pause));
  assign xor_31_out = in_32 ^ 32'h2000;  // XOR_Gate xor_31, 32 bits wide
  Pull_Resistor pull_resistor_31 (.node(in_32));
  Multiplexer #(.width(32), .enable("false")) multiplexer_32 (
    .in0(in_33), .in1(xor_32_out), .out(out_97), .sel(is_pause));
  assign xor_32_out = in_33 ^ 32'h2000;  // XOR_Gate xor_32, 32 bits wide
  Pull_Resistor pull_resistor_32 (.node(in_33));
  Multiplexer #(.width(32), .enable("false")) multiplexer_33 (
    .in0(in_34), .in1(xor_33_out), .out(out_98), .sel(is_pause));
  assign xor_33_out = in_34 ^ 32'h2000;  // XOR_Gate xor_33, 32 bits wide
  Pull_Resistor pull_resistor_33 (.node(in_34));
  Multiplexer #(.width(32), .enable("false")) multiplexer_34 (
    .in0(in_35), .in1(xor_34_out), .out(out_99), .sel(is_pause));
  assign xor_34_out = in_35 ^ 32'hfc000;  // XOR_Gate xor_34, 32 bits wide
  Pull_Resistor pull_resistor_34 (.node(in_35));
  Multiplexer #(.width(32), .enable("false")) multiplexer_35 (
    .in0(in_36), .in1(xor_35_out), .out(out_100), .sel(is_pause));
  assign xor_35_out = in_36 ^ {32{1'b0}};  // XOR_Gate xor_35, 32 bits wide
  Pull_Resistor pull_resistor_35 (.node(in_36));
  Multiplexer #(.width(32), .enable("false")) multiplexer_36 (
    .in0(in_37), .in1(xor_36_out), .out(out_101), .sel(is_pause));
  assign xor_36_out = in_37 ^ 32'h62000;  // XOR_Gate xor_36, 32 bits wide
  Pull_Resistor pull_resistor_36 (.node(in_37));
  Multiplexer #(.width(32), .enable("false")) multiplexer_37 (
    .in0(in_38), .in1(xor_37_out), .out(out_102), .sel(is_pause));
  assign xor_37_out = in_38 ^ 32'h92000;  // XOR_Gate xor_37, 32 bits wide
  Pull_Resistor pull_resistor_37 (.node(in_38));
  Multiplexer #(.width(32), .enable("false")) multiplexer_38 (
    .in0(in_39), .in1(xor_38_out), .out(out_103), .sel(is_pause));
  assign xor_38_out = in_39 ^ 32'h92000;  // XOR_Gate xor_38, 32 bits wide
  Pull_Resistor pull_resistor_38 (.node(in_39));
  Multiplexer #(.width(32), .enable("false")) multiplexer_39 (
    .in0(in_40), .in1(xor_39_out), .out(out_104), .sel(is_pause));
  assign xor_39_out = in_40 ^ 32'h92000;  // XOR_Gate xor_39, 32 bits wide
  Pull_Resistor pull_resistor_39 (.node(in_40));
  Multiplexer #(.width(32), .enable("false")) multiplexer_40 (
    .in0(in_41), .in1(xor_40_out), .out(out_105), .sel(is_pause));
  assign xor_40_out = in_41 ^ 32'h8c000;  // XOR_Gate xor_40, 32 bits wide
  Pull_Resistor pull_resistor_40 (.node(in_41));
  Multiplexer #(.width(32), .enable("false")) multiplexer_41 (
    .in0(in_42), .in1(xor_41_out), .out(out_106), .sel(is_pause));
  assign xor_41_out = in_42 ^ {32{1'b0}};  // XOR_Gate xor_41, 32 bits wide
  Pull_Resistor pull_resistor_41 (.node(in_42));
  Multiplexer #(.width(32), .enable("false")) multiplexer_42 (
    .in0(in_43), .in1(xor_42_out), .out(out_107), .sel(is_pause));
  assign xor_42_out = in_43 ^ 32'hfe000;  // XOR_Gate xor_42, 32 bits wide
  Pull_Resistor pull_resistor_42 (.node(in_43));
  Multiplexer #(.width(32), .enable("false")) multiplexer_43 (
    .in0(in_44), .in1(xor_43_out), .out(out_108), .sel(is_pause));
  assign xor_43_out = in_44 ^ 32'h92000;  // XOR_Gate xor_43, 32 bits wide
  Pull_Resistor pull_resistor_43 (.node(in_44));
  Multiplexer #(.width(32), .enable("false")) multiplexer_44 (
    .in0(in_45), .in1(xor_44_out), .out(out_109), .sel(is_pause));
  assign xor_44_out = in_45 ^ 32'h92000;  // XOR_Gate xor_44, 32 bits wide
  Pull_Resistor pull_resistor_44 (.node(in_45));
  Multiplexer #(.width(32), .enable("false")) multiplexer_45 (
    .in0(in_46), .in1(xor_45_out), .out(out_110), .sel(is_pause));
  assign xor_45_out = in_46 ^ 32'h92000;  // XOR_Gate xor_45, 32 bits wide
  Pull_Resistor pull_resistor_45 (.node(in_46));
  Multiplexer #(.width(32), .enable("false")) multiplexer_46 (
    .in0(in_47), .in1(xor_46_out), .out(out_111), .sel(is_pause));
  assign xor_46_out = in_47 ^ 32'h92000;  // XOR_Gate xor_46, 32 bits wide
  Pull_Resistor pull_resistor_46 (.node(in_47));
  Multiplexer #(.width(32), .enable("false")) multiplexer_47 (
    .in0(in_48), .in1(xor_47_out), .out(out_112), .sel(is_pause));
  assign xor_47_out = in_48 ^ {32{1'b0}};  // XOR_Gate xor_47, 32 bits wide
  Pull_Resistor pull_resistor_47 (.node(in_48));
  Multiplexer #(.width(32), .enable("false")) multiplexer_48 (
    .in0(in_49), .in1(xor_48_out), .out(out_113), .sel(is_pause));
  assign xor_48_out = in_49 ^ {32{1'b0}};  // XOR_Gate xor_48, 32 bits wide
  Pull_Resistor pull_resistor_48 (.node(in_49));
  Multiplexer #(.width(32), .enable("false")) multiplexer_49 (
    .in0(in_50), .in1(xor_49_out), .out(out_114), .sel(is_pause));
  assign xor_49_out = in_50 ^ {32{1'b0}};  // XOR_Gate xor_49, 32 bits wide
  Pull_Resistor pull_resistor_49 (.node(in_50));
  Multiplexer #(.width(32), .enable("false")) multiplexer_50 (
    .in0(in_51), .in1(xor_50_out), .out(out_115), .sel(is_pause));
  assign xor_50_out = in_51 ^ {32{1'b0}};  // XOR_Gate xor_50, 32 bits wide
  Pull_Resistor pull_resistor_50 (.node(in_51));
  Multiplexer #(.width(32), .enable("false")) multiplexer_51 (
    .in0(in_52), .in1(xor_51_out), .out(out_116), .sel(is_pause));
  assign xor_51_out = in_52 ^ {32{1'b0}};  // XOR_Gate xor_51, 32 bits wide
  Pull_Resistor pull_resistor_51 (.node(in_52));
  Multiplexer #(.width(32), .enable("false")) multiplexer_52 (
    .in0(in_53), .in1(xor_52_out), .out(out_117), .sel(is_pause));
  assign xor_52_out = in_53 ^ {32{1'b0}};  // XOR_Gate xor_52, 32 bits wide
  Pull_Resistor pull_resistor_52 (.node(in_53));
  Multiplexer #(.width(32), .enable("false")) multiplexer_53 (
    .in0(in_54), .in1(xor_53_out), .out(out_118), .sel(is_pause));
  assign xor_53_out = in_54 ^ {32{1'b0}};  // XOR_Gate xor_53, 32 bits wide
  Pull_Resistor pull_resistor_53 (.node(in_54));
  Multiplexer #(.width(32), .enable("false")) multiplexer_54 (
    .in0(in_55), .in1(xor_54_out), .out(out_119), .sel(is_pause));
  assign xor_54_out = in_55 ^ {32{1'b0}};  // XOR_Gate xor_54, 32 bits wide
  Pull_Resistor pull_resistor_54 (.node(in_55));
  Multiplexer #(.width(32), .enable("false")) multiplexer_55 (
    .in0(in_56), .in1(xor_55_out), .out(out_120), .sel(is_pause));
  assign xor_55_out = in_56 ^ {32{1'b0}};  // XOR_Gate xor_55, 32 bits wide
  Pull_Resistor pull_resistor_55 (.node(in_56));
  Multiplexer #(.width(32), .enable("false")) multiplexer_56 (
    .in0(in_57), .in1(xor_56_out), .out(out_121), .sel(is_pause));
  assign xor_56_out = in_57 ^ {32{1'b0}};  // XOR_Gate xor_56, 32 bits wide
  Pull_Resistor pull_resistor_56 (.node(in_57));
  Multiplexer #(.width(32), .enable("false")) multiplexer_57 (
    .in0(in_58), .in1(xor_57_out), .out(out_122), .sel(is_pause));
  assign xor_57_out = in_58 ^ {32{1'b0}};  // XOR_Gate xor_57, 32 bits wide
  Pull_Resistor pull_resistor_57 (.node(in_58));
  Multiplexer #(.width(32), .enable("false")) multiplexer_58 (
    .in0(in_59), .in1(xor_58_out), .out(out_123), .sel(is_pause));
  assign xor_58_out = in_59 ^ {32{1'b0}};  // XOR_Gate xor_58, 32 bits wide
  Pull_Resistor pull_resistor_58 (.node(in_59));
  Multiplexer #(.width(32), .enable("false")) multiplexer_59 (
    .in0(in_60), .in1(xor_59_out), .out(out_124), .sel(is_pause));
  assign xor_59_out = in_60 ^ {32{1'b0}};  // XOR_Gate xor_59, 32 bits wide
  Pull_Resistor pull_resistor_59 (.node(in_60));
  Multiplexer #(.width(32), .enable("false")) multiplexer_60 (
    .in0(in_61), .in1(xor_60_out), .out(out_125), .sel(is_pause));
  assign xor_60_out = in_61 ^ {32{1'b0}};  // XOR_Gate xor_60, 32 bits wide
  Pull_Resistor pull_resistor_60 (.node(in_61));
  Multiplexer #(.width(32), .enable("false")) multiplexer_61 (
    .in0(in_62), .in1(xor_61_out), .out(out_126), .sel(is_pause));
  assign xor_61_out = in_62 ^ {32{1'b0}};  // XOR_Gate xor_61, 32 bits wide
  Pull_Resistor pull_resistor_61 (.node(in_62));
  Multiplexer #(.width(32), .enable("false")) multiplexer_62 (
    .in0(in_63), .in1(xor_62_out), .out(out_127), .sel(is_pause));
  assign xor_62_out = in_63 ^ {32{1'b0}};  // XOR_Gate xor_62, 32 bits wide
  Pull_Resistor pull_resistor_62 (.node(in_63));
  Multiplexer #(.width(32), .enable("false")) multiplexer_63 (
    .in0(in_64), .in1(xor_63_out), .out(out_128), .sel(is_pause));
  assign xor_63_out = in_64 ^ {32{1'b0}};  // XOR_Gate xor_63, 32 bits wide
  Pull_Resistor pull_resistor_63 (.node(in_64));
  Multiplexer #(.width(32), .enable("false")) multiplexer_64 (
    .in0(in_65), .in1(xor_64_out), .out(out_129), .sel(is_pause));
  assign xor_64_out = in_65 ^ {32{1'b0}};  // XOR_Gate xor_64, 32 bits wide
  Pull_Resistor pull_resistor_64 (.node(in_65));
endmodule
